// Logisim project ideal_pipeline.circ as structural Verilog: 11 circuits, main circuit ◇单周期MIPS
module \单周期MIPS  (
);

  wire and_1_out, and_3_out, and_4_out, CLK, comparator_1_eq, con_if, Go, HALT, JAL, JMP, JR,
       mips_alu_1_equal, or_2_out, RST, SignedExt, Syscall, uncon_if, \硬布线控制器_1_alu_src , \硬布线控制器_1_beq ,
       \硬布线控制器_1_bne , \硬布线控制器_1_memtoreg , \硬布线控制器_1_memwrite , \硬布线控制器_1_regdst , \硬布线控制器_1_regwrite ;
  wire [0:0] or_1_out;
  wire [3:0] \硬布线控制器_1_alu_op ;
  wire [4:0] multiplexer_2_out, multiplexer_3_out, multiplexer_4_out, multiplexer_5_out, rom_1_data_2;
  wire [15:0] \总周期数 , \无条件分支数 , \条件分支成功数 ;
  wire [31:0] b_pc, bit_extender_1_out, bit_extender_2_out, bit_extender_3_out, j_pc, LedData,
       mips_alu_1_result, multiplexer_1_out, multiplexer_6_out, multiplexer_7_out, multiplexer_8_out,
       multiplexer_9_out, next_pc, PC_q, R2, ram_1_data, result2, rom_1_data, RS, shifter_2_out;

  Button \u_总复位  (.out(RST));
  Button u_Go (.out(Go));
  Clock clock_1 (.out(CLK));
  Hex_Digit_Display hex_digit_display_1 (.value(LedData[31:28]));  // open: dp
  Hex_Digit_Display hex_digit_display_2 (.value(LedData[27:24]));  // open: dp
  or or_1 (or_1_out[0], con_if, JR);
  Hex_Digit_Display hex_digit_display_3 (.value(LedData[23:20]));  // open: dp
  Hex_Digit_Display hex_digit_display_4 (.value(LedData[19:16]));  // open: dp
  Multiplexer #(.select(2), .width(32), .enable("false")) multiplexer_1 (
    .in0(next_pc), .in1(b_pc), .in2(j_pc), .in3(RS), .out(multiplexer_1_out), .sel({uncon_if, or_1_out[0]}));
  or or_2 (or_2_out, Go, ~HALT);  // OR_Gate
  Hex_Digit_Display hex_digit_display_5 (.value(LedData[15:12]));  // open: dp
  Hex_Digit_Display hex_digit_display_6 (.value(LedData[11:8]));  // open: dp
  Hex_Digit_Display hex_digit_display_7 (.value(LedData[7:4]));  // open: dp
  Hex_Digit_Display hex_digit_display_8 (.value(LedData[3:0]));  // open: dp
  Counter #(.width(16), .max('hffff)) counter_1 (
    .count(con_if), .Q(\条件分支成功数 ), .clk(CLK), .clr(RST));  // open: load, D, carry
  Counter #(.width(16), .max('hffff)) counter_2 (
    .count(uncon_if), .Q(\无条件分支数 ), .clk(CLK), .clr(RST));  // open: load, D, carry
  Counter #(.width(16), .max('hffff)) counter_3 (
    .count(or_2_out), .Q(\总周期数 ), .clk(CLK), .clr(RST));  // open: load, D, carry
  Register #(.width(32)) PC (.D(multiplexer_1_out), .en(or_2_out), .Q(PC_q), .clk(CLK), .clr(RST));
  Adder #(.width(32)) adder_1 (.a(PC_q), .b(32'h4), .out(next_pc));  // open: cin, cout
  ROM #(.addrWidth(10), .dataWidth(32)) rom_1 (
    .addr(PC_q[11:2]), .data({rom_1_data[31:11], rom_1_data_2, rom_1_data[5:0]}));  // open: sel
  // Probe on \总周期数 
  // Probe on \无条件分支数 
  // Probe on \条件分支成功数 
  or or_3 (uncon_if, JAL, JMP, JR);
  \硬布线控制器  \u_硬布线控制器_1  (
    .Func(rom_1_data[5:0]), .OP(rom_1_data[31:26]), .ALU_OP(\硬布线控制器_1_alu_op ),
    .MemToReg(\硬布线控制器_1_memtoreg ), .MemWrite(\硬布线控制器_1_memwrite ), .ALU_SRC(\硬布线控制器_1_alu_src ),
    .RegWrite(\硬布线控制器_1_regwrite ), .SysCALL(Syscall), .SignedExt(SignedExt), .RegDst(\硬布线控制器_1_regdst ),
    .JR(JR), .JMP(JMP), .Beq(\硬布线控制器_1_beq ), .JAL(JAL), .Bne(\硬布线控制器_1_bne ));
  Multiplexer #(.width(5), .enable("false")) multiplexer_2 (
    .in0(rom_1_data[25:21]), .in1(5'b00010), .out(multiplexer_2_out), .sel(Syscall));
  Multiplexer #(.width(5), .enable("false")) multiplexer_3 (
    .in0(rom_1_data[20:16]), .in1(5'b00100), .out(multiplexer_3_out), .sel(Syscall));
  Multiplexer #(.width(5), .enable("false")) multiplexer_4 (
    .in0(rom_1_data[20:16]), .in1(rom_1_data[15:11]), .out(multiplexer_4_out), .sel(\硬布线控制器_1_regdst ));
  assign bit_extender_1_out = {{16{1'b0}}, {rom_1_data[15:11], rom_1_data_2, rom_1_data[5:0]}};  // Bit_Extender bit_extender_1
  assign bit_extender_2_out = {{16{rom_1_data[15]}}, {rom_1_data[15:11], rom_1_data_2, rom_1_data[5:0]}};  // Bit_Extender bit_extender_2
  assign bit_extender_3_out = {{6{1'b0}}, {rom_1_data[25:11], rom_1_data_2, rom_1_data[5:0]}};  // Bit_Extender bit_extender_3
  Comparator #(.width(32)) comparator_1 (.a(RS), .b(32'h22), .eq(comparator_1_eq));  // open: gt, lt
  Multiplexer #(.width(5), .enable("false")) multiplexer_5 (
    .in0(multiplexer_4_out), .in1({5{1'b1}}), .out(multiplexer_5_out), .sel(JAL));
  Multiplexer #(.width(32), .enable("false")) multiplexer_6 (
    .in0(bit_extender_1_out), .in1(bit_extender_2_out), .out(multiplexer_6_out), .sel(SignedExt));
  Shifter #(.width(32)) shifter_1 (.in(bit_extender_3_out), .\dist (5'b00010), .out(j_pc));
  and and_1 (and_1_out, Syscall, comparator_1_eq);
  and and_2 (HALT, ~comparator_1_eq, Syscall);  // AND_Gate
  Register #(.width(32)) Led (.D(R2), .en(and_1_out), .Q(LedData), .clk(CLK), .clr(RST));
  MIPS_Regifile mips_regifile_1 (
    .Din(multiplexer_8_out), .Clk(CLK), .R1(RS), .R2(R2), .WE(\硬布线控制器_1_regwrite ),
    .W_num(multiplexer_5_out), .R1_num(multiplexer_2_out), .R2_num(multiplexer_3_out));
  Shifter #(.width(32)) shifter_2 (.in(multiplexer_6_out), .\dist (5'b00010), .out(shifter_2_out));
  Multiplexer #(.width(32), .enable("false")) multiplexer_7 (
    .in0(R2), .in1(multiplexer_6_out), .out(multiplexer_7_out), .sel(\硬布线控制器_1_alu_src ));
  Adder #(.width(32)) adder_2 (.a(shifter_2_out), .b(next_pc), .out(b_pc));  // open: cin, cout
  MIPS_ALU mips_alu_1 (
    .X(RS), .Y(multiplexer_7_out), .AluOP(\硬布线控制器_1_alu_op ), .Equal(mips_alu_1_equal),
    .Result(mips_alu_1_result), .Result_2(result2), .shamt(rom_1_data_2));
  and and_3 (and_3_out, mips_alu_1_equal, \硬布线控制器_1_beq );
  and and_4 (and_4_out, \硬布线控制器_1_bne , ~mips_alu_1_equal);  // AND_Gate
  or or_4 (con_if, and_3_out, and_4_out);
  Multiplexer #(.width(32), .enable("false")) multiplexer_8 (
    .in0(multiplexer_9_out), .in1(next_pc), .out(multiplexer_8_out), .sel(JAL));
  RAM #(.addrWidth(10), .dataWidth(32), .bus("separate")) ram_1 (
    .addr(mips_alu_1_result[11:2]), .din(R2), .data(ram_1_data), .str(\硬布线控制器_1_memwrite ), .clk(CLK));  // open: sel, ld, clr
  Multiplexer #(.width(32), .enable("false")) multiplexer_9 (
    .in0(mips_alu_1_result), .in1(ram_1_data), .out(multiplexer_9_out), .sel(\硬布线控制器_1_memtoreg ));

  // Notes on the sheet:
  //   数码管输出应该用寄存器锁存，否则显示数据只能一闪而过
  //   可以通过项目增加Logisim库的方式将前几次实验完成的电路作为子电路引入到本电路中使用
  //   数码管输出
  //   指令存储器
  //   contents of rom_1 (hex, n*v repeats v):
  //   20110001 8000c05 20110001 20120002 20130003 8000c09 20110001 20120002 20130003 8000c0d 20110001
  //   20120002 20130003 8000c11 20110001 20120002 20130003 c000cbb 20100001 20110001 118fc0 112020
  //   20020022 c 118882 12200001 8000c15 112020 20020022 c 20110001 118880 112020 20020022 c 12200001
  //   8000c1f 20110001 118fc0 112020 20020022 c 1188c3 112020 20020022 c 118903 112020 20020022 c 118903
  //   112020 20020022 c 118903 112020 20020022 c 118903 112020 20020022 c 118903 112020 20020022 c 118903
  //   112020 20020022 c 118903 112020 20020022 c 20100001 109fc0 139fc3 8021 2012000c 24160003 26100001
  //   3210000f 20080008 20090001 139900 2709825 132020 20020022 c 1094022 1500fff9 22100001 2018000f
  //   2188024 108700 20080008 20090001 139902 2709825 132021 20020022 c 1094022 1500fff9 108702 2c9b022
  //   12c00001 8000c50 4020 1084027 84400 3508ffff 82021 20020022 c 2010ffff 20110000 ae300000 22100001
  //   22310004 ae300000 22100001 22310004 ae300000 22100001 22310004 ae300000 22100001 22310004 ae300000
  //   22100001 22310004 ae300000 22100001 22310004 ae300000 22100001 22310004 ae300000 22100001 22310004
  //   ae300000 22100001 22310004 ae300000 22100001 22310004 ae300000 22100001 22310004 ae300000 22100001
  //   22310004 ae300000 22100001 22310004 ae300000 22100001 22310004 ae300000 22100001 22310004 ae300000
  //   22100001 22310004 22100001 8020 2011003c 8e130000 8e340000 274402a 11000002 ae330000 ae140000
  //   2231fffc 1611fff8 102020 20020022 c 22100004 2011003c 1611fff2 20020032 c 8000c00 2002000a c
  //   20100000 22100001 102020 20020022 c 22100002 102020 20020022 c 22100003 102020 20020022 c 22100004
  //   102020 20020022 c 22100005 102020 20020022 c 22100006 102020 20020022 c 22100007 102020 20020022 c
  //   22100008 102020 20020022 20020022 c 3e00008
  //   总复位信号应将除ROM以外所有存储组件全部清零
  //   指令字
  //   OP
  //   Func
  //   rs
  //   rt
  //   rd
  //   shamt
  //   Imm
  //   j-addr
  //   JMP
  //   JR
  //   OP
  //   Func
  //   Beq
  //   MemWrite
  //   AluOP
  //   AluSrcB
  //   RegWrite
  //   JAL
  //   RegDst
  //   Syscall
endmodule

// 单周期硬布线控制器
module \硬布线控制器  (
  input  [5:0] OP,
  input  [5:0] Func,
  output [3:0] ALU_OP,
  output MemToReg,
  output MemWrite,
  output ALU_SRC,
  output RegWrite,
  output SysCALL,
  output SignedExt,
  output RegDst,
  output Beq,
  output Bne,
  output JR,
  output JMP,
  output JAL
);

  \运算控制器  \u_运算控制器_1  (
    .OP0(OP[0]), .OP1(OP[1]), .OP2(OP[2]), .OP3(OP[3]), .OP4(OP[4]), .OP5(OP[5]), .F0(Func[0]), .F1(Func[1]),
    .F2(Func[2]), .F3(Func[3]), .F4(Func[4]), .F5(Func[5]), .S0(ALU_OP[0]), .S1(ALU_OP[1]), .S2(ALU_OP[2]),
    .S3(ALU_OP[3]));
  \控制信号生成  \u_控制信号生成_1  (
    .OP0(OP[0]), .OP1(OP[1]), .OP2(OP[2]), .OP3(OP[3]), .OP4(OP[4]), .OP5(OP[5]), .F0(Func[0]), .F1(Func[1]),
    .F2(Func[2]), .F3(Func[3]), .F4(Func[4]), .F5(Func[5]), .MemWrite(MemWrite), .JAL(JAL), .JMP(JMP),
    .ALU_SRC(ALU_SRC), .RegWrite(RegWrite), .SysCALL(SysCALL), .MemtoReg(MemToReg), .SignedExt(SignedExt),
    .RegDst(RegDst), .BEQ(Beq), .BNE(Bne), .JR(JR));

  // Other names for the same wires on the sheet: OP_CODE[5:0] = OP

  // Notes on the sheet:
  //   运算器控制器，根据指令生成运算器功能选择信号
  //   控制信号生成，产生数据通路需要的其他控制信号
endmodule

// 运算器控制器
module \运算控制器  (
  input  OP0,
  input  OP1,
  input  OP2,
  input  OP3,
  input  OP4,
  input  OP5,
  input  F0,
  input  F1,
  input  F2,
  input  F3,
  input  F4,
  input  F5,
  output S0,
  output S1,
  output S2,
  output S3
);

  wire and_1_out, and_2_out, and_3_out, and_4_out, and_5_out, and_6_out, and_7_out, and_8_out, and_9_out,
       and_10_out, and_11_out, and_12_out, and_13_out, and_14_out, and_15_out, and_16_out, and_17_out,
       and_18_out, and_19_out, and_20_out, and_21_out, and_22_out, and_23_out, and_24_out, and_25_out,
       and_26_out, and_27_out, and_28_out, and_29_out, and_30_out, and_31_out, and_32_out, and_33_out,
       and_34_out, and_35_out, and_36_out, and_37_out, and_38_out, and_39_out, and_40_out, and_41_out,
       and_42_out, and_43_out, and_44_out, and_45_out, and_46_out, and_47_out, not_1_out, not_2_out,
       not_3_out, not_4_out, not_5_out, not_6_out, not_7_out, not_8_out, not_9_out, not_10_out, not_11_out,
       not_12_out, not_13_out, not_14_out, not_15_out, not_16_out, not_17_out, not_18_out, not_19_out,
       not_20_out, not_21_out, not_22_out, not_23_out, not_24_out, not_25_out, not_26_out, not_27_out,
       not_28_out, not_29_out, not_30_out, not_31_out, not_32_out, not_33_out, not_34_out, not_35_out,
       not_36_out, not_37_out, not_38_out, not_39_out, not_40_out, not_41_out, not_42_out, not_43_out,
       not_44_out, not_45_out, not_46_out, not_47_out, not_48_out, not_49_out, not_50_out, not_51_out,
       not_52_out, not_53_out, not_54_out, not_55_out, not_56_out, not_57_out, not_58_out, not_59_out,
       not_60_out, not_61_out, not_62_out, not_63_out, not_64_out, not_65_out, not_66_out, not_67_out,
       not_68_out, not_69_out, not_70_out, not_71_out, not_72_out, not_73_out, not_74_out, not_75_out,
       not_76_out, not_77_out, not_78_out, not_79_out, not_80_out, not_81_out, not_82_out, not_83_out,
       not_84_out, not_85_out, not_86_out, not_87_out, not_88_out, not_89_out, not_90_out, not_91_out,
       not_92_out, not_93_out, not_94_out, not_95_out, not_96_out, not_97_out, not_98_out, not_99_out,
       not_100_out, not_101_out, not_102_out, not_103_out, not_104_out, not_105_out, not_106_out,
       not_107_out, not_108_out, not_109_out, not_110_out, not_111_out, not_112_out, not_113_out,
       not_114_out, not_115_out, not_116_out, not_117_out, not_118_out, not_119_out, not_120_out,
       not_121_out, not_122_out, not_123_out, not_124_out, not_125_out, not_126_out, not_127_out,
       not_128_out, not_129_out, not_130_out, not_131_out, not_132_out, not_133_out, not_134_out,
       not_135_out, not_136_out, not_137_out, not_138_out, not_139_out, not_140_out, not_141_out,
       not_142_out, not_143_out, not_144_out, not_145_out, not_146_out, not_147_out, not_148_out,
       not_149_out, not_150_out, not_151_out, not_152_out, not_153_out, not_154_out, not_155_out,
       not_156_out, not_157_out, not_158_out, not_159_out, not_160_out, not_161_out, not_162_out,
       not_163_out, not_164_out, not_165_out, not_166_out, not_167_out, not_168_out, not_169_out,
       not_170_out, not_171_out, not_172_out, not_173_out, not_174_out, not_175_out, not_176_out,
       not_177_out, not_178_out, not_179_out, not_180_out, not_181_out, not_182_out, not_183_out,
       not_184_out, not_185_out, not_186_out, not_187_out, not_188_out, not_189_out, not_190_out,
       not_191_out, not_192_out, not_193_out, not_194_out, not_195_out, not_196_out, not_197_out,
       not_198_out, not_199_out, not_200_out, not_201_out, not_202_out, not_203_out, not_204_out,
       not_205_out, not_206_out, not_207_out, not_208_out, not_209_out, not_210_out, not_211_out,
       not_212_out, not_213_out, not_214_out, not_215_out, not_216_out, not_217_out, not_218_out,
       not_219_out, not_220_out, not_221_out, not_222_out, not_223_out, not_224_out, not_225_out,
       not_226_out, not_227_out, not_228_out, not_229_out, not_230_out, not_231_out, not_232_out,
       not_233_out, not_234_out, not_235_out, not_236_out, not_237_out, not_238_out, not_239_out,
       not_240_out, not_241_out, not_242_out, not_243_out, not_244_out, not_245_out, not_246_out,
       not_247_out, not_248_out, not_249_out, not_250_out, not_251_out, not_252_out, not_253_out,
       not_254_out, not_255_out, not_256_out, not_257_out, not_258_out, not_259_out, not_260_out,
       not_261_out, not_262_out, not_263_out, not_264_out, not_265_out, not_266_out, not_267_out,
       not_268_out, not_269_out, not_270_out, not_271_out, not_272_out, not_273_out, not_274_out,
       not_275_out, not_276_out, not_277_out, not_278_out, not_279_out, not_280_out, not_281_out,
       not_282_out, not_283_out, not_284_out, not_285_out, not_286_out, not_287_out, not_288_out,
       not_289_out, not_290_out, not_291_out, not_292_out, not_293_out, not_294_out, not_295_out,
       not_296_out, not_297_out, not_298_out, not_299_out, not_300_out, not_301_out, not_302_out,
       not_303_out, not_304_out;

  not not_1 (not_1_out, OP5);
  not not_2 (not_2_out, OP4);
  not not_3 (not_3_out, OP3);
  not not_4 (not_4_out, OP2);
  not not_5 (not_5_out, OP1);
  not not_6 (not_6_out, OP0);
  not not_7 (not_7_out, F5);
  not not_8 (not_8_out, F4);
  not not_9 (not_9_out, F3);
  not not_10 (not_10_out, F2);
  not not_11 (not_11_out, OP5);
  not not_12 (not_12_out, OP4);
  not not_13 (not_13_out, OP3);
  not not_14 (not_14_out, OP2);
  not not_15 (not_15_out, OP1);
  not not_16 (not_16_out, OP0);
  not not_17 (not_17_out, F4);
  not not_18 (not_18_out, F3);
  not not_19 (not_19_out, F2);
  not not_20 (not_20_out, F1);
  not not_21 (not_21_out, F0);
  not not_22 (not_22_out, OP5);
  not not_23 (not_23_out, OP4);
  not not_24 (not_24_out, OP3);
  not not_25 (not_25_out, OP2);
  not not_26 (not_26_out, OP1);
  not not_27 (not_27_out, OP0);
  not not_28 (not_28_out, F4);
  not not_29 (not_29_out, F3);
  not not_30 (not_30_out, F2);
  not not_31 (not_31_out, F1);
  not not_32 (not_32_out, OP5);
  not not_33 (not_33_out, OP4);
  not not_34 (not_34_out, OP3);
  not not_35 (not_35_out, OP2);
  not not_36 (not_36_out, OP1);
  not not_37 (not_37_out, OP0);
  not not_38 (not_38_out, F4);
  not not_39 (not_39_out, F3);
  not not_40 (not_40_out, F1);
  not not_41 (not_41_out, F0);
  not not_42 (not_42_out, OP5);
  not not_43 (not_43_out, OP4);
  not not_44 (not_44_out, OP3);
  not not_45 (not_45_out, OP2);
  not not_46 (not_46_out, OP1);
  not not_47 (not_47_out, OP0);
  not not_48 (not_48_out, F4);
  not not_49 (not_49_out, F2);
  not not_50 (not_50_out, F0);
  not not_51 (not_51_out, OP5);
  not not_52 (not_52_out, OP4);
  not not_53 (not_53_out, OP3);
  not not_54 (not_54_out, OP1);
  not not_55 (not_55_out, OP0);
  not not_56 (not_56_out, OP5);
  not not_57 (not_57_out, OP4);
  not not_58 (not_58_out, OP3);
  not not_59 (not_59_out, OP1);
  not not_60 (not_60_out, OP5);
  not not_61 (not_61_out, OP4);
  not not_62 (not_62_out, OP2);
  not not_63 (not_63_out, OP1);
  not not_64 (not_64_out, OP0);
  not not_65 (not_65_out, OP5);
  not not_66 (not_66_out, OP4);
  not not_67 (not_67_out, OP1);
  not not_68 (not_68_out, OP0);
  not not_69 (not_69_out, OP5);
  not not_70 (not_70_out, OP4);
  not not_71 (not_71_out, OP2);
  not not_72 (not_72_out, OP1);
  not not_73 (not_73_out, OP5);
  not not_74 (not_74_out, OP4);
  not not_75 (not_75_out, OP2);
  not not_76 (not_76_out, OP0);
  not not_77 (not_77_out, OP4);
  not not_78 (not_78_out, OP3);
  not not_79 (not_79_out, OP2);
  not not_80 (not_80_out, OP4);
  not not_81 (not_81_out, OP2);
  not not_82 (not_82_out, OP5);
  not not_83 (not_83_out, OP4);
  not not_84 (not_84_out, OP3);
  not not_85 (not_85_out, OP2);
  not not_86 (not_86_out, OP1);
  not not_87 (not_87_out, OP0);
  not not_88 (not_88_out, F5);
  not not_89 (not_89_out, F2);
  not not_90 (not_90_out, F1);
  not not_91 (not_91_out, OP4);
  not not_92 (not_92_out, OP2);
  not not_93 (not_93_out, OP1);
  not not_94 (not_94_out, OP0);
  not not_95 (not_95_out, OP5);
  not not_96 (not_96_out, OP4);
  not not_97 (not_97_out, OP3);
  not not_98 (not_98_out, OP2);
  not not_99 (not_99_out, OP1);
  not not_100 (not_100_out, OP5);
  not not_101 (not_101_out, OP4);
  not not_102 (not_102_out, OP3);
  not not_103 (not_103_out, OP2);
  not not_104 (not_104_out, OP1);
  not not_105 (not_105_out, OP0);
  not not_106 (not_106_out, F5);
  not not_107 (not_107_out, F4);
  not not_108 (not_108_out, F3);
  not not_109 (not_109_out, F2);
  not not_110 (not_110_out, F0);
  not not_111 (not_111_out, OP5);
  not not_112 (not_112_out, OP4);
  not not_113 (not_113_out, OP3);
  not not_114 (not_114_out, OP2);
  not not_115 (not_115_out, OP1);
  not not_116 (not_116_out, OP0);
  not not_117 (not_117_out, F4);
  not not_118 (not_118_out, F3);
  not not_119 (not_119_out, F2);
  not not_120 (not_120_out, F0);
  not not_121 (not_121_out, OP5);
  not not_122 (not_122_out, OP4);
  not not_123 (not_123_out, OP3);
  not not_124 (not_124_out, OP2);
  not not_125 (not_125_out, OP1);
  not not_126 (not_126_out, OP0);
  not not_127 (not_127_out, F4);
  not not_128 (not_128_out, F3);
  not not_129 (not_129_out, F1);
  not not_130 (not_130_out, F0);
  not not_131 (not_131_out, OP5);
  not not_132 (not_132_out, OP4);
  not not_133 (not_133_out, OP3);
  not not_134 (not_134_out, OP2);
  not not_135 (not_135_out, OP1);
  not not_136 (not_136_out, OP0);
  not not_137 (not_137_out, F4);
  not not_138 (not_138_out, F3);
  not not_139 (not_139_out, OP5);
  not not_140 (not_140_out, OP4);
  not not_141 (not_141_out, OP3);
  not not_142 (not_142_out, OP2);
  not not_143 (not_143_out, OP1);
  not not_144 (not_144_out, OP0);
  not not_145 (not_145_out, F4);
  not not_146 (not_146_out, F2);
  not not_147 (not_147_out, F0);
  not not_148 (not_148_out, OP5);
  not not_149 (not_149_out, OP4);
  not not_150 (not_150_out, OP3);
  not not_151 (not_151_out, OP1);
  not not_152 (not_152_out, OP0);
  not not_153 (not_153_out, OP5);
  not not_154 (not_154_out, OP4);
  not not_155 (not_155_out, OP3);
  not not_156 (not_156_out, OP1);
  not not_157 (not_157_out, OP5);
  not not_158 (not_158_out, OP4);
  not not_159 (not_159_out, OP1);
  not not_160 (not_160_out, OP0);
  not not_161 (not_161_out, OP5);
  not not_162 (not_162_out, OP4);
  not not_163 (not_163_out, OP2);
  not not_164 (not_164_out, OP0);
  not not_165 (not_165_out, OP5);
  not not_166 (not_166_out, OP4);
  not not_167 (not_167_out, OP3);
  not not_168 (not_168_out, OP2);
  not not_169 (not_169_out, OP1);
  not not_170 (not_170_out, OP0);
  not not_171 (not_171_out, F5);
  not not_172 (not_172_out, F2);
  not not_173 (not_173_out, F1);
  not not_174 (not_174_out, OP5);
  not not_175 (not_175_out, OP4);
  not not_176 (not_176_out, OP3);
  not not_177 (not_177_out, OP2);
  not not_178 (not_178_out, OP1);
  not not_179 (not_179_out, OP5);
  not not_180 (not_180_out, OP4);
  not not_181 (not_181_out, OP3);
  not not_182 (not_182_out, OP2);
  not not_183 (not_183_out, OP1);
  not not_184 (not_184_out, OP0);
  not not_185 (not_185_out, F4);
  not not_186 (not_186_out, F3);
  not not_187 (not_187_out, F2);
  not not_188 (not_188_out, F1);
  not not_189 (not_189_out, F0);
  not not_190 (not_190_out, OP5);
  not not_191 (not_191_out, OP4);
  not not_192 (not_192_out, OP3);
  not not_193 (not_193_out, OP2);
  not not_194 (not_194_out, OP1);
  not not_195 (not_195_out, OP0);
  not not_196 (not_196_out, F4);
  not not_197 (not_197_out, F3);
  not not_198 (not_198_out, F2);
  not not_199 (not_199_out, F1);
  not not_200 (not_200_out, OP5);
  not not_201 (not_201_out, OP4);
  not not_202 (not_202_out, OP3);
  not not_203 (not_203_out, OP2);
  not not_204 (not_204_out, OP1);
  not not_205 (not_205_out, OP0);
  not not_206 (not_206_out, F4);
  not not_207 (not_207_out, F3);
  not not_208 (not_208_out, F2);
  not not_209 (not_209_out, F0);
  not not_210 (not_210_out, OP5);
  not not_211 (not_211_out, OP4);
  not not_212 (not_212_out, OP3);
  not not_213 (not_213_out, OP2);
  not not_214 (not_214_out, OP1);
  not not_215 (not_215_out, OP0);
  not not_216 (not_216_out, F4);
  not not_217 (not_217_out, F3);
  not not_218 (not_218_out, F1);
  not not_219 (not_219_out, F0);
  not not_220 (not_220_out, OP5);
  not not_221 (not_221_out, OP4);
  not not_222 (not_222_out, OP3);
  not not_223 (not_223_out, OP2);
  not not_224 (not_224_out, OP1);
  not not_225 (not_225_out, OP0);
  not not_226 (not_226_out, F4);
  not not_227 (not_227_out, F2);
  not not_228 (not_228_out, OP5);
  not not_229 (not_229_out, OP4);
  not not_230 (not_230_out, OP2);
  not not_231 (not_231_out, OP1);
  not not_232 (not_232_out, OP0);
  not not_233 (not_233_out, OP5);
  not not_234 (not_234_out, OP4);
  not not_235 (not_235_out, OP1);
  not not_236 (not_236_out, OP0);
  not not_237 (not_237_out, OP5);
  not not_238 (not_238_out, OP4);
  not not_239 (not_239_out, OP2);
  not not_240 (not_240_out, OP1);
  not not_241 (not_241_out, OP4);
  not not_242 (not_242_out, OP3);
  not not_243 (not_243_out, OP2);
  not not_244 (not_244_out, OP4);
  not not_245 (not_245_out, OP2);
  not not_246 (not_246_out, OP4);
  not not_247 (not_247_out, OP2);
  not not_248 (not_248_out, OP1);
  not not_249 (not_249_out, OP0);
  not not_250 (not_250_out, OP5);
  not not_251 (not_251_out, OP4);
  not not_252 (not_252_out, OP3);
  not not_253 (not_253_out, OP2);
  not not_254 (not_254_out, OP1);
  not not_255 (not_255_out, OP0);
  not not_256 (not_256_out, F4);
  not not_257 (not_257_out, F3);
  not not_258 (not_258_out, F1);
  not not_259 (not_259_out, OP5);
  not not_260 (not_260_out, OP4);
  not not_261 (not_261_out, OP3);
  not not_262 (not_262_out, OP2);
  not not_263 (not_263_out, OP1);
  not not_264 (not_264_out, OP0);
  not not_265 (not_265_out, F4);
  not not_266 (not_266_out, F3);
  not not_267 (not_267_out, OP5);
  not not_268 (not_268_out, OP4);
  not not_269 (not_269_out, OP3);
  not not_270 (not_270_out, OP2);
  not not_271 (not_271_out, OP1);
  not not_272 (not_272_out, OP0);
  not not_273 (not_273_out, F4);
  not not_274 (not_274_out, F2);
  not not_275 (not_275_out, F0);
  not not_276 (not_276_out, OP5);
  not not_277 (not_277_out, OP4);
  not not_278 (not_278_out, OP3);
  not not_279 (not_279_out, OP2);
  not not_280 (not_280_out, OP1);
  not not_281 (not_281_out, OP0);
  not not_282 (not_282_out, F4);
  not not_283 (not_283_out, F2);
  not not_284 (not_284_out, OP5);
  not not_285 (not_285_out, OP4);
  not not_286 (not_286_out, OP3);
  not not_287 (not_287_out, OP1);
  not not_288 (not_288_out, OP0);
  not not_289 (not_289_out, OP5);
  not not_290 (not_290_out, OP4);
  not not_291 (not_291_out, OP3);
  not not_292 (not_292_out, OP1);
  not not_293 (not_293_out, OP5);
  not not_294 (not_294_out, OP4);
  not not_295 (not_295_out, OP2);
  not not_296 (not_296_out, OP0);
  not not_297 (not_297_out, OP5);
  not not_298 (not_298_out, OP4);
  not not_299 (not_299_out, OP1);
  not not_300 (not_300_out, OP5);
  not not_301 (not_301_out, OP4);
  not not_302 (not_302_out, OP3);
  not not_303 (not_303_out, OP2);
  not not_304 (not_304_out, OP1);
  and and_1 (and_1_out, not_1_out, not_2_out, not_3_out, not_4_out, not_5_out, not_6_out, not_7_out, not_8_out, not_9_out, not_10_out, F1, F0);
  and and_2 (and_2_out, not_11_out, not_12_out, not_13_out, not_14_out, not_15_out, not_16_out, F5, not_17_out, not_18_out, not_19_out, not_20_out, not_21_out);
  and and_3 (and_3_out, not_22_out, not_23_out, not_24_out, not_25_out, not_26_out, not_27_out, F5, not_28_out, not_29_out, not_30_out, not_31_out, F0);
  and and_4 (and_4_out, not_32_out, not_33_out, not_34_out, not_35_out, not_36_out, not_37_out, F5, not_38_out, not_39_out, F2, not_40_out, not_41_out);
  and and_5 (and_5_out, not_42_out, not_43_out, not_44_out, not_45_out, not_46_out, not_47_out, F5, not_48_out, F3, not_49_out, F1, not_50_out);
  and and_6 (and_6_out, not_51_out, not_52_out, not_53_out, OP2, not_54_out, not_55_out);
  and and_7 (and_7_out, not_56_out, not_57_out, not_58_out, OP2, not_59_out, OP0);
  and and_8 (and_8_out, not_60_out, not_61_out, OP3, not_62_out, not_63_out, not_64_out);
  and and_9 (and_9_out, not_65_out, not_66_out, OP3, OP2, not_67_out, not_68_out);
  and and_10 (and_10_out, not_69_out, not_70_out, OP3, not_71_out, not_72_out, OP0);
  and and_11 (and_11_out, not_73_out, not_74_out, OP3, not_75_out, OP1, not_76_out);
  and and_12 (and_12_out, OP5, not_77_out, not_78_out, not_79_out, OP1, OP0);
  and and_13 (and_13_out, OP5, not_80_out, OP3, not_81_out, OP1, OP0);
  and and_14 (and_14_out, not_82_out, not_83_out, not_84_out, not_85_out, not_86_out, not_87_out, not_88_out, F4, F3, not_89_out, not_90_out, F0);
  and and_15 (and_15_out, OP5, not_91_out, OP3, not_92_out, not_93_out, not_94_out);
  and and_16 (and_16_out, not_95_out, not_96_out, not_97_out, not_98_out, not_99_out, OP0);
  and and_17 (and_17_out, not_100_out, not_101_out, not_102_out, not_103_out, not_104_out, not_105_out, not_106_out, not_107_out, not_108_out, not_109_out, F1, not_110_out);
  and and_18 (and_18_out, not_111_out, not_112_out, not_113_out, not_114_out, not_115_out, not_116_out, F5, not_117_out, not_118_out, not_119_out, F1, not_120_out);
  and and_19 (and_19_out, not_121_out, not_122_out, not_123_out, not_124_out, not_125_out, not_126_out, F5, not_127_out, not_128_out, F2, not_129_out, not_130_out);
  and and_20 (and_20_out, not_131_out, not_132_out, not_133_out, not_134_out, not_135_out, not_136_out, F5, not_137_out, not_138_out, F2, F1, F0);
  and and_21 (and_21_out, not_139_out, not_140_out, not_141_out, not_142_out, not_143_out, not_144_out, F5, not_145_out, F3, not_146_out, F1, not_147_out);
  and and_22 (and_22_out, not_148_out, not_149_out, not_150_out, OP2, not_151_out, not_152_out);
  and and_23 (and_23_out, not_153_out, not_154_out, not_155_out, OP2, not_156_out, OP0);
  and and_24 (and_24_out, not_157_out, not_158_out, OP3, OP2, not_159_out, not_160_out);
  and and_25 (and_25_out, not_161_out, not_162_out, OP3, not_163_out, OP1, not_164_out);
  and and_26 (and_26_out, not_165_out, not_166_out, not_167_out, not_168_out, not_169_out, not_170_out, not_171_out, F4, F3, not_172_out, not_173_out, F0);
  and and_27 (and_27_out, not_174_out, not_175_out, not_176_out, not_177_out, not_178_out, OP0);
  and and_28 (and_28_out, not_179_out, not_180_out, not_181_out, not_182_out, not_183_out, not_184_out, F5, not_185_out, not_186_out, not_187_out, not_188_out, not_189_out);
  and and_29 (and_29_out, not_190_out, not_191_out, not_192_out, not_193_out, not_194_out, not_195_out, F5, not_196_out, not_197_out, not_198_out, not_199_out, F0);
  and and_30 (and_30_out, not_200_out, not_201_out, not_202_out, not_203_out, not_204_out, not_205_out, F5, not_206_out, not_207_out, not_208_out, F1, not_209_out);
  and and_31 (and_31_out, not_210_out, not_211_out, not_212_out, not_213_out, not_214_out, not_215_out, F5, not_216_out, not_217_out, F2, not_218_out, not_219_out);
  and and_32 (and_32_out, not_220_out, not_221_out, not_222_out, not_223_out, not_224_out, not_225_out, F5, not_226_out, F3, not_227_out, F1, F0);
  and and_33 (and_33_out, not_228_out, not_229_out, OP3, not_230_out, not_231_out, not_232_out);
  and and_34 (and_34_out, not_233_out, not_234_out, OP3, OP2, not_235_out, not_236_out);
  and and_35 (and_35_out, not_237_out, not_238_out, OP3, not_239_out, not_240_out, OP0);
  and and_36 (and_36_out, OP5, not_241_out, not_242_out, not_243_out, OP1, OP0);
  and and_37 (and_37_out, OP5, not_244_out, OP3, not_245_out, OP1, OP0);
  and and_38 (and_38_out, OP5, not_246_out, OP3, not_247_out, not_248_out, not_249_out);
  and and_39 (and_39_out, not_250_out, not_251_out, not_252_out, not_253_out, not_254_out, not_255_out, F5, not_256_out, not_257_out, F2, not_258_out, F0);
  and and_40 (and_40_out, not_259_out, not_260_out, not_261_out, not_262_out, not_263_out, not_264_out, F5, not_265_out, not_266_out, F2, F1, F0);
  and and_41 (and_41_out, not_267_out, not_268_out, not_269_out, not_270_out, not_271_out, not_272_out, F5, not_273_out, F3, not_274_out, F1, not_275_out);
  and and_42 (and_42_out, not_276_out, not_277_out, not_278_out, not_279_out, not_280_out, not_281_out, F5, not_282_out, F3, not_283_out, F1, F0);
  and and_43 (and_43_out, not_284_out, not_285_out, not_286_out, OP2, not_287_out, not_288_out);
  and and_44 (and_44_out, not_289_out, not_290_out, not_291_out, OP2, not_292_out, OP0);
  and and_45 (and_45_out, not_293_out, not_294_out, OP3, not_295_out, OP1, not_296_out);
  and and_46 (and_46_out, not_297_out, not_298_out, OP3, OP2, not_299_out, OP0);
  and and_47 (and_47_out, not_300_out, not_301_out, not_302_out, not_303_out, not_304_out, OP0);
  or or_1 (S1, and_17_out, and_18_out, and_19_out, and_20_out, and_21_out, and_22_out, and_23_out, and_24_out, and_25_out, and_26_out, and_27_out);
  or or_2 (S2, and_28_out, and_29_out, and_30_out, and_31_out, and_32_out, and_33_out, and_34_out, and_35_out, and_36_out, and_37_out, and_38_out);
  or or_3 (S3, and_39_out, and_40_out, and_41_out, and_42_out, and_43_out, and_44_out, and_45_out, and_46_out, and_47_out);
  or or_4 (S0, and_1_out, and_2_out, and_3_out, and_4_out, and_5_out, and_6_out, and_7_out, and_8_out, and_9_out, and_10_out, and_11_out, and_12_out, and_13_out, and_14_out, and_15_out, and_16_out);
endmodule

// 控制信号生成
module \控制信号生成  (
  input  OP0,
  input  OP1,
  input  OP2,
  input  OP3,
  input  OP4,
  input  OP5,
  input  F0,
  input  F1,
  input  F2,
  input  F3,
  input  F4,
  input  F5,
  output MemWrite,
  output JAL,
  output JMP,
  output ALU_SRC,
  output RegWrite,
  output SysCALL,
  output MemtoReg,
  output SignedExt,
  output RegDst,
  output BEQ,
  output BNE,
  output JR
);

  wire and_1_out, and_2_out, and_5_out, and_6_out, and_7_out, and_8_out, and_9_out, and_10_out, and_11_out,
       and_12_out, and_13_out, and_14_out, and_15_out, and_16_out, and_17_out, and_18_out, and_19_out,
       and_20_out, and_21_out, and_22_out, and_23_out, and_24_out, and_25_out, and_26_out, and_27_out,
       and_28_out, and_29_out, and_30_out, and_31_out, and_34_out, and_35_out, and_36_out, and_37_out,
       and_38_out, and_39_out, and_40_out, and_41_out, and_42_out, and_43_out, and_44_out, and_45_out,
       and_46_out, and_47_out, and_48_out, and_49_out, and_50_out, and_51_out, and_52_out, and_53_out,
       not_1_out, not_2_out, not_3_out, not_4_out, not_5_out, not_6_out, not_7_out, not_8_out, not_9_out,
       not_10_out, not_11_out, not_12_out, not_13_out, not_14_out, not_15_out, not_16_out, not_17_out,
       not_18_out, not_19_out, not_20_out, not_21_out, not_22_out, not_23_out, not_24_out, not_25_out,
       not_26_out, not_27_out, not_28_out, not_29_out, not_30_out, not_31_out, not_32_out, not_33_out,
       not_34_out, not_35_out, not_36_out, not_37_out, not_38_out, not_39_out, not_40_out, not_41_out,
       not_42_out, not_43_out, not_44_out, not_45_out, not_46_out, not_47_out, not_48_out, not_49_out,
       not_50_out, not_51_out, not_52_out, not_53_out, not_54_out, not_55_out, not_56_out, not_57_out,
       not_58_out, not_59_out, not_60_out, not_61_out, not_62_out, not_63_out, not_64_out, not_65_out,
       not_66_out, not_67_out, not_68_out, not_69_out, not_70_out, not_71_out, not_72_out, not_73_out,
       not_74_out, not_75_out, not_76_out, not_77_out, not_78_out, not_79_out, not_80_out, not_81_out,
       not_82_out, not_83_out, not_84_out, not_85_out, not_86_out, not_87_out, not_88_out, not_89_out,
       not_90_out, not_91_out, not_92_out, not_93_out, not_94_out, not_95_out, not_96_out, not_97_out,
       not_98_out, not_99_out, not_100_out, not_101_out, not_102_out, not_103_out, not_104_out, not_105_out,
       not_106_out, not_107_out, not_108_out, not_109_out, not_110_out, not_111_out, not_112_out,
       not_113_out, not_114_out, not_115_out, not_116_out, not_117_out, not_118_out, not_119_out,
       not_120_out, not_121_out, not_122_out, not_123_out, not_124_out, not_125_out, not_126_out,
       not_127_out, not_128_out, not_129_out, not_130_out, not_131_out, not_132_out, not_133_out,
       not_134_out, not_135_out, not_136_out, not_137_out, not_138_out, not_139_out, not_140_out,
       not_141_out, not_142_out, not_143_out, not_144_out, not_145_out, not_146_out, not_147_out,
       not_148_out, not_149_out, not_150_out, not_151_out, not_152_out, not_153_out, not_154_out,
       not_155_out, not_156_out, not_157_out, not_158_out, not_159_out, not_160_out, not_161_out,
       not_162_out, not_163_out, not_164_out, not_165_out, not_166_out, not_167_out, not_168_out,
       not_169_out, not_170_out, not_171_out, not_172_out, not_173_out, not_174_out, not_175_out,
       not_176_out, not_177_out, not_178_out, not_179_out, not_180_out, not_181_out, not_182_out,
       not_183_out, not_184_out, not_185_out, not_186_out, not_187_out, not_188_out, not_189_out,
       not_190_out, not_191_out, not_192_out, not_193_out, not_194_out, not_195_out, not_196_out,
       not_197_out, not_198_out, not_199_out, not_200_out, not_201_out, not_202_out, not_203_out,
       not_204_out, not_205_out, not_206_out, not_207_out, not_208_out, not_209_out, not_210_out,
       not_211_out, not_212_out, not_213_out, not_214_out, not_215_out, not_216_out, not_217_out,
       not_218_out, not_219_out, not_220_out, not_221_out, not_222_out, not_223_out, not_224_out,
       not_225_out, not_226_out, not_227_out, not_228_out, not_229_out, not_230_out, not_231_out,
       not_232_out, not_233_out, not_234_out, not_235_out, not_236_out, not_237_out, not_238_out,
       not_239_out, not_240_out, not_241_out, not_242_out, not_243_out, not_244_out, not_245_out,
       not_246_out, not_247_out, not_248_out, not_249_out, not_250_out, not_251_out, not_252_out,
       not_253_out, not_254_out, not_255_out, not_256_out, not_257_out, not_258_out, not_259_out,
       not_260_out, not_261_out, not_262_out, not_263_out, not_264_out, not_265_out, not_266_out,
       not_267_out, not_268_out, not_269_out, not_270_out, not_271_out, not_272_out, not_273_out,
       not_274_out, not_275_out, not_276_out, not_277_out, not_278_out, not_279_out, not_280_out,
       not_281_out, not_282_out, not_283_out, not_284_out, not_285_out, not_286_out, not_287_out,
       not_288_out, not_289_out, not_290_out, not_291_out, not_292_out, not_293_out, not_294_out,
       not_295_out, not_296_out, not_297_out, not_298_out, not_299_out, not_300_out, not_301_out,
       not_302_out, not_303_out, not_304_out, not_305_out, not_306_out, not_307_out, not_308_out,
       not_309_out, not_310_out, not_311_out, not_312_out, not_313_out, not_314_out, not_315_out,
       not_316_out, not_317_out, not_318_out, not_319_out, not_320_out, not_321_out, not_322_out,
       not_323_out, not_324_out, not_325_out, not_326_out, not_327_out, not_328_out, not_329_out,
       not_330_out, not_331_out, not_332_out, not_333_out, not_334_out, not_335_out, not_336_out,
       not_337_out, not_338_out, not_339_out, not_340_out, not_341_out, not_342_out, not_343_out,
       not_344_out, not_345_out, not_346_out, not_347_out, not_348_out, not_349_out, not_350_out,
       not_351_out, not_352_out, not_353_out, not_354_out, not_355_out, not_356_out, not_357_out,
       not_358_out, not_359_out, not_360_out, not_361_out, not_362_out, not_363_out, not_364_out,
       not_365_out, not_366_out, not_367_out, not_368_out, not_369_out, not_370_out, not_371_out, not_372_out;

  not not_1 (not_1_out, OP4);
  not not_2 (not_2_out, OP2);
  not not_3 (not_3_out, OP4);
  not not_4 (not_4_out, OP2);
  not not_5 (not_5_out, OP1);
  not not_6 (not_6_out, OP0);
  not not_7 (not_7_out, OP5);
  not not_8 (not_8_out, OP4);
  not not_9 (not_9_out, OP3);
  not not_10 (not_10_out, OP2);
  not not_11 (not_11_out, OP5);
  not not_12 (not_12_out, OP4);
  not not_13 (not_13_out, OP3);
  not not_14 (not_14_out, OP2);
  not not_15 (not_15_out, OP0);
  not not_16 (not_16_out, OP5);
  not not_17 (not_17_out, OP4);
  not not_18 (not_18_out, OP2);
  not not_19 (not_19_out, OP1);
  not not_20 (not_20_out, OP0);
  not not_21 (not_21_out, OP5);
  not not_22 (not_22_out, OP4);
  not not_23 (not_23_out, OP1);
  not not_24 (not_24_out, OP0);
  not not_25 (not_25_out, OP5);
  not not_26 (not_26_out, OP4);
  not not_27 (not_27_out, OP2);
  not not_28 (not_28_out, OP1);
  not not_29 (not_29_out, OP5);
  not not_30 (not_30_out, OP4);
  not not_31 (not_31_out, OP2);
  not not_32 (not_32_out, OP0);
  not not_33 (not_33_out, OP5);
  not not_34 (not_34_out, OP4);
  not not_35 (not_35_out, OP1);
  not not_36 (not_36_out, OP4);
  not not_37 (not_37_out, OP3);
  not not_38 (not_38_out, OP2);
  not not_39 (not_39_out, OP4);
  not not_40 (not_40_out, OP2);
  not not_41 (not_41_out, OP4);
  not not_42 (not_42_out, OP2);
  not not_43 (not_43_out, OP1);
  not not_44 (not_44_out, OP0);
  not not_45 (not_45_out, OP5);
  not not_46 (not_46_out, OP4);
  not not_47 (not_47_out, OP3);
  not not_48 (not_48_out, OP2);
  not not_49 (not_49_out, OP1);
  not not_50 (not_50_out, OP0);
  not not_51 (not_51_out, F5);
  not not_52 (not_52_out, F4);
  not not_53 (not_53_out, F3);
  not not_54 (not_54_out, F2);
  not not_55 (not_55_out, F1);
  not not_56 (not_56_out, F0);
  not not_57 (not_57_out, OP5);
  not not_58 (not_58_out, OP4);
  not not_59 (not_59_out, OP3);
  not not_60 (not_60_out, OP2);
  not not_61 (not_61_out, OP1);
  not not_62 (not_62_out, OP0);
  not not_63 (not_63_out, F5);
  not not_64 (not_64_out, F4);
  not not_65 (not_65_out, F3);
  not not_66 (not_66_out, F2);
  not not_67 (not_67_out, OP5);
  not not_68 (not_68_out, OP4);
  not not_69 (not_69_out, OP3);
  not not_70 (not_70_out, OP2);
  not not_71 (not_71_out, OP1);
  not not_72 (not_72_out, OP0);
  not not_73 (not_73_out, F5);
  not not_74 (not_74_out, F4);
  not not_75 (not_75_out, F3);
  not not_76 (not_76_out, F2);
  not not_77 (not_77_out, F0);
  not not_78 (not_78_out, OP5);
  not not_79 (not_79_out, OP4);
  not not_80 (not_80_out, OP3);
  not not_81 (not_81_out, OP2);
  not not_82 (not_82_out, OP1);
  not not_83 (not_83_out, OP0);
  not not_84 (not_84_out, F4);
  not not_85 (not_85_out, F3);
  not not_86 (not_86_out, F2);
  not not_87 (not_87_out, F1);
  not not_88 (not_88_out, F0);
  not not_89 (not_89_out, OP5);
  not not_90 (not_90_out, OP4);
  not not_91 (not_91_out, OP3);
  not not_92 (not_92_out, OP2);
  not not_93 (not_93_out, OP1);
  not not_94 (not_94_out, OP0);
  not not_95 (not_95_out, F4);
  not not_96 (not_96_out, F3);
  not not_97 (not_97_out, F2);
  not not_98 (not_98_out, F1);
  not not_99 (not_99_out, OP5);
  not not_100 (not_100_out, OP4);
  not not_101 (not_101_out, OP3);
  not not_102 (not_102_out, OP2);
  not not_103 (not_103_out, OP1);
  not not_104 (not_104_out, OP0);
  not not_105 (not_105_out, F4);
  not not_106 (not_106_out, F3);
  not not_107 (not_107_out, F2);
  not not_108 (not_108_out, F0);
  not not_109 (not_109_out, OP5);
  not not_110 (not_110_out, OP4);
  not not_111 (not_111_out, OP3);
  not not_112 (not_112_out, OP2);
  not not_113 (not_113_out, OP1);
  not not_114 (not_114_out, OP0);
  not not_115 (not_115_out, F4);
  not not_116 (not_116_out, F3);
  not not_117 (not_117_out, F1);
  not not_118 (not_118_out, F0);
  not not_119 (not_119_out, OP5);
  not not_120 (not_120_out, OP4);
  not not_121 (not_121_out, OP3);
  not not_122 (not_122_out, OP2);
  not not_123 (not_123_out, OP1);
  not not_124 (not_124_out, OP0);
  not not_125 (not_125_out, F4);
  not not_126 (not_126_out, F3);
  not not_127 (not_127_out, F1);
  not not_128 (not_128_out, OP5);
  not not_129 (not_129_out, OP4);
  not not_130 (not_130_out, OP3);
  not not_131 (not_131_out, OP2);
  not not_132 (not_132_out, OP1);
  not not_133 (not_133_out, OP0);
  not not_134 (not_134_out, F4);
  not not_135 (not_135_out, F3);
  not not_136 (not_136_out, OP5);
  not not_137 (not_137_out, OP4);
  not not_138 (not_138_out, OP3);
  not not_139 (not_139_out, OP2);
  not not_140 (not_140_out, OP1);
  not not_141 (not_141_out, OP0);
  not not_142 (not_142_out, F4);
  not not_143 (not_143_out, F2);
  not not_144 (not_144_out, F0);
  not not_145 (not_145_out, OP5);
  not not_146 (not_146_out, OP4);
  not not_147 (not_147_out, OP3);
  not not_148 (not_148_out, OP2);
  not not_149 (not_149_out, OP1);
  not not_150 (not_150_out, OP0);
  not not_151 (not_151_out, F4);
  not not_152 (not_152_out, F2);
  not not_153 (not_153_out, OP5);
  not not_154 (not_154_out, OP4);
  not not_155 (not_155_out, OP3);
  not not_156 (not_156_out, OP2);
  not not_157 (not_157_out, OP5);
  not not_158 (not_158_out, OP4);
  not not_159 (not_159_out, OP2);
  not not_160 (not_160_out, OP1);
  not not_161 (not_161_out, OP0);
  not not_162 (not_162_out, OP5);
  not not_163 (not_163_out, OP4);
  not not_164 (not_164_out, OP1);
  not not_165 (not_165_out, OP0);
  not not_166 (not_166_out, OP5);
  not not_167 (not_167_out, OP4);
  not not_168 (not_168_out, OP2);
  not not_169 (not_169_out, OP1);
  not not_170 (not_170_out, OP5);
  not not_171 (not_171_out, OP4);
  not not_172 (not_172_out, OP2);
  not not_173 (not_173_out, OP0);
  not not_174 (not_174_out, OP5);
  not not_175 (not_175_out, OP4);
  not not_176 (not_176_out, OP1);
  not not_177 (not_177_out, OP4);
  not not_178 (not_178_out, OP3);
  not not_179 (not_179_out, OP2);
  not not_180 (not_180_out, OP5);
  not not_181 (not_181_out, OP4);
  not not_182 (not_182_out, OP3);
  not not_183 (not_183_out, OP2);
  not not_184 (not_184_out, OP1);
  not not_185 (not_185_out, OP0);
  not not_186 (not_186_out, F5);
  not not_187 (not_187_out, F3);
  not not_188 (not_188_out, F2);
  not not_189 (not_189_out, F0);
  not not_190 (not_190_out, OP5);
  not not_191 (not_191_out, OP4);
  not not_192 (not_192_out, OP3);
  not not_193 (not_193_out, OP2);
  not not_194 (not_194_out, OP1);
  not not_195 (not_195_out, OP0);
  not not_196 (not_196_out, F5);
  not not_197 (not_197_out, F4);
  not not_198 (not_198_out, F1);
  not not_199 (not_199_out, F0);
  not not_200 (not_200_out, OP4);
  not not_201 (not_201_out, OP3);
  not not_202 (not_202_out, OP2);
  not not_203 (not_203_out, OP5);
  not not_204 (not_204_out, OP4);
  not not_205 (not_205_out, OP3);
  not not_206 (not_206_out, OP1);
  not not_207 (not_207_out, OP0);
  not not_208 (not_208_out, OP5);
  not not_209 (not_209_out, OP4);
  not not_210 (not_210_out, OP3);
  not not_211 (not_211_out, OP1);
  not not_212 (not_212_out, OP5);
  not not_213 (not_213_out, OP4);
  not not_214 (not_214_out, OP2);
  not not_215 (not_215_out, OP1);
  not not_216 (not_216_out, OP0);
  not not_217 (not_217_out, OP5);
  not not_218 (not_218_out, OP4);
  not not_219 (not_219_out, OP2);
  not not_220 (not_220_out, OP0);
  not not_221 (not_221_out, OP4);
  not not_222 (not_222_out, OP3);
  not not_223 (not_223_out, OP2);
  not not_224 (not_224_out, OP4);
  not not_225 (not_225_out, OP2);
  not not_226 (not_226_out, OP4);
  not not_227 (not_227_out, OP2);
  not not_228 (not_228_out, OP1);
  not not_229 (not_229_out, OP0);
  not not_230 (not_230_out, OP5);
  not not_231 (not_231_out, OP4);
  not not_232 (not_232_out, OP3);
  not not_233 (not_233_out, OP2);
  not not_234 (not_234_out, OP1);
  not not_235 (not_235_out, OP5);
  not not_236 (not_236_out, OP4);
  not not_237 (not_237_out, OP3);
  not not_238 (not_238_out, OP2);
  not not_239 (not_239_out, OP1);
  not not_240 (not_240_out, OP0);
  not not_241 (not_241_out, F5);
  not not_242 (not_242_out, F4);
  not not_243 (not_243_out, F3);
  not not_244 (not_244_out, F2);
  not not_245 (not_245_out, F1);
  not not_246 (not_246_out, F0);
  not not_247 (not_247_out, OP5);
  not not_248 (not_248_out, OP4);
  not not_249 (not_249_out, OP3);
  not not_250 (not_250_out, OP2);
  not not_251 (not_251_out, OP1);
  not not_252 (not_252_out, OP0);
  not not_253 (not_253_out, F5);
  not not_254 (not_254_out, F4);
  not not_255 (not_255_out, F3);
  not not_256 (not_256_out, F2);
  not not_257 (not_257_out, OP5);
  not not_258 (not_258_out, OP4);
  not not_259 (not_259_out, OP3);
  not not_260 (not_260_out, OP2);
  not not_261 (not_261_out, OP1);
  not not_262 (not_262_out, OP0);
  not not_263 (not_263_out, F5);
  not not_264 (not_264_out, F4);
  not not_265 (not_265_out, F3);
  not not_266 (not_266_out, F2);
  not not_267 (not_267_out, F0);
  not not_268 (not_268_out, OP5);
  not not_269 (not_269_out, OP4);
  not not_270 (not_270_out, OP3);
  not not_271 (not_271_out, OP2);
  not not_272 (not_272_out, OP1);
  not not_273 (not_273_out, OP0);
  not not_274 (not_274_out, F4);
  not not_275 (not_275_out, F3);
  not not_276 (not_276_out, F2);
  not not_277 (not_277_out, F1);
  not not_278 (not_278_out, F0);
  not not_279 (not_279_out, OP5);
  not not_280 (not_280_out, OP4);
  not not_281 (not_281_out, OP3);
  not not_282 (not_282_out, OP2);
  not not_283 (not_283_out, OP1);
  not not_284 (not_284_out, OP0);
  not not_285 (not_285_out, F4);
  not not_286 (not_286_out, F3);
  not not_287 (not_287_out, F2);
  not not_288 (not_288_out, F1);
  not not_289 (not_289_out, OP5);
  not not_290 (not_290_out, OP4);
  not not_291 (not_291_out, OP3);
  not not_292 (not_292_out, OP2);
  not not_293 (not_293_out, OP1);
  not not_294 (not_294_out, OP0);
  not not_295 (not_295_out, F4);
  not not_296 (not_296_out, F3);
  not not_297 (not_297_out, F2);
  not not_298 (not_298_out, F0);
  not not_299 (not_299_out, OP5);
  not not_300 (not_300_out, OP4);
  not not_301 (not_301_out, OP3);
  not not_302 (not_302_out, OP2);
  not not_303 (not_303_out, OP1);
  not not_304 (not_304_out, OP0);
  not not_305 (not_305_out, F4);
  not not_306 (not_306_out, F3);
  not not_307 (not_307_out, F1);
  not not_308 (not_308_out, F0);
  not not_309 (not_309_out, OP5);
  not not_310 (not_310_out, OP4);
  not not_311 (not_311_out, OP3);
  not not_312 (not_312_out, OP2);
  not not_313 (not_313_out, OP1);
  not not_314 (not_314_out, OP0);
  not not_315 (not_315_out, F4);
  not not_316 (not_316_out, F3);
  not not_317 (not_317_out, F1);
  not not_318 (not_318_out, OP5);
  not not_319 (not_319_out, OP4);
  not not_320 (not_320_out, OP3);
  not not_321 (not_321_out, OP2);
  not not_322 (not_322_out, OP1);
  not not_323 (not_323_out, OP0);
  not not_324 (not_324_out, F4);
  not not_325 (not_325_out, F3);
  not not_326 (not_326_out, OP5);
  not not_327 (not_327_out, OP4);
  not not_328 (not_328_out, OP3);
  not not_329 (not_329_out, OP2);
  not not_330 (not_330_out, OP1);
  not not_331 (not_331_out, OP0);
  not not_332 (not_332_out, F4);
  not not_333 (not_333_out, F2);
  not not_334 (not_334_out, F0);
  not not_335 (not_335_out, OP5);
  not not_336 (not_336_out, OP4);
  not not_337 (not_337_out, OP3);
  not not_338 (not_338_out, OP2);
  not not_339 (not_339_out, OP1);
  not not_340 (not_340_out, OP0);
  not not_341 (not_341_out, F4);
  not not_342 (not_342_out, F2);
  not not_343 (not_343_out, OP5);
  not not_344 (not_344_out, OP4);
  not not_345 (not_345_out, OP3);
  not not_346 (not_346_out, OP2);
  not not_347 (not_347_out, OP1);
  not not_348 (not_348_out, OP0);
  not not_349 (not_349_out, F5);
  not not_350 (not_350_out, F3);
  not not_351 (not_351_out, F2);
  not not_352 (not_352_out, F0);
  not not_353 (not_353_out, OP5);
  not not_354 (not_354_out, OP4);
  not not_355 (not_355_out, OP3);
  not not_356 (not_356_out, OP1);
  not not_357 (not_357_out, OP0);
  not not_358 (not_358_out, OP5);
  not not_359 (not_359_out, OP4);
  not not_360 (not_360_out, OP3);
  not not_361 (not_361_out, OP1);
  not not_362 (not_362_out, OP5);
  not not_363 (not_363_out, OP4);
  not not_364 (not_364_out, OP3);
  not not_365 (not_365_out, OP2);
  not not_366 (not_366_out, OP1);
  not not_367 (not_367_out, OP0);
  not not_368 (not_368_out, F5);
  not not_369 (not_369_out, F4);
  not not_370 (not_370_out, F2);
  not not_371 (not_371_out, F1);
  not not_372 (not_372_out, F0);
  and and_1 (and_1_out, OP5, not_1_out, OP3, not_2_out, OP1, OP0);
  and and_2 (and_2_out, OP5, not_3_out, OP3, not_4_out, not_5_out, not_6_out);
  and and_3 (JAL, not_7_out, not_8_out, not_9_out, not_10_out, OP1, OP0);
  and and_4 (JMP, not_11_out, not_12_out, not_13_out, not_14_out, OP1, not_15_out);
  and and_5 (and_5_out, not_16_out, not_17_out, OP3, not_18_out, not_19_out, not_20_out);
  and and_6 (and_6_out, not_21_out, not_22_out, OP3, OP2, not_23_out, not_24_out);
  and and_7 (and_7_out, not_25_out, not_26_out, OP3, not_27_out, not_28_out, OP0);
  and and_8 (and_8_out, not_29_out, not_30_out, OP3, not_31_out, OP1, not_32_out);
  and and_9 (and_9_out, not_33_out, not_34_out, OP3, OP2, not_35_out, OP0);
  and and_10 (and_10_out, OP5, not_36_out, not_37_out, not_38_out, OP1, OP0);
  and and_11 (and_11_out, OP5, not_39_out, OP3, not_40_out, OP1, OP0);
  and and_12 (and_12_out, OP5, not_41_out, OP3, not_42_out, not_43_out, not_44_out);
  and and_13 (and_13_out, not_45_out, not_46_out, not_47_out, not_48_out, not_49_out, not_50_out, not_51_out, not_52_out, not_53_out, not_54_out, not_55_out, not_56_out);
  and and_14 (and_14_out, not_57_out, not_58_out, not_59_out, not_60_out, not_61_out, not_62_out, not_63_out, not_64_out, not_65_out, not_66_out, F1, F0);
  and and_15 (and_15_out, not_67_out, not_68_out, not_69_out, not_70_out, not_71_out, not_72_out, not_73_out, not_74_out, not_75_out, not_76_out, F1, not_77_out);
  and and_16 (and_16_out, not_78_out, not_79_out, not_80_out, not_81_out, not_82_out, not_83_out, F5, not_84_out, not_85_out, not_86_out, not_87_out, not_88_out);
  and and_17 (and_17_out, not_89_out, not_90_out, not_91_out, not_92_out, not_93_out, not_94_out, F5, not_95_out, not_96_out, not_97_out, not_98_out, F0);
  and and_18 (and_18_out, not_99_out, not_100_out, not_101_out, not_102_out, not_103_out, not_104_out, F5, not_105_out, not_106_out, not_107_out, F1, not_108_out);
  and and_19 (and_19_out, not_109_out, not_110_out, not_111_out, not_112_out, not_113_out, not_114_out, F5, not_115_out, not_116_out, F2, not_117_out, not_118_out);
  and and_20 (and_20_out, not_119_out, not_120_out, not_121_out, not_122_out, not_123_out, not_124_out, F5, not_125_out, not_126_out, F2, not_127_out, F0);
  and and_21 (and_21_out, not_128_out, not_129_out, not_130_out, not_131_out, not_132_out, not_133_out, F5, not_134_out, not_135_out, F2, F1, F0);
  and and_22 (and_22_out, not_136_out, not_137_out, not_138_out, not_139_out, not_140_out, not_141_out, F5, not_142_out, F3, not_143_out, F1, not_144_out);
  and and_23 (and_23_out, not_145_out, not_146_out, not_147_out, not_148_out, not_149_out, not_150_out, F5, not_151_out, F3, not_152_out, F1, F0);
  and and_24 (and_24_out, not_153_out, not_154_out, not_155_out, not_156_out, OP1, OP0);
  and and_25 (and_25_out, not_157_out, not_158_out, OP3, not_159_out, not_160_out, not_161_out);
  and and_26 (and_26_out, not_162_out, not_163_out, OP3, OP2, not_164_out, not_165_out);
  and and_27 (and_27_out, not_166_out, not_167_out, OP3, not_168_out, not_169_out, OP0);
  and and_28 (and_28_out, not_170_out, not_171_out, OP3, not_172_out, OP1, not_173_out);
  and and_29 (and_29_out, not_174_out, not_175_out, OP3, OP2, not_176_out, OP0);
  and and_30 (and_30_out, OP5, not_177_out, not_178_out, not_179_out, OP1, OP0);
  and and_31 (and_31_out, not_180_out, not_181_out, not_182_out, not_183_out, not_184_out, not_185_out, not_186_out, F4, not_187_out, not_188_out, F1, not_189_out);
  and and_32 (SysCALL, not_190_out, not_191_out, not_192_out, not_193_out, not_194_out, not_195_out, not_196_out, not_197_out, F3, F2, not_198_out, not_199_out);
  and and_33 (MemtoReg, OP5, not_200_out, not_201_out, not_202_out, OP1, OP0);
  and and_34 (and_34_out, not_203_out, not_204_out, not_205_out, OP2, not_206_out, not_207_out);
  and and_35 (and_35_out, not_208_out, not_209_out, not_210_out, OP2, not_211_out, OP0);
  and and_36 (and_36_out, not_212_out, not_213_out, OP3, not_214_out, not_215_out, not_216_out);
  and and_37 (and_37_out, not_217_out, not_218_out, OP3, not_219_out, OP1, not_220_out);
  and and_38 (and_38_out, OP5, not_221_out, not_222_out, not_223_out, OP1, OP0);
  and and_39 (and_39_out, OP5, not_224_out, OP3, not_225_out, OP1, OP0);
  and and_40 (and_40_out, OP5, not_226_out, OP3, not_227_out, not_228_out, not_229_out);
  and and_41 (and_41_out, not_230_out, not_231_out, not_232_out, not_233_out, not_234_out, OP0);
  and and_42 (and_42_out, not_235_out, not_236_out, not_237_out, not_238_out, not_239_out, not_240_out, not_241_out, not_242_out, not_243_out, not_244_out, not_245_out, not_246_out);
  and and_43 (and_43_out, not_247_out, not_248_out, not_249_out, not_250_out, not_251_out, not_252_out, not_253_out, not_254_out, not_255_out, not_256_out, F1, F0);
  and and_44 (and_44_out, not_257_out, not_258_out, not_259_out, not_260_out, not_261_out, not_262_out, not_263_out, not_264_out, not_265_out, not_266_out, F1, not_267_out);
  and and_45 (and_45_out, not_268_out, not_269_out, not_270_out, not_271_out, not_272_out, not_273_out, F5, not_274_out, not_275_out, not_276_out, not_277_out, not_278_out);
  and and_46 (and_46_out, not_279_out, not_280_out, not_281_out, not_282_out, not_283_out, not_284_out, F5, not_285_out, not_286_out, not_287_out, not_288_out, F0);
  and and_47 (and_47_out, not_289_out, not_290_out, not_291_out, not_292_out, not_293_out, not_294_out, F5, not_295_out, not_296_out, not_297_out, F1, not_298_out);
  and and_48 (and_48_out, not_299_out, not_300_out, not_301_out, not_302_out, not_303_out, not_304_out, F5, not_305_out, not_306_out, F2, not_307_out, not_308_out);
  and and_49 (and_49_out, not_309_out, not_310_out, not_311_out, not_312_out, not_313_out, not_314_out, F5, not_315_out, not_316_out, F2, not_317_out, F0);
  and and_50 (and_50_out, not_318_out, not_319_out, not_320_out, not_321_out, not_322_out, not_323_out, F5, not_324_out, not_325_out, F2, F1, F0);
  and and_51 (and_51_out, not_326_out, not_327_out, not_328_out, not_329_out, not_330_out, not_331_out, F5, not_332_out, F3, not_333_out, F1, not_334_out);
  and and_52 (and_52_out, not_335_out, not_336_out, not_337_out, not_338_out, not_339_out, not_340_out, F5, not_341_out, F3, not_342_out, F1, F0);
  and and_53 (and_53_out, not_343_out, not_344_out, not_345_out, not_346_out, not_347_out, not_348_out, not_349_out, F4, not_350_out, not_351_out, F1, not_352_out);
  and and_54 (BEQ, not_353_out, not_354_out, not_355_out, OP2, not_356_out, not_357_out);
  and and_55 (BNE, not_358_out, not_359_out, not_360_out, OP2, not_361_out, OP0);
  and and_56 (JR, not_362_out, not_363_out, not_364_out, not_365_out, not_366_out, not_367_out, not_368_out, not_369_out, F3, not_370_out, not_371_out, not_372_out);
  or or_1 (MemWrite, and_1_out, and_2_out);
  or or_2 (ALU_SRC, and_5_out, and_6_out, and_7_out, and_8_out, and_9_out, and_10_out, and_11_out, and_12_out);
  or or_3 (SignedExt, and_34_out, and_35_out, and_36_out, and_37_out, and_38_out, and_39_out, and_40_out, and_41_out);
  or or_4 (RegWrite, and_13_out, and_14_out, and_15_out, and_16_out, and_17_out, and_18_out, and_19_out, and_20_out, and_21_out, and_22_out, and_23_out, and_24_out, and_25_out, and_26_out, and_27_out, and_28_out, and_29_out, and_30_out, and_31_out);
  or or_5 (RegDst, and_42_out, and_43_out, and_44_out, and_45_out, and_46_out, and_47_out, and_48_out, and_49_out, and_50_out, and_51_out, and_52_out, and_53_out);
endmodule

// ALU
module MIPS_ALU (
  input  [4:0] shamt,
  input  [31:0] X,
  input  [31:0] Y,
  input  [3:0] AluOP,
  output Equal,
  output [31:0] Result,
  output [31:0] Result_2
);

  wire [0:0] comparator_1_lt, comparator_2_lt;
  wire [31:0] adder_1_out, AND_out, divider_1_out, divider_1_rem, multiplier_1_cout, multiplier_1_out,
       NOR_out, OR_out, shifter_1_out, shifter_2_out, shifter_3_out, subtractor_1_out, XOR_out;

  assign AND_out = X & Y;  // AND_Gate AND, 32 bits wide
  assign OR_out = X | Y;  // OR_Gate OR, 32 bits wide
  Shifter #(.width(32)) shifter_1 (.in(Y), .\dist (shamt), .out(shifter_1_out));
  Shifter #(.width(32), .shift("ar")) shifter_2 (.in(Y), .\dist (shamt), .out(shifter_2_out));
  Shifter #(.width(32), .shift("lr")) shifter_3 (.in(Y), .\dist (shamt), .out(shifter_3_out));
  Multiplier #(.width(32)) multiplier_1 (.a(X), .b(Y), .out(multiplier_1_out), .cout(multiplier_1_cout));  // open: cin
  Divider #(.width(32)) divider_1 (.a(X), .b(Y), .out(divider_1_out), .rem(divider_1_rem));  // open: upper
  Adder #(.width(32)) adder_1 (.a(X), .b(Y), .out(adder_1_out));  // open: cin, cout
  Subtractor #(.width(32)) subtractor_1 (.a(X), .b(Y), .out(subtractor_1_out));  // open: bin, bout
  assign XOR_out = X ^ Y;  // XOR_Gate XOR, 32 bits wide
  assign NOR_out = ~(X | Y);  // NOR_Gate NOR, 32 bits wide
  Comparator #(.width(32)) comparator_1 (.a(X), .b(Y), .eq(Equal), .lt(comparator_1_lt[0]));  // open: gt
  Comparator #(.width(32), .mode("unsigned")) comparator_2 (.a(X), .b(Y), .lt(comparator_2_lt[0]));  // open: gt, eq
  Multiplexer #(.select(4), .width(32), .enable("false")) multiplexer_1 (
    .in0(shifter_1_out), .in1(shifter_2_out), .in2(shifter_3_out), .in3(multiplier_1_out),
    .in4(divider_1_out), .in5(adder_1_out), .in6(subtractor_1_out), .in7(AND_out), .in8(OR_out),
    .in9(XOR_out), .in10(NOR_out), .in11({{31{1'b0}}, comparator_1_lt[0]}),
    .in12({{31{1'b0}}, comparator_2_lt[0]}), .in13({32{1'b0}}), .in14({32{1'b0}}), .in15({32{1'b0}}),
    .out(Result), .sel(AluOP));
  Multiplexer #(.select(4), .width(32), .enable("false")) multiplexer_2 (
    .in0({32{1'b0}}), .in1({32{1'b0}}), .in2({32{1'b0}}), .in3(multiplier_1_cout), .in4(divider_1_rem),
    .in5({32{1'b0}}), .in6({32{1'b0}}), .in7({32{1'b0}}), .in8({32{1'b0}}), .in9({32{1'b0}}),
    .in10({32{1'b0}}), .in11({32{1'b0}}), .in12({32{1'b0}}), .in13({32{1'b0}}), .in14({32{1'b0}}),
    .in15({32{1'b0}}), .out(Result_2), .sel(AluOP));

  // Other names for the same wires on the sheet: Result2[31:0] = Result_2; S[3:0] = AluOP

  // Notes on the sheet:
  //   不要改变此引脚区域内容，也不要改变ALU封装形式
  //   输入引脚
  //   输出引脚
endmodule

module MIPS_Regifile (
  input  [31:0] Din,
  input  Clk,
  input  WE,
  input  [4:0] R1_num,
  input  [4:0] W_num,
  input  [4:0] R2_num,
  output [31:0] R1,
  output [31:0] R2
);

  // RegisterFile registerfile_1: pin names not known; wires that end beside it: Din, Clk, WE, W_num, R1_num, R2_num, R1, R2
endmodule

module ideal_pipeline (
);

  wire and_1_out, and_3_out, and_4_out, Branch, CLK, comparator_1_eq, ex_mem_1_en_out, ex_mem_1_memtoreg_out,
       ex_mem_1_memwrite_out, ex_mem_1_regwrite_out, Go, HALT, id_ex_1_alusrcb_out, id_ex_1_beq_out,
       id_ex_1_bne_out, id_ex_1_en_out, id_ex_1_memtoreg_out, id_ex_1_memwrite_out, id_ex_1_regwrite_out,
       JAL, JMP, JR, mem_wb_1_en_out, mem_wb_1_memtoreg_out, mem_wb_1_regwrite_out, mips_alu_1_equal,
       or_1_out, or_2_out, RST, SignedExt, Syscall, \硬布线控制器_1_alu_src , \硬布线控制器_1_beq , \硬布线控制器_1_bne ,
       \硬布线控制器_1_memtoreg , \硬布线控制器_1_memwrite , \硬布线控制器_1_regdst , \硬布线控制器_1_regwrite ;
  wire [3:0] id_ex_1_aluop_out, \硬布线控制器_1_alu_op ;
  wire [4:0] ex_mem_1_w__out, id_ex_1_shamt_out, id_ex_1_w__out, if_id_1_ir_out_2, mem_wb_1_w__out,
       multiplexer_2_out, multiplexer_3_out, multiplexer_4_out;
  wire [15:0] \总周期数 ;
  wire [31:0] adder_1_out, adder_2_out, AluResult2, bit_extender_1_out, bit_extender_2_out,
       bit_extender_3_out, ex_mem_1_alu_result_out, ex_mem_1_pc_out, ex_mem_1_reg_b_out, id_ex_1_imm_out,
       id_ex_1_pc_out, id_ex_1_reg_a_out, id_ex_1_reg_b_out, if_id_1_ir_out, if_id_1_pc_out, \JPC_不支持 ,
       LedData, mem_wb_1_alu_result_out, mem_wb_1_memdata_out, mem_wb_1_pc_out, mips_alu_1_result,
       multiplexer_1_out, multiplexer_5_out, multiplexer_6_out, multiplexer_7_out, multiplexer_8_out, PC_q,
       R2, ram_1_data, rom_1_data, RS, shifter_1_out, shifter_2_out;

  Button \u_总复位  (.out(RST));
  Button u_Go (.out(Go));
  Clock clock_1 (.out(CLK));
  Hex_Digit_Display hex_digit_display_1 (.value(LedData[27:24]));  // open: dp
  Hex_Digit_Display hex_digit_display_2 (.value(LedData[31:28]));  // open: dp
  Multiplexer #(.width(32), .enable("false")) multiplexer_1 (
    .in0(adder_1_out), .in1(adder_2_out), .out(multiplexer_1_out), .sel(Branch));
  or or_1 (or_1_out, mem_wb_1_en_out, or_2_out);
  Hex_Digit_Display hex_digit_display_3 (.value(LedData[19:16]));  // open: dp
  Hex_Digit_Display hex_digit_display_4 (.value(LedData[23:20]));  // open: dp
  or or_2 (or_2_out, Go, ~HALT);  // OR_Gate
  Hex_Digit_Display hex_digit_display_5 (.value(LedData[15:12]));  // open: dp
  Hex_Digit_Display hex_digit_display_6 (.value(LedData[11:8]));  // open: dp
  Counter #(.width(16), .max('hffff)) counter_1 (
    .count(or_1_out), .Q(\总周期数 ), .clk(CLK), .clr(RST));  // open: load, D, carry
  Register #(.width(32)) PC (.D(multiplexer_1_out), .en(or_2_out), .Q(PC_q), .clk(CLK), .clr(RST));
  Hex_Digit_Display hex_digit_display_7 (.value(LedData[7:4]));  // open: dp
  Hex_Digit_Display hex_digit_display_8 (.value(LedData[3:0]));  // open: dp
  Adder #(.width(32)) adder_1 (.a(PC_q), .b(32'h4), .out(adder_1_out));  // open: cin, cout
  ROM #(.addrWidth(10), .dataWidth(32)) rom_1 (.addr(PC_q[11:2]), .data(rom_1_data));  // open: sel
  // Probe on \总周期数 
  // Probe on {16{1'b0}}
  // Probe on {16{1'b0}}
  IF_ID if_id_1 (
    .IR(rom_1_data), .PC(adder_1_out), .En(or_2_out), .clk(CLK), .rst(RST),
    .IR_out({if_id_1_ir_out[31:11], if_id_1_ir_out_2, if_id_1_ir_out[5:0]}), .PC_out(if_id_1_pc_out));  // open: En_out
  \硬布线控制器  \u_硬布线控制器_1  (
    .Func(if_id_1_ir_out[5:0]), .OP(if_id_1_ir_out[31:26]), .ALU_OP(\硬布线控制器_1_alu_op ),
    .MemToReg(\硬布线控制器_1_memtoreg ), .MemWrite(\硬布线控制器_1_memwrite ), .ALU_SRC(\硬布线控制器_1_alu_src ),
    .RegWrite(\硬布线控制器_1_regwrite ), .SysCALL(Syscall), .SignedExt(SignedExt), .RegDst(\硬布线控制器_1_regdst ),
    .JR(JR), .JMP(JMP), .Beq(\硬布线控制器_1_beq ), .JAL(JAL), .Bne(\硬布线控制器_1_bne ));
  Multiplexer #(.width(5), .enable("false")) multiplexer_2 (
    .in0(if_id_1_ir_out[25:21]), .in1(5'b00010), .out(multiplexer_2_out), .sel(Syscall));
  Multiplexer #(.width(5), .enable("false")) multiplexer_3 (
    .in0(if_id_1_ir_out[20:16]), .in1(5'b00100), .out(multiplexer_3_out), .sel(Syscall));
  Multiplexer #(.width(5), .enable("false")) multiplexer_4 (
    .in0(if_id_1_ir_out[20:16]), .in1(if_id_1_ir_out[15:11]), .out(multiplexer_4_out), .sel(\硬布线控制器_1_regdst ));
  assign bit_extender_1_out = {{16{1'b0}}, {if_id_1_ir_out[15:11], if_id_1_ir_out_2, if_id_1_ir_out[5:0]}};  // Bit_Extender bit_extender_1
  assign bit_extender_2_out = {{16{if_id_1_ir_out[15]}}, {if_id_1_ir_out[15:11], if_id_1_ir_out_2, if_id_1_ir_out[5:0]}};  // Bit_Extender bit_extender_2
  assign bit_extender_3_out = {{6{1'b0}}, {if_id_1_ir_out[25:11], if_id_1_ir_out_2, if_id_1_ir_out[5:0]}};  // Bit_Extender bit_extender_3
  MIPS_Regifile mips_regifile_1 (
    .Din(multiplexer_7_out), .Clk(CLK), .R1(RS), .R2(R2), .WE(mem_wb_1_regwrite_out),
    .W_num(mem_wb_1_w__out), .R1_num(multiplexer_2_out), .R2_num(multiplexer_3_out));
  Multiplexer #(.width(32), .enable("false")) multiplexer_5 (
    .in0(bit_extender_1_out), .in1(bit_extender_2_out), .out(multiplexer_5_out), .sel(SignedExt));
  Shifter #(.width(32)) shifter_1 (.in(bit_extender_3_out), .\dist (5'b00010), .out(shifter_1_out));
  Comparator #(.width(32)) comparator_1 (.a(RS), .b(32'h22), .eq(comparator_1_eq));  // open: gt, lt
  and and_1 (and_1_out, Syscall, comparator_1_eq);
  Register #(.width(32)) Led (.D(R2), .en(and_1_out), .Q(LedData), .clk(CLK), .clr(RST));
  and and_2 (HALT, ~comparator_1_eq, Syscall);  // AND_Gate
  ID_EX id_ex_1 (
    .PC(if_id_1_pc_out), .Reg_A(RS), .Reg_B(R2), .Imm(multiplexer_5_out), .En(or_2_out), .clk(CLK),
    .rst(RST), .PC_out(id_ex_1_pc_out), .Reg_A_out(id_ex_1_reg_a_out), .Reg_B_out(id_ex_1_reg_b_out),
    .Imm_out(id_ex_1_imm_out), .RegWrite(\硬布线控制器_1_regwrite ), .RegWrite_out(id_ex_1_regwrite_out),
    .MemtoReg(\硬布线控制器_1_memtoreg ), .MemtoReg_out(id_ex_1_memtoreg_out), .W_num(multiplexer_4_out),
    .W__out(id_ex_1_w__out), .beq(\硬布线控制器_1_beq ), .beq_out(id_ex_1_beq_out), .bne(\硬布线控制器_1_bne ),
    .bne_out(id_ex_1_bne_out), .ALUop(\硬布线控制器_1_alu_op ), .ALUop_out(id_ex_1_aluop_out),
    .MemWrite(\硬布线控制器_1_memwrite ), .MemWrite_out(id_ex_1_memwrite_out), .ALUsrcB(\硬布线控制器_1_alu_src ),
    .ALUsrcB_out(id_ex_1_alusrcb_out), .shamt(if_id_1_ir_out_2), .shamt_out(id_ex_1_shamt_out),
    .JPC(shifter_1_out), .JPC_out(\JPC_不支持 ), .En_out(id_ex_1_en_out));
  Shifter #(.width(32)) shifter_2 (.in(id_ex_1_imm_out), .\dist (5'b00010), .out(shifter_2_out));
  Multiplexer #(.width(32), .enable("false")) multiplexer_6 (
    .in0(id_ex_1_reg_b_out), .in1(id_ex_1_imm_out), .out(multiplexer_6_out), .sel(id_ex_1_alusrcb_out));
  Adder #(.width(32)) adder_2 (.a(id_ex_1_pc_out), .b(shifter_2_out), .out(adder_2_out));  // open: cin, cout
  MIPS_ALU mips_alu_1 (
    .X(id_ex_1_reg_a_out), .Y(multiplexer_6_out), .AluOP(id_ex_1_aluop_out), .Equal(mips_alu_1_equal),
    .Result(mips_alu_1_result), .Result_2(AluResult2), .shamt(id_ex_1_shamt_out));
  and and_3 (and_3_out, mips_alu_1_equal, id_ex_1_beq_out);
  and and_4 (and_4_out, id_ex_1_bne_out, ~mips_alu_1_equal);  // AND_Gate
  or or_3 (Branch, and_3_out, and_4_out);
  EX_MEM ex_mem_1 (
    .PC(id_ex_1_pc_out), .RegWrite(id_ex_1_regwrite_out), .ALU_Result(mips_alu_1_result),
    .MemtoReg(id_ex_1_memtoreg_out), .Reg_B(id_ex_1_reg_b_out), .W_num(id_ex_1_w__out),
    .MemWrite(id_ex_1_memwrite_out), .En(id_ex_1_en_out), .clk(CLK), .rst(RST), .PC_out(ex_mem_1_pc_out),
    .RegWrite_out(ex_mem_1_regwrite_out), .ALU_Result_out(ex_mem_1_alu_result_out),
    .MemtoReg_out(ex_mem_1_memtoreg_out), .Reg_B_out(ex_mem_1_reg_b_out), .W__out(ex_mem_1_w__out),
    .MemWrite_out(ex_mem_1_memwrite_out), .En_out(ex_mem_1_en_out));
  RAM #(.addrWidth(10), .dataWidth(32), .bus("separate")) ram_1 (
    .addr(ex_mem_1_alu_result_out[11:2]), .din(ex_mem_1_reg_b_out), .data(ram_1_data),
    .str(ex_mem_1_memwrite_out), .clk(CLK));  // open: sel, ld, clr
  Multiplexer #(.width(32), .enable("false")) multiplexer_7 (
    .in0(multiplexer_8_out), .in1(mem_wb_1_pc_out), .out(multiplexer_7_out), .sel(JAL));
  MEM_WB mem_wb_1 (
    .PC(ex_mem_1_pc_out), .RegWrite(ex_mem_1_regwrite_out), .ALU_Result(ex_mem_1_alu_result_out),
    .MemtoReg(ex_mem_1_memtoreg_out), .MemData(ram_1_data), .W_num(ex_mem_1_w__out), .En(ex_mem_1_en_out),
    .clk(CLK), .rst(RST), .PC_out(mem_wb_1_pc_out), .RegWrite_out(mem_wb_1_regwrite_out),
    .ALU_Result_out(mem_wb_1_alu_result_out), .MemtoReg_out(mem_wb_1_memtoreg_out),
    .MemData_out(mem_wb_1_memdata_out), .W__out(mem_wb_1_w__out), .En_out(mem_wb_1_en_out));
  Multiplexer #(.width(32), .enable("false")) multiplexer_8 (
    .in0(mem_wb_1_alu_result_out), .in1(mem_wb_1_memdata_out), .out(multiplexer_8_out),
    .sel(mem_wb_1_memtoreg_out));

  // Notes on the sheet:
  //   数码管输出应该用寄存器锁存，否则显示数据只能一闪而过
  //   可以通过项目增加Logisim库的方式将前几次实验完成的电路作为子电路引入到本电路中使用
  //   数码管输出
  //   指令存储器
  //   contents of rom_1 (hex, n*v repeats v):
  //   20100000 20110000 20120000 20130000 36100000 36310001 36520002 36730003 ae100000 ae110004 ae120008
  //   ae13000c 2002000a 20110000 20120000 20130000 c
  //   总复位信号应将除ROM以外所有存储组件全部清零
  //   指令字
  //   OP
  //   Func
  //   rs
  //   rt
  //   rd
  //   shamt
  //   Imm
  //   j-addr
  //   Beq
  //   JMP
  //   Bne
  //   JR
  //   OP
  //   JAL
  //   Func
  //   MemToReg
  //   MemWrite
  //   AluOP
  //   AluSrcB
  //   RegWrite
  //   RegDst
  //   Syscall
endmodule

module IF_ID (
  input  [31:0] IR,
  input  [31:0] PC,
  input  En,
  input  clk,
  input  rst,
  output [31:0] IR_out,
  output [31:0] PC_out,
  output En_out
);

  Register #(.width(32)) register_1 (.D(IR), .en(En), .Q(IR_out), .clk(clk), .clr(rst));
  Register #(.width(32)) register_2 (.D(PC), .en(En), .Q(PC_out), .clk(clk), .clr(rst));
  Register #(.width(1)) register_3 (.D(En), .en(1'b1), .Q(En_out), .clk(clk), .clr(rst));
endmodule

module ID_EX (
  input  [4:0] shamt,
  input  [31:0] JPC,
  input  [31:0] PC,
  input  RegWrite,
  input  beq,
  input  [31:0] Reg_A,
  input  MemtoReg,
  input  bne,
  input  [31:0] Reg_B,
  input  [4:0] W_num,
  input  [3:0] ALUop,
  input  MemWrite,
  input  ALUsrcB,
  input  [31:0] Imm,
  input  En,
  input  clk,
  input  rst,
  output [4:0] shamt_out,
  output [31:0] JPC_out,
  output [31:0] PC_out,
  output RegWrite_out,
  output beq_out,
  output [31:0] Reg_A_out,
  output MemtoReg_out,
  output bne_out,
  output [31:0] Reg_B_out,
  output [4:0] W__out,
  output [3:0] ALUop_out,
  output MemWrite_out,
  output ALUsrcB_out,
  output [31:0] Imm_out,
  output En_out
);

  Register #(.width(5)) register_1 (.D(shamt), .en(En), .Q(shamt_out), .clk(clk), .clr(rst));
  Register #(.width(32)) register_2 (.D(PC), .en(En), .Q(PC_out), .clk(clk), .clr(rst));
  Register #(.width(32)) register_3 (.D(Reg_A), .Q(Reg_A_out), .clk(clk), .clr(rst));  // open: en
  Register #(.width(32)) register_4 (.D(Reg_B), .en(En), .Q(Reg_B_out), .clk(clk), .clr(rst));
  Register #(.width(32)) register_5 (.D(Imm), .en(En), .Q(Imm_out), .clk(clk), .clr(rst));
  Register #(.width(1)) register_6 (.D(En), .en(1'b1), .Q(En_out), .clk(clk), .clr(rst));
  Register #(.width(32)) register_7 (.D(JPC), .en(En), .Q(JPC_out), .clk(clk), .clr(rst));
  Register #(.width(1)) register_8 (.D(RegWrite), .en(En), .Q(RegWrite_out), .clk(clk), .clr(rst));
  Register #(.width(1)) register_9 (.D(MemtoReg), .en(En), .Q(MemtoReg_out), .clk(clk), .clr(rst));
  Register #(.width(5)) register_10 (.D(W_num), .en(En), .Q(W__out), .clk(clk), .clr(rst));
  Register #(.width(1)) register_11 (.D(MemWrite), .en(En), .Q(MemWrite_out), .clk(clk), .clr(rst));
  Register #(.width(1)) register_12 (.D(beq), .en(En), .Q(beq_out), .clk(clk), .clr(rst));
  Register #(.width(1)) register_13 (.D(bne), .Q(bne_out), .clk(clk), .clr(rst));  // open: en
  Register #(.width(4)) register_14 (.D(ALUop), .en(En), .Q(ALUop_out), .clk(clk), .clr(rst));
  Register #(.width(1)) register_15 (.D(ALUsrcB), .en(En), .Q(ALUsrcB_out), .clk(clk), .clr(rst));
endmodule

module EX_MEM (
  input  [31:0] PC,
  input  RegWrite,
  input  [31:0] ALU_Result,
  input  MemtoReg,
  input  [31:0] Reg_B,
  input  [4:0] W_num,
  input  MemWrite,
  input  En,
  input  clk,
  input  rst,
  output [31:0] PC_out,
  output RegWrite_out,
  output [31:0] ALU_Result_out,
  output MemtoReg_out,
  output [31:0] Reg_B_out,
  output [4:0] W__out,
  output MemWrite_out,
  output En_out
);

  Register #(.width(32)) register_1 (.D(PC), .en(En), .Q(PC_out), .clk(clk), .clr(rst));
  Register #(.width(32)) register_2 (.D(ALU_Result), .Q(ALU_Result_out), .clk(clk), .clr(rst));  // open: en
  Register #(.width(32)) register_3 (.D(Reg_B), .en(En), .Q(Reg_B_out), .clk(clk), .clr(rst));
  Register #(.width(1)) register_4 (.D(En), .en(1'b1), .Q(En_out), .clk(clk), .clr(rst));
  Register #(.width(1)) register_5 (.D(RegWrite), .en(En), .Q(RegWrite_out), .clk(clk), .clr(rst));
  Register #(.width(1)) register_6 (.D(MemtoReg), .en(En), .Q(MemtoReg_out), .clk(clk), .clr(rst));
  Register #(.width(5)) register_7 (.D(W_num), .en(En), .Q(W__out), .clk(clk), .clr(rst));
  Register #(.width(1)) register_8 (.D(MemWrite), .en(En), .Q(MemWrite_out), .clk(clk), .clr(rst));
endmodule

module MEM_WB (
  input  [31:0] PC,
  input  RegWrite,
  input  [31:0] ALU_Result,
  input  MemtoReg,
  input  [31:0] MemData,
  input  [4:0] W_num,
  input  En,
  input  clk,
  input  rst,
  output [31:0] PC_out,
  output RegWrite_out,
  output [31:0] ALU_Result_out,
  output MemtoReg_out,
  output [31:0] MemData_out,
  output [4:0] W__out,
  output En_out
);

  Register #(.width(32)) register_1 (.D(PC), .en(En), .Q(PC_out), .clk(clk), .clr(rst));
  Register #(.width(32)) register_2 (.D(ALU_Result), .Q(ALU_Result_out), .clk(clk), .clr(rst));  // open: en
  Register #(.width(32)) register_3 (.D(MemData), .en(En), .Q(MemData_out), .clk(clk), .clr(rst));
  Register #(.width(1)) register_4 (.D(En), .en(1'b1), .Q(En_out), .clk(clk), .clr(rst));
  Register #(.width(1)) register_5 (.D(RegWrite), .en(En), .Q(RegWrite_out), .clk(clk), .clr(rst));
  Register #(.width(1)) register_6 (.D(MemtoReg), .en(En), .Q(MemtoReg_out), .clk(clk), .clr(rst));
  Register #(.width(5)) register_7 (.D(W_num), .en(En), .Q(W__out), .clk(clk), .clr(rst));
endmodule
