// Logisim project temp.circ as structural Verilog: 14 circuits, main circuit ◇单周期MIPS
module \单周期MIPS  (
);

  wire and_1_out, and_3_out, and_4_out, CLK, comparator_1_eq, con_if, Go, HALT, JAL, JMP, JR,
       mips_alu_1_equal, or_2_out, RST, SignedExt, Syscall, uncon_if, \硬布线控制器_1_alu_src , \硬布线控制器_1_beq ,
       \硬布线控制器_1_bne , \硬布线控制器_1_memtoreg , \硬布线控制器_1_memwrite , \硬布线控制器_1_regdst , \硬布线控制器_1_regwrite ;
  wire [0:0] or_1_out;
  wire [3:0] \硬布线控制器_1_alu_op ;
  wire [4:0] multiplexer_2_out, multiplexer_3_out, multiplexer_4_out, multiplexer_5_out;
  wire [15:0] \总周期数 , \无条件分支数 , \条件分支成功数 ;
  wire [31:0] b_pc, bit_extender_1_out, bit_extender_2_out, bit_extender_3_out, j_pc, LedData,
       mips_alu_1_result, multiplexer_1_out, multiplexer_6_out, multiplexer_7_out, multiplexer_8_out,
       multiplexer_9_out, next_pc, PC_q, R2, ram_1_data, result2, rom_1_data, RS, shifter_2_out;

  Button \u_总复位  (.out(RST));
  Button u_Go (.out(Go));
  Clock clock_1 (.out(CLK));
  Hex_Digit_Display hex_digit_display_1 (.value(LedData[31:28]));  // open: dp
  Hex_Digit_Display hex_digit_display_2 (.value(LedData[27:24]));  // open: dp
  or or_1 (or_1_out[0], con_if, JR);
  Hex_Digit_Display hex_digit_display_3 (.value(LedData[19:16]));  // open: dp
  Hex_Digit_Display hex_digit_display_4 (.value(LedData[23:20]));  // open: dp
  Multiplexer #(.select(2), .width(32), .enable("false")) multiplexer_1 (
    .in0(next_pc), .in1(b_pc), .in2(j_pc), .in3(RS), .out(multiplexer_1_out), .sel({uncon_if, or_1_out[0]}));
  or or_2 (or_2_out, Go, ~HALT);  // OR_Gate
  Hex_Digit_Display hex_digit_display_5 (.value(LedData[15:12]));  // open: dp
  Hex_Digit_Display hex_digit_display_6 (.value(LedData[11:8]));  // open: dp
  Hex_Digit_Display hex_digit_display_7 (.value(LedData[7:4]));  // open: dp
  Hex_Digit_Display hex_digit_display_8 (.value(LedData[3:0]));  // open: dp
  Counter #(.width(16), .max('hffff)) counter_1 (
    .count(con_if), .Q(\条件分支成功数 ), .clk(CLK), .clr(RST));  // open: load, D, carry
  Counter #(.width(16), .max('hffff)) counter_2 (
    .count(uncon_if), .Q(\无条件分支数 ), .clk(CLK), .clr(RST));  // open: load, D, carry
  Counter #(.width(16), .max('hffff)) counter_3 (
    .count(or_2_out), .Q(\总周期数 ), .clk(CLK), .clr(RST));  // open: load, D, carry
  Register #(.width(32)) PC (.D(multiplexer_1_out), .en(or_2_out), .Q(PC_q), .clk(CLK), .clr(RST));
  Adder #(.width(32)) adder_1 (.a(PC_q), .b(32'h4), .out(next_pc));  // open: cin, cout
  ROM #(.addrWidth(10), .dataWidth(32)) rom_1 (.addr(PC_q[11:2]), .data(rom_1_data));  // open: sel
  // Probe on \总周期数 
  // Probe on \无条件分支数 
  // Probe on \条件分支成功数 
  or or_3 (uncon_if, JAL, JMP, JR);
  \硬布线控制器  \u_硬布线控制器_1  (
    .Func(rom_1_data[5:0]), .OP(rom_1_data[31:26]), .ALU_OP(\硬布线控制器_1_alu_op ),
    .MemToReg(\硬布线控制器_1_memtoreg ), .MemWrite(\硬布线控制器_1_memwrite ), .ALU_SRC(\硬布线控制器_1_alu_src ),
    .RegWrite(\硬布线控制器_1_regwrite ), .SysCALL(Syscall), .SignedExt(SignedExt), .RegDst(\硬布线控制器_1_regdst ),
    .JR(JR), .JMP(JMP), .Beq(\硬布线控制器_1_beq ), .JAL(JAL), .Bne(\硬布线控制器_1_bne ));  // open: R1_Used, R2_Used, BLEZ, SRLV, LBU
  Multiplexer #(.width(5), .enable("false")) multiplexer_2 (
    .in0(rom_1_data[25:21]), .in1(5'b00010), .out(multiplexer_2_out), .sel(Syscall));
  Multiplexer #(.width(5), .enable("false")) multiplexer_3 (
    .in0(rom_1_data[20:16]), .in1(5'b00100), .out(multiplexer_3_out), .sel(Syscall));
  Multiplexer #(.width(5), .enable("false")) multiplexer_4 (
    .in0(rom_1_data[20:16]), .in1(rom_1_data[15:11]), .out(multiplexer_4_out), .sel(\硬布线控制器_1_regdst ));
  assign bit_extender_1_out = {{16{1'b0}}, rom_1_data[15:0]};  // Bit_Extender bit_extender_1
  assign bit_extender_2_out = {{16{rom_1_data[15]}}, rom_1_data[15:0]};  // Bit_Extender bit_extender_2
  assign bit_extender_3_out = {{6{1'b0}}, rom_1_data[25:0]};  // Bit_Extender bit_extender_3
  Comparator #(.width(32)) comparator_1 (.a(RS), .b(32'h22), .eq(comparator_1_eq));  // open: gt, lt
  Multiplexer #(.width(5), .enable("false")) multiplexer_5 (
    .in0(multiplexer_4_out), .in1({5{1'b1}}), .out(multiplexer_5_out), .sel(JAL));
  Multiplexer #(.width(32), .enable("false")) multiplexer_6 (
    .in0(bit_extender_1_out), .in1(bit_extender_2_out), .out(multiplexer_6_out), .sel(SignedExt));
  Shifter #(.width(32)) shifter_1 (.in(bit_extender_3_out), .\dist (5'b00010), .out(j_pc));
  and and_1 (and_1_out, Syscall, comparator_1_eq);
  and and_2 (HALT, ~comparator_1_eq, Syscall);  // AND_Gate
  Register #(.width(32)) Led (.D(R2), .en(and_1_out), .Q(LedData), .clk(CLK), .clr(RST));
  MIPS_Regifile mips_regifile_1 (
    .Din(multiplexer_8_out), .Clk(CLK), .R1(RS), .R2(R2), .WE(\硬布线控制器_1_regwrite ),
    .W_num(multiplexer_5_out), .R1_num(multiplexer_2_out), .R2_num(multiplexer_3_out));
  Shifter #(.width(32)) shifter_2 (.in(multiplexer_6_out), .\dist (5'b00010), .out(shifter_2_out));
  Multiplexer #(.width(32), .enable("false")) multiplexer_7 (
    .in0(R2), .in1(multiplexer_6_out), .out(multiplexer_7_out), .sel(\硬布线控制器_1_alu_src ));
  Adder #(.width(32)) adder_2 (.a(shifter_2_out), .b(next_pc), .out(b_pc));  // open: cin, cout
  MIPS_ALU mips_alu_1 (
    .X(RS), .Y(multiplexer_7_out), .AluOP(\硬布线控制器_1_alu_op ), .Equal(mips_alu_1_equal),
    .Result(mips_alu_1_result), .Result_2(result2), .shamt(rom_1_data[10:6]));
  and and_3 (and_3_out, mips_alu_1_equal, \硬布线控制器_1_beq );
  and and_4 (and_4_out, \硬布线控制器_1_bne , ~mips_alu_1_equal);  // AND_Gate
  or or_4 (con_if, and_3_out, and_4_out);
  Multiplexer #(.width(32), .enable("false")) multiplexer_8 (
    .in0(multiplexer_9_out), .in1(next_pc), .out(multiplexer_8_out), .sel(JAL));
  RAM #(.addrWidth(10), .dataWidth(32), .bus("separate")) ram_1 (
    .addr(mips_alu_1_result[11:2]), .din(R2), .data(ram_1_data), .str(\硬布线控制器_1_memwrite ), .clk(CLK));  // open: sel, ld, clr
  Multiplexer #(.width(32), .enable("false")) multiplexer_9 (
    .in0(mips_alu_1_result), .in1(ram_1_data), .out(multiplexer_9_out), .sel(\硬布线控制器_1_memtoreg ));

  // Notes on the sheet:
  //   数码管输出应该用寄存器锁存，否则显示数据只能一闪而过
  //   可以通过项目增加Logisim库的方式将前几次实验完成的电路作为子电路引入到本电路中使用
  //   数码管输出
  //   指令存储器
  //   contents of rom_1 (hex, n*v repeats v):
  //   20110020 20020022 8000c06 20110004 20120005 20130006 10000003 20110007 20120008 20130009 14110003
  //   2011000a 2012000b 2013000c c000c14 2002000a 0 0 0 c 2231ffff 0 0 0 112020 0 0 0 c 1620fff6 3e00008
  //   总复位信号应将除ROM以外所有存储组件全部清零
  //   指令字
  //   OP
  //   Func
  //   rs
  //   rt
  //   rd
  //   shamt
  //   Imm
  //   j-addr
  //   JMP
  //   JR
  //   OP
  //   Func
  //   Beq
  //   MemWrite
  //   AluOP
  //   AluSrcB
  //   RegWrite
  //   JAL
  //   RegDst
  //   Syscall
endmodule

// 单周期硬布线控制器
module \硬布线控制器  (
  input  [5:0] OP,
  input  [5:0] Func,
  output [3:0] ALU_OP,
  output MemWrite,
  output JAL,
  output JMP,
  output ALU_SRC,
  output RegWrite,
  output SysCALL,
  output MemToReg,
  output SignedExt,
  output RegDst,
  output Beq,
  output Bne,
  output JR,
  output R1_Used,
  output R2_Used,
  output SRLV,
  output LBU,
  output BLEZ
);

  \运算控制器  \u_运算控制器_1  (
    .OP0(OP[0]), .OP1(OP[1]), .OP2(OP[2]), .OP3(OP[3]), .OP4(OP[4]), .OP5(OP[5]), .F0(Func[0]), .F1(Func[1]),
    .F2(Func[2]), .F3(Func[3]), .F4(Func[4]), .F5(Func[5]), .S0(ALU_OP[0]), .S1(ALU_OP[1]), .S2(ALU_OP[2]),
    .S3(ALU_OP[3]));
  \控制信号生成  \u_控制信号生成_1  (
    .OP0(OP[0]), .MemWrite(MemWrite), .OP1(OP[1]), .OP2(OP[2]), .OP3(OP[3]), .JAL(JAL), .OP4(OP[4]),
    .OP5(OP[5]), .JMP(JMP), .F0(Func[0]), .F1(Func[1]), .F2(Func[2]), .F3(Func[3]), .F4(Func[4]),
    .F5(Func[5]), .ALU_SRC(ALU_SRC), .RegWrite(RegWrite), .SysCALL(SysCALL), .MemtoReg(MemToReg),
    .SignedExt(SignedExt), .RegDst(RegDst), .BEQ(Beq), .BNE(Bne), .JR(JR));
  \源寄存器使用情况检测  \u_源寄存器使用情况检测_1  (
    .OP0(OP[0]), .OP1(OP[1]), .OP2(OP[2]), .OP3(OP[3]), .OP4(OP[4]), .OP5(OP[5]), .F0(Func[0]), .F1(Func[1]),
    .F2(Func[2]), .F3(Func[3]), .F4(Func[4]), .F5(Func[5]), .R1_used(R1_Used), .R2_used(R2_Used));
  \CCMB控制信号生成  \ccmb控制信号生成_1  (
    .OP0(OP[0]), .OP1(OP[1]), .OP2(OP[2]), .OP3(OP[3]), .OP4(OP[4]), .OP5(OP[5]), .F0(Func[0]), .F1(Func[1]),
    .F2(Func[2]), .F3(Func[3]), .F4(Func[4]), .F5(Func[5]), .SRLV(SRLV), .LBU(LBU), .BLEZ(BLEZ));

  // Other names for the same wires on the sheet: OP_CODE[5:0] = OP

  // Notes on the sheet:
  //   运算器控制器，根据指令生成运算器功能选择信号
  //   控制信号生成，产生数据通路需要的其他控制信号
endmodule

// 运算器控制器
module \运算控制器  (
  input  OP0,
  input  OP1,
  input  OP2,
  input  OP3,
  input  OP4,
  input  OP5,
  input  F0,
  input  F1,
  input  F2,
  input  F3,
  input  F4,
  input  F5,
  output S0,
  output S1,
  output S2,
  output S3
);

  wire and_1_out, and_2_out, and_3_out, and_4_out, and_5_out, and_6_out, and_7_out, and_8_out, and_9_out,
       and_10_out, and_11_out, and_12_out, and_13_out, and_14_out, and_15_out, and_16_out, and_17_out,
       and_18_out, and_19_out, and_20_out, and_21_out, and_22_out, and_23_out, and_24_out, and_25_out,
       and_26_out, and_27_out, and_28_out, and_29_out, and_30_out, and_31_out, and_32_out, and_33_out,
       and_34_out, and_35_out, and_36_out, and_37_out, and_38_out, and_39_out, and_40_out, and_41_out,
       and_42_out, and_43_out, and_44_out, and_45_out, and_46_out, and_47_out, and_48_out, and_49_out,
       and_50_out, and_51_out, and_52_out, and_53_out, and_54_out, and_55_out, and_56_out, and_57_out,
       and_58_out, and_59_out, and_60_out, and_61_out, and_62_out, not_1_out, not_2_out, not_3_out,
       not_4_out, not_5_out, not_6_out, not_7_out, not_8_out, not_9_out, not_10_out, not_11_out, not_12_out,
       not_13_out, not_14_out, not_15_out, not_16_out, not_17_out, not_18_out, not_19_out, not_20_out,
       not_21_out, not_22_out, not_23_out, not_24_out, not_25_out, not_26_out, not_27_out, not_28_out,
       not_29_out, not_30_out, not_31_out, not_32_out, not_33_out, not_34_out, not_35_out, not_36_out,
       not_37_out, not_38_out, not_39_out, not_40_out, not_41_out, not_42_out, not_43_out, not_44_out,
       not_45_out, not_46_out, not_47_out, not_48_out, not_49_out, not_50_out, not_51_out, not_52_out,
       not_53_out, not_54_out, not_55_out, not_56_out, not_57_out, not_58_out, not_59_out, not_60_out,
       not_61_out, not_62_out, not_63_out, not_64_out, not_65_out, not_66_out, not_67_out, not_68_out,
       not_69_out, not_70_out, not_71_out, not_72_out, not_73_out, not_74_out, not_75_out, not_76_out,
       not_77_out, not_78_out, not_79_out, not_80_out, not_81_out, not_82_out, not_83_out, not_84_out,
       not_85_out, not_86_out, not_87_out, not_88_out, not_89_out, not_90_out, not_91_out, not_92_out,
       not_93_out, not_94_out, not_95_out, not_96_out, not_97_out, not_98_out, not_99_out, not_100_out,
       not_101_out, not_102_out, not_103_out, not_104_out, not_105_out, not_106_out, not_107_out,
       not_108_out, not_109_out, not_110_out, not_111_out, not_112_out, not_113_out, not_114_out,
       not_115_out, not_116_out, not_117_out, not_118_out, not_119_out, not_120_out, not_121_out,
       not_122_out, not_123_out, not_124_out, not_125_out, not_126_out, not_127_out, not_128_out,
       not_129_out, not_130_out, not_131_out, not_132_out, not_133_out, not_134_out, not_135_out,
       not_136_out, not_137_out, not_138_out, not_139_out, not_140_out, not_141_out, not_142_out,
       not_143_out, not_144_out, not_145_out, not_146_out, not_147_out, not_148_out, not_149_out,
       not_150_out, not_151_out, not_152_out, not_153_out, not_154_out, not_155_out, not_156_out,
       not_157_out, not_158_out, not_159_out, not_160_out, not_161_out, not_162_out, not_163_out,
       not_164_out, not_165_out, not_166_out, not_167_out, not_168_out, not_169_out, not_170_out,
       not_171_out, not_172_out, not_173_out, not_174_out, not_175_out, not_176_out, not_177_out,
       not_178_out, not_179_out, not_180_out, not_181_out, not_182_out, not_183_out, not_184_out,
       not_185_out, not_186_out, not_187_out, not_188_out, not_189_out, not_190_out, not_191_out,
       not_192_out, not_193_out, not_194_out, not_195_out, not_196_out, not_197_out, not_198_out,
       not_199_out, not_200_out, not_201_out, not_202_out, not_203_out, not_204_out, not_205_out,
       not_206_out, not_207_out, not_208_out, not_209_out, not_210_out, not_211_out, not_212_out,
       not_213_out, not_214_out, not_215_out, not_216_out, not_217_out, not_218_out, not_219_out,
       not_220_out, not_221_out, not_222_out, not_223_out, not_224_out, not_225_out, not_226_out,
       not_227_out, not_228_out, not_229_out, not_230_out, not_231_out, not_232_out, not_233_out,
       not_234_out, not_235_out, not_236_out, not_237_out, not_238_out, not_239_out, not_240_out,
       not_241_out, not_242_out, not_243_out, not_244_out, not_245_out, not_246_out, not_247_out,
       not_248_out, not_249_out, not_250_out, not_251_out, not_252_out, not_253_out, not_254_out,
       not_255_out, not_256_out, not_257_out, not_258_out, not_259_out, not_260_out, not_261_out,
       not_262_out, not_263_out, not_264_out, not_265_out, not_266_out, not_267_out, not_268_out,
       not_269_out, not_270_out, not_271_out, not_272_out, not_273_out, not_274_out, not_275_out,
       not_276_out, not_277_out, not_278_out, not_279_out, not_280_out, not_281_out, not_282_out,
       not_283_out, not_284_out, not_285_out, not_286_out, not_287_out, not_288_out, not_289_out,
       not_290_out, not_291_out, not_292_out, not_293_out, not_294_out, not_295_out, not_296_out,
       not_297_out, not_298_out, not_299_out, not_300_out, not_301_out, not_302_out, not_303_out,
       not_304_out, not_305_out, not_306_out, not_307_out, not_308_out, not_309_out, not_310_out,
       not_311_out, not_312_out, not_313_out, not_314_out, not_315_out, not_316_out, not_317_out,
       not_318_out, not_319_out, not_320_out, not_321_out, not_322_out, not_323_out, not_324_out,
       not_325_out, not_326_out, not_327_out, not_328_out, not_329_out, not_330_out, not_331_out,
       not_332_out, not_333_out, not_334_out, not_335_out, not_336_out, not_337_out, not_338_out,
       not_339_out, not_340_out, not_341_out, not_342_out, not_343_out, not_344_out, not_345_out,
       not_346_out, not_347_out, not_348_out, not_349_out, not_350_out, not_351_out, not_352_out,
       not_353_out, not_354_out, not_355_out, not_356_out, not_357_out, not_358_out, not_359_out,
       not_360_out, not_361_out, not_362_out, not_363_out, not_364_out, not_365_out, not_366_out,
       not_367_out, not_368_out, not_369_out, not_370_out, not_371_out, not_372_out, not_373_out,
       not_374_out, not_375_out, not_376_out, not_377_out, not_378_out, not_379_out, not_380_out,
       not_381_out, not_382_out, not_383_out, not_384_out, not_385_out, not_386_out, not_387_out,
       not_388_out, not_389_out, not_390_out, not_391_out, not_392_out, not_393_out, not_394_out,
       not_395_out, not_396_out, not_397_out, not_398_out, not_399_out, not_400_out, not_401_out,
       not_402_out, not_403_out, not_404_out, not_405_out, not_406_out, not_407_out, not_408_out,
       not_409_out, not_410_out, not_411_out, not_412_out, not_413_out, not_414_out, not_415_out,
       not_416_out, not_417_out, not_418_out, not_419_out, not_420_out, not_421_out, not_422_out,
       not_423_out, not_424_out, not_425_out, not_426_out;

  not not_1 (not_1_out, OP5);
  not not_2 (not_2_out, OP4);
  not not_3 (not_3_out, OP3);
  not not_4 (not_4_out, OP2);
  not not_5 (not_5_out, OP1);
  not not_6 (not_6_out, OP0);
  not not_7 (not_7_out, F5);
  not not_8 (not_8_out, F4);
  not not_9 (not_9_out, F3);
  not not_10 (not_10_out, F2);
  not not_11 (not_11_out, OP5);
  not not_12 (not_12_out, OP4);
  not not_13 (not_13_out, OP3);
  not not_14 (not_14_out, OP2);
  not not_15 (not_15_out, OP1);
  not not_16 (not_16_out, OP0);
  not not_17 (not_17_out, F4);
  not not_18 (not_18_out, F3);
  not not_19 (not_19_out, F2);
  not not_20 (not_20_out, F1);
  not not_21 (not_21_out, F0);
  not not_22 (not_22_out, OP5);
  not not_23 (not_23_out, OP4);
  not not_24 (not_24_out, OP3);
  not not_25 (not_25_out, OP2);
  not not_26 (not_26_out, OP1);
  not not_27 (not_27_out, OP0);
  not not_28 (not_28_out, F4);
  not not_29 (not_29_out, F3);
  not not_30 (not_30_out, F2);
  not not_31 (not_31_out, F1);
  not not_32 (not_32_out, OP5);
  not not_33 (not_33_out, OP4);
  not not_34 (not_34_out, OP3);
  not not_35 (not_35_out, OP2);
  not not_36 (not_36_out, OP1);
  not not_37 (not_37_out, OP0);
  not not_38 (not_38_out, F4);
  not not_39 (not_39_out, F3);
  not not_40 (not_40_out, F1);
  not not_41 (not_41_out, F0);
  not not_42 (not_42_out, OP5);
  not not_43 (not_43_out, OP4);
  not not_44 (not_44_out, OP3);
  not not_45 (not_45_out, OP2);
  not not_46 (not_46_out, OP1);
  not not_47 (not_47_out, OP0);
  not not_48 (not_48_out, F4);
  not not_49 (not_49_out, F2);
  not not_50 (not_50_out, F0);
  not not_51 (not_51_out, OP5);
  not not_52 (not_52_out, OP4);
  not not_53 (not_53_out, OP2);
  not not_54 (not_54_out, OP1);
  not not_55 (not_55_out, OP0);
  not not_56 (not_56_out, OP5);
  not not_57 (not_57_out, OP4);
  not not_58 (not_58_out, OP1);
  not not_59 (not_59_out, OP0);
  not not_60 (not_60_out, OP5);
  not not_61 (not_61_out, OP4);
  not not_62 (not_62_out, OP2);
  not not_63 (not_63_out, OP1);
  not not_64 (not_64_out, OP5);
  not not_65 (not_65_out, OP4);
  not not_66 (not_66_out, OP2);
  not not_67 (not_67_out, OP0);
  not not_68 (not_68_out, OP4);
  not not_69 (not_69_out, OP3);
  not not_70 (not_70_out, OP2);
  not not_71 (not_71_out, OP4);
  not not_72 (not_72_out, OP2);
  not not_73 (not_73_out, OP5);
  not not_74 (not_74_out, OP4);
  not not_75 (not_75_out, OP3);
  not not_76 (not_76_out, OP2);
  not not_77 (not_77_out, OP1);
  not not_78 (not_78_out, OP0);
  not not_79 (not_79_out, F4);
  not not_80 (not_80_out, F3);
  not not_81 (not_81_out, F0);
  not not_82 (not_82_out, OP4);
  not not_83 (not_83_out, OP3);
  not not_84 (not_84_out, OP1);
  not not_85 (not_85_out, OP0);
  not not_86 (not_86_out, OP5);
  not not_87 (not_87_out, OP4);
  not not_88 (not_88_out, OP3);
  not not_89 (not_89_out, OP0);
  not not_90 (not_90_out, OP5);
  not not_91 (not_91_out, OP4);
  not not_92 (not_92_out, OP3);
  not not_93 (not_93_out, OP2);
  not not_94 (not_94_out, OP1);
  not not_95 (not_95_out, OP0);
  not not_96 (not_96_out, F5);
  not not_97 (not_97_out, F4);
  not not_98 (not_98_out, F3);
  not not_99 (not_99_out, F2);
  not not_100 (not_100_out, F0);
  not not_101 (not_101_out, OP5);
  not not_102 (not_102_out, OP4);
  not not_103 (not_103_out, OP3);
  not not_104 (not_104_out, OP2);
  not not_105 (not_105_out, OP1);
  not not_106 (not_106_out, OP0);
  not not_107 (not_107_out, F4);
  not not_108 (not_108_out, F3);
  not not_109 (not_109_out, F2);
  not not_110 (not_110_out, F0);
  not not_111 (not_111_out, OP5);
  not not_112 (not_112_out, OP4);
  not not_113 (not_113_out, OP3);
  not not_114 (not_114_out, OP2);
  not not_115 (not_115_out, OP1);
  not not_116 (not_116_out, OP0);
  not not_117 (not_117_out, F4);
  not not_118 (not_118_out, F3);
  not not_119 (not_119_out, F1);
  not not_120 (not_120_out, F0);
  not not_121 (not_121_out, OP5);
  not not_122 (not_122_out, OP4);
  not not_123 (not_123_out, OP3);
  not not_124 (not_124_out, OP2);
  not not_125 (not_125_out, OP1);
  not not_126 (not_126_out, OP0);
  not not_127 (not_127_out, F4);
  not not_128 (not_128_out, F3);
  not not_129 (not_129_out, OP5);
  not not_130 (not_130_out, OP4);
  not not_131 (not_131_out, OP3);
  not not_132 (not_132_out, OP2);
  not not_133 (not_133_out, OP1);
  not not_134 (not_134_out, OP0);
  not not_135 (not_135_out, F4);
  not not_136 (not_136_out, F2);
  not not_137 (not_137_out, F0);
  not not_138 (not_138_out, OP5);
  not not_139 (not_139_out, OP4);
  not not_140 (not_140_out, OP1);
  not not_141 (not_141_out, OP0);
  not not_142 (not_142_out, OP5);
  not not_143 (not_143_out, OP4);
  not not_144 (not_144_out, OP2);
  not not_145 (not_145_out, OP0);
  not not_146 (not_146_out, OP5);
  not not_147 (not_147_out, OP4);
  not not_148 (not_148_out, OP3);
  not not_149 (not_149_out, OP2);
  not not_150 (not_150_out, OP1);
  not not_151 (not_151_out, OP0);
  not not_152 (not_152_out, F5);
  not not_153 (not_153_out, F4);
  not not_154 (not_154_out, F3);
  not not_155 (not_155_out, F0);
  not not_156 (not_156_out, OP5);
  not not_157 (not_157_out, OP4);
  not not_158 (not_158_out, OP3);
  not not_159 (not_159_out, OP0);
  not not_160 (not_160_out, OP5);
  not not_161 (not_161_out, OP4);
  not not_162 (not_162_out, OP3);
  not not_163 (not_163_out, OP2);
  not not_164 (not_164_out, OP1);
  not not_165 (not_165_out, OP0);
  not not_166 (not_166_out, F4);
  not not_167 (not_167_out, F3);
  not not_168 (not_168_out, F2);
  not not_169 (not_169_out, F1);
  not not_170 (not_170_out, F0);
  not not_171 (not_171_out, OP5);
  not not_172 (not_172_out, OP4);
  not not_173 (not_173_out, OP3);
  not not_174 (not_174_out, OP2);
  not not_175 (not_175_out, OP1);
  not not_176 (not_176_out, OP0);
  not not_177 (not_177_out, F4);
  not not_178 (not_178_out, F3);
  not not_179 (not_179_out, F2);
  not not_180 (not_180_out, F1);
  not not_181 (not_181_out, OP5);
  not not_182 (not_182_out, OP4);
  not not_183 (not_183_out, OP3);
  not not_184 (not_184_out, OP2);
  not not_185 (not_185_out, OP1);
  not not_186 (not_186_out, OP0);
  not not_187 (not_187_out, F4);
  not not_188 (not_188_out, F3);
  not not_189 (not_189_out, F2);
  not not_190 (not_190_out, F0);
  not not_191 (not_191_out, OP5);
  not not_192 (not_192_out, OP4);
  not not_193 (not_193_out, OP3);
  not not_194 (not_194_out, OP2);
  not not_195 (not_195_out, OP1);
  not not_196 (not_196_out, OP0);
  not not_197 (not_197_out, F4);
  not not_198 (not_198_out, F3);
  not not_199 (not_199_out, F1);
  not not_200 (not_200_out, F0);
  not not_201 (not_201_out, OP5);
  not not_202 (not_202_out, OP4);
  not not_203 (not_203_out, OP3);
  not not_204 (not_204_out, OP2);
  not not_205 (not_205_out, OP1);
  not not_206 (not_206_out, OP0);
  not not_207 (not_207_out, F4);
  not not_208 (not_208_out, F2);
  not not_209 (not_209_out, OP5);
  not not_210 (not_210_out, OP4);
  not not_211 (not_211_out, OP2);
  not not_212 (not_212_out, OP1);
  not not_213 (not_213_out, OP0);
  not not_214 (not_214_out, OP5);
  not not_215 (not_215_out, OP4);
  not not_216 (not_216_out, OP1);
  not not_217 (not_217_out, OP0);
  not not_218 (not_218_out, OP5);
  not not_219 (not_219_out, OP4);
  not not_220 (not_220_out, OP2);
  not not_221 (not_221_out, OP1);
  not not_222 (not_222_out, OP4);
  not not_223 (not_223_out, OP3);
  not not_224 (not_224_out, OP2);
  not not_225 (not_225_out, OP4);
  not not_226 (not_226_out, OP2);
  not not_227 (not_227_out, OP4);
  not not_228 (not_228_out, OP3);
  not not_229 (not_229_out, OP1);
  not not_230 (not_230_out, OP0);
  not not_231 (not_231_out, OP5);
  not not_232 (not_232_out, OP4);
  not not_233 (not_233_out, OP3);
  not not_234 (not_234_out, OP2);
  not not_235 (not_235_out, OP1);
  not not_236 (not_236_out, OP0);
  not not_237 (not_237_out, F4);
  not not_238 (not_238_out, F3);
  not not_239 (not_239_out, F2);
  not not_240 (not_240_out, F1);
  not not_241 (not_241_out, F0);
  not not_242 (not_242_out, OP5);
  not not_243 (not_243_out, OP4);
  not not_244 (not_244_out, OP3);
  not not_245 (not_245_out, OP2);
  not not_246 (not_246_out, OP1);
  not not_247 (not_247_out, OP0);
  not not_248 (not_248_out, F4);
  not not_249 (not_249_out, F3);
  not not_250 (not_250_out, F2);
  not not_251 (not_251_out, F1);
  not not_252 (not_252_out, OP5);
  not not_253 (not_253_out, OP4);
  not not_254 (not_254_out, OP3);
  not not_255 (not_255_out, OP2);
  not not_256 (not_256_out, OP1);
  not not_257 (not_257_out, OP0);
  not not_258 (not_258_out, F4);
  not not_259 (not_259_out, F3);
  not not_260 (not_260_out, F2);
  not not_261 (not_261_out, F0);
  not not_262 (not_262_out, OP5);
  not not_263 (not_263_out, OP4);
  not not_264 (not_264_out, OP3);
  not not_265 (not_265_out, OP2);
  not not_266 (not_266_out, OP1);
  not not_267 (not_267_out, OP0);
  not not_268 (not_268_out, F4);
  not not_269 (not_269_out, F3);
  not not_270 (not_270_out, F1);
  not not_271 (not_271_out, F0);
  not not_272 (not_272_out, OP5);
  not not_273 (not_273_out, OP4);
  not not_274 (not_274_out, OP3);
  not not_275 (not_275_out, OP2);
  not not_276 (not_276_out, OP1);
  not not_277 (not_277_out, OP0);
  not not_278 (not_278_out, F4);
  not not_279 (not_279_out, F2);
  not not_280 (not_280_out, OP5);
  not not_281 (not_281_out, OP4);
  not not_282 (not_282_out, OP2);
  not not_283 (not_283_out, OP1);
  not not_284 (not_284_out, OP0);
  not not_285 (not_285_out, OP5);
  not not_286 (not_286_out, OP4);
  not not_287 (not_287_out, OP1);
  not not_288 (not_288_out, OP0);
  not not_289 (not_289_out, OP5);
  not not_290 (not_290_out, OP4);
  not not_291 (not_291_out, OP2);
  not not_292 (not_292_out, OP1);
  not not_293 (not_293_out, OP4);
  not not_294 (not_294_out, OP3);
  not not_295 (not_295_out, OP2);
  not not_296 (not_296_out, OP4);
  not not_297 (not_297_out, OP2);
  not not_298 (not_298_out, OP4);
  not not_299 (not_299_out, OP3);
  not not_300 (not_300_out, OP1);
  not not_301 (not_301_out, OP0);
  not not_302 (not_302_out, OP5);
  not not_303 (not_303_out, OP4);
  not not_304 (not_304_out, OP3);
  not not_305 (not_305_out, OP2);
  not not_306 (not_306_out, OP1);
  not not_307 (not_307_out, OP0);
  not not_308 (not_308_out, F4);
  not not_309 (not_309_out, F3);
  not not_310 (not_310_out, F2);
  not not_311 (not_311_out, F1);
  not not_312 (not_312_out, F0);
  not not_313 (not_313_out, OP5);
  not not_314 (not_314_out, OP4);
  not not_315 (not_315_out, OP3);
  not not_316 (not_316_out, OP2);
  not not_317 (not_317_out, OP1);
  not not_318 (not_318_out, OP0);
  not not_319 (not_319_out, F4);
  not not_320 (not_320_out, F3);
  not not_321 (not_321_out, F2);
  not not_322 (not_322_out, F1);
  not not_323 (not_323_out, OP5);
  not not_324 (not_324_out, OP4);
  not not_325 (not_325_out, OP3);
  not not_326 (not_326_out, OP2);
  not not_327 (not_327_out, OP1);
  not not_328 (not_328_out, OP0);
  not not_329 (not_329_out, F4);
  not not_330 (not_330_out, F3);
  not not_331 (not_331_out, F2);
  not not_332 (not_332_out, F0);
  not not_333 (not_333_out, OP5);
  not not_334 (not_334_out, OP4);
  not not_335 (not_335_out, OP3);
  not not_336 (not_336_out, OP2);
  not not_337 (not_337_out, OP1);
  not not_338 (not_338_out, OP0);
  not not_339 (not_339_out, F4);
  not not_340 (not_340_out, F3);
  not not_341 (not_341_out, F1);
  not not_342 (not_342_out, F0);
  not not_343 (not_343_out, OP5);
  not not_344 (not_344_out, OP4);
  not not_345 (not_345_out, OP3);
  not not_346 (not_346_out, OP2);
  not not_347 (not_347_out, OP1);
  not not_348 (not_348_out, OP0);
  not not_349 (not_349_out, F4);
  not not_350 (not_350_out, F2);
  not not_351 (not_351_out, OP5);
  not not_352 (not_352_out, OP4);
  not not_353 (not_353_out, OP2);
  not not_354 (not_354_out, OP1);
  not not_355 (not_355_out, OP0);
  not not_356 (not_356_out, OP5);
  not not_357 (not_357_out, OP4);
  not not_358 (not_358_out, OP1);
  not not_359 (not_359_out, OP0);
  not not_360 (not_360_out, OP5);
  not not_361 (not_361_out, OP4);
  not not_362 (not_362_out, OP2);
  not not_363 (not_363_out, OP1);
  not not_364 (not_364_out, OP4);
  not not_365 (not_365_out, OP3);
  not not_366 (not_366_out, OP2);
  not not_367 (not_367_out, OP4);
  not not_368 (not_368_out, OP2);
  not not_369 (not_369_out, OP4);
  not not_370 (not_370_out, OP3);
  not not_371 (not_371_out, OP1);
  not not_372 (not_372_out, OP0);
  not not_373 (not_373_out, OP5);
  not not_374 (not_374_out, OP4);
  not not_375 (not_375_out, OP3);
  not not_376 (not_376_out, OP2);
  not not_377 (not_377_out, OP1);
  not not_378 (not_378_out, OP0);
  not not_379 (not_379_out, F4);
  not not_380 (not_380_out, F3);
  not not_381 (not_381_out, F1);
  not not_382 (not_382_out, OP5);
  not not_383 (not_383_out, OP4);
  not not_384 (not_384_out, OP3);
  not not_385 (not_385_out, OP2);
  not not_386 (not_386_out, OP1);
  not not_387 (not_387_out, OP0);
  not not_388 (not_388_out, F4);
  not not_389 (not_389_out, F3);
  not not_390 (not_390_out, OP5);
  not not_391 (not_391_out, OP4);
  not not_392 (not_392_out, OP3);
  not not_393 (not_393_out, OP2);
  not not_394 (not_394_out, OP1);
  not not_395 (not_395_out, OP0);
  not not_396 (not_396_out, F4);
  not not_397 (not_397_out, F2);
  not not_398 (not_398_out, F0);
  not not_399 (not_399_out, OP5);
  not not_400 (not_400_out, OP4);
  not not_401 (not_401_out, OP3);
  not not_402 (not_402_out, OP2);
  not not_403 (not_403_out, OP1);
  not not_404 (not_404_out, OP0);
  not not_405 (not_405_out, F4);
  not not_406 (not_406_out, F2);
  not not_407 (not_407_out, OP5);
  not not_408 (not_408_out, OP4);
  not not_409 (not_409_out, OP2);
  not not_410 (not_410_out, OP0);
  not not_411 (not_411_out, OP5);
  not not_412 (not_412_out, OP4);
  not not_413 (not_413_out, OP1);
  not not_414 (not_414_out, OP5);
  not not_415 (not_415_out, OP4);
  not not_416 (not_416_out, OP3);
  not not_417 (not_417_out, OP2);
  not not_418 (not_418_out, OP1);
  not not_419 (not_419_out, OP0);
  not not_420 (not_420_out, F4);
  not not_421 (not_421_out, F3);
  not not_422 (not_422_out, F0);
  not not_423 (not_423_out, OP5);
  not not_424 (not_424_out, OP4);
  not not_425 (not_425_out, OP3);
  not not_426 (not_426_out, OP0);
  and and_1 (and_1_out, not_1_out, not_2_out, not_3_out, not_4_out, not_5_out, not_6_out, not_7_out, not_8_out, not_9_out, not_10_out, F1, F0);
  and and_2 (and_2_out, not_11_out, not_12_out, not_13_out, not_14_out, not_15_out, not_16_out, F5, not_17_out, not_18_out, not_19_out, not_20_out, not_21_out);
  and and_3 (and_3_out, not_22_out, not_23_out, not_24_out, not_25_out, not_26_out, not_27_out, F5, not_28_out, not_29_out, not_30_out, not_31_out, F0);
  and and_4 (and_4_out, not_32_out, not_33_out, not_34_out, not_35_out, not_36_out, not_37_out, F5, not_38_out, not_39_out, F2, not_40_out, not_41_out);
  and and_5 (and_5_out, not_42_out, not_43_out, not_44_out, not_45_out, not_46_out, not_47_out, F5, not_48_out, F3, not_49_out, F1, not_50_out);
  and and_6 (and_6_out, not_51_out, not_52_out, OP3, not_53_out, not_54_out, not_55_out);
  and and_7 (and_7_out, not_56_out, not_57_out, OP3, OP2, not_58_out, not_59_out);
  and and_8 (and_8_out, not_60_out, not_61_out, OP3, not_62_out, not_63_out, OP0);
  and and_9 (and_9_out, not_64_out, not_65_out, OP3, not_66_out, OP1, not_67_out);
  and and_10 (and_10_out, OP5, not_68_out, not_69_out, not_70_out, OP1, OP0);
  and and_11 (and_11_out, OP5, not_71_out, OP3, not_72_out, OP1, OP0);
  and and_12 (and_12_out, not_73_out, not_74_out, not_75_out, not_76_out, not_77_out, not_78_out, F5, not_79_out, not_80_out, F2, F1, not_81_out);
  and and_13 (and_13_out, OP5, not_82_out, not_83_out, OP2, not_84_out, not_85_out);
  and and_14 (and_14_out, not_86_out, not_87_out, not_88_out, OP2, OP1, not_89_out);
  and and_15 (and_15_out, not_90_out, not_91_out, not_92_out, not_93_out, not_94_out, not_95_out, not_96_out, not_97_out, not_98_out, not_99_out, F1, not_100_out);
  and and_16 (and_16_out, not_101_out, not_102_out, not_103_out, not_104_out, not_105_out, not_106_out, F5, not_107_out, not_108_out, not_109_out, F1, not_110_out);
  and and_17 (and_17_out, not_111_out, not_112_out, not_113_out, not_114_out, not_115_out, not_116_out, F5, not_117_out, not_118_out, F2, not_119_out, not_120_out);
  and and_18 (and_18_out, not_121_out, not_122_out, not_123_out, not_124_out, not_125_out, not_126_out, F5, not_127_out, not_128_out, F2, F1, F0);
  and and_19 (and_19_out, not_129_out, not_130_out, not_131_out, not_132_out, not_133_out, not_134_out, F5, not_135_out, F3, not_136_out, F1, not_137_out);
  and and_20 (and_20_out, not_138_out, not_139_out, OP3, OP2, not_140_out, not_141_out);
  and and_21 (and_21_out, not_142_out, not_143_out, OP3, not_144_out, OP1, not_145_out);
  and and_22 (and_22_out, not_146_out, not_147_out, not_148_out, not_149_out, not_150_out, not_151_out, not_152_out, not_153_out, not_154_out, F2, F1, not_155_out);
  and and_23 (and_23_out, not_156_out, not_157_out, not_158_out, OP2, OP1, not_159_out);
  and and_24 (and_24_out, not_160_out, not_161_out, not_162_out, not_163_out, not_164_out, not_165_out, F5, not_166_out, not_167_out, not_168_out, not_169_out, not_170_out);
  and and_25 (and_25_out, not_171_out, not_172_out, not_173_out, not_174_out, not_175_out, not_176_out, F5, not_177_out, not_178_out, not_179_out, not_180_out, F0);
  and and_26 (and_26_out, not_181_out, not_182_out, not_183_out, not_184_out, not_185_out, not_186_out, F5, not_187_out, not_188_out, not_189_out, F1, not_190_out);
  and and_27 (and_27_out, not_191_out, not_192_out, not_193_out, not_194_out, not_195_out, not_196_out, F5, not_197_out, not_198_out, F2, not_199_out, not_200_out);
  and and_28 (and_28_out, not_201_out, not_202_out, not_203_out, not_204_out, not_205_out, not_206_out, F5, not_207_out, F3, not_208_out, F1, F0);
  and and_29 (and_29_out, not_209_out, not_210_out, OP3, not_211_out, not_212_out, not_213_out);
  and and_30 (and_30_out, not_214_out, not_215_out, OP3, OP2, not_216_out, not_217_out);
  and and_31 (and_31_out, not_218_out, not_219_out, OP3, not_220_out, not_221_out, OP0);
  and and_32 (and_32_out, OP5, not_222_out, not_223_out, not_224_out, OP1, OP0);
  and and_33 (and_33_out, OP5, not_225_out, OP3, not_226_out, OP1, OP0);
  and and_34 (and_34_out, OP5, not_227_out, not_228_out, OP2, not_229_out, not_230_out, not_231_out, not_232_out, not_233_out, not_234_out, not_235_out, not_236_out, F5, not_237_out, not_238_out, not_239_out, not_240_out, not_241_out);
  and and_35 (and_35_out, not_242_out, not_243_out, not_244_out, not_245_out, not_246_out, not_247_out, F5, not_248_out, not_249_out, not_250_out, not_251_out, F0);
  and and_36 (and_36_out, not_252_out, not_253_out, not_254_out, not_255_out, not_256_out, not_257_out, F5, not_258_out, not_259_out, not_260_out, F1, not_261_out);
  and and_37 (and_37_out, not_262_out, not_263_out, not_264_out, not_265_out, not_266_out, not_267_out, F5, not_268_out, not_269_out, F2, not_270_out, not_271_out);
  and and_38 (and_38_out, not_272_out, not_273_out, not_274_out, not_275_out, not_276_out, not_277_out, F5, not_278_out, F3, not_279_out, F1, F0);
  and and_39 (and_39_out, not_280_out, not_281_out, OP3, not_282_out, not_283_out, not_284_out);
  and and_40 (and_40_out, not_285_out, not_286_out, OP3, OP2, not_287_out, not_288_out);
  and and_41 (and_41_out, not_289_out, not_290_out, OP3, not_291_out, not_292_out, OP0);
  and and_42 (and_42_out, OP5, not_293_out, not_294_out, not_295_out, OP1, OP0);
  and and_43 (and_43_out, OP5, not_296_out, OP3, not_297_out, OP1, OP0);
  and and_44 (and_44_out, OP5, not_298_out, not_299_out, OP2, not_300_out, not_301_out, not_302_out, not_303_out, not_304_out, not_305_out, not_306_out, not_307_out, F5, not_308_out, not_309_out, not_310_out, not_311_out, not_312_out);
  and and_45 (and_45_out, not_313_out, not_314_out, not_315_out, not_316_out, not_317_out, not_318_out, F5, not_319_out, not_320_out, not_321_out, not_322_out, F0);
  and and_46 (and_46_out, not_323_out, not_324_out, not_325_out, not_326_out, not_327_out, not_328_out, F5, not_329_out, not_330_out, not_331_out, F1, not_332_out);
  and and_47 (and_47_out, not_333_out, not_334_out, not_335_out, not_336_out, not_337_out, not_338_out, F5, not_339_out, not_340_out, F2, not_341_out, not_342_out);
  and and_48 (and_48_out, not_343_out, not_344_out, not_345_out, not_346_out, not_347_out, not_348_out, F5, not_349_out, F3, not_350_out, F1, F0);
  and and_49 (and_49_out, not_351_out, not_352_out, OP3, not_353_out, not_354_out, not_355_out);
  and and_50 (and_50_out, not_356_out, not_357_out, OP3, OP2, not_358_out, not_359_out);
  and and_51 (and_51_out, not_360_out, not_361_out, OP3, not_362_out, not_363_out, OP0);
  and and_52 (and_52_out, OP5, not_364_out, not_365_out, not_366_out, OP1, OP0);
  and and_53 (and_53_out, OP5, not_367_out, OP3, not_368_out, OP1, OP0);
  and and_54 (and_54_out, OP5, not_369_out, not_370_out, OP2, not_371_out, not_372_out);
  and and_55 (and_55_out, not_373_out, not_374_out, not_375_out, not_376_out, not_377_out, not_378_out, F5, not_379_out, not_380_out, F2, not_381_out, F0);
  and and_56 (and_56_out, not_382_out, not_383_out, not_384_out, not_385_out, not_386_out, not_387_out, F5, not_388_out, not_389_out, F2, F1, F0);
  and and_57 (and_57_out, not_390_out, not_391_out, not_392_out, not_393_out, not_394_out, not_395_out, F5, not_396_out, F3, not_397_out, F1, not_398_out);
  and and_58 (and_58_out, not_399_out, not_400_out, not_401_out, not_402_out, not_403_out, not_404_out, F5, not_405_out, F3, not_406_out, F1, F0);
  and and_59 (and_59_out, not_407_out, not_408_out, OP3, not_409_out, OP1, not_410_out);
  and and_60 (and_60_out, not_411_out, not_412_out, OP3, OP2, not_413_out, OP0);
  and and_61 (and_61_out, not_414_out, not_415_out, not_416_out, not_417_out, not_418_out, not_419_out, F5, not_420_out, not_421_out, F2, F1, not_422_out);
  and and_62 (and_62_out, not_423_out, not_424_out, not_425_out, OP2, OP1, not_426_out);
  or or_1 (S1, and_15_out, and_16_out, and_17_out, and_18_out, and_19_out, and_20_out, and_21_out, and_22_out, and_23_out);
  or or_2 (S3, and_55_out, and_56_out, and_57_out, and_58_out, and_59_out, and_60_out, and_61_out, and_62_out);
  or or_3 (S0, and_1_out, and_2_out, and_3_out, and_4_out, and_5_out, and_6_out, and_7_out, and_8_out, and_9_out, and_10_out, and_11_out, and_12_out, and_13_out, and_14_out);
  or or_4 (S2, and_24_out, and_25_out, and_26_out, and_27_out, and_28_out, and_29_out, and_30_out, and_31_out, and_32_out, and_33_out, and_34_out, and_35_out, and_36_out, and_37_out, and_38_out, and_39_out, and_40_out, and_41_out, and_42_out, and_43_out, and_44_out, and_45_out, and_46_out, and_47_out, and_48_out, and_49_out, and_50_out, and_51_out, and_52_out, and_53_out, and_54_out);
endmodule

// 控制信号生成
module \控制信号生成  (
  input  OP0,
  input  OP1,
  input  OP2,
  input  OP3,
  input  OP4,
  input  OP5,
  input  F0,
  input  F1,
  input  F2,
  input  F3,
  input  F4,
  input  F5,
  output MemWrite,
  output JAL,
  output JMP,
  output ALU_SRC,
  output RegWrite,
  output SysCALL,
  output MemtoReg,
  output SignedExt,
  output RegDst,
  output BEQ,
  output BNE,
  output JR
);

  wire and_4_out, and_5_out, and_6_out, and_7_out, and_8_out, and_9_out, and_10_out, and_11_out, and_12_out,
       and_13_out, and_14_out, and_15_out, and_16_out, and_17_out, and_18_out, and_19_out, and_20_out,
       and_21_out, and_22_out, and_23_out, and_24_out, and_25_out, and_26_out, and_27_out, and_28_out,
       and_29_out, and_30_out, and_31_out, and_32_out, and_34_out, and_35_out, and_36_out, and_37_out,
       and_38_out, and_39_out, and_40_out, and_41_out, and_42_out, and_43_out, and_44_out, and_45_out,
       and_46_out, and_47_out, and_48_out, and_49_out, and_50_out, and_51_out, and_52_out, and_53_out,
       and_54_out, and_55_out, and_56_out, not_1_out, not_2_out, not_3_out, not_4_out, not_5_out, not_6_out,
       not_7_out, not_8_out, not_9_out, not_10_out, not_11_out, not_12_out, not_13_out, not_14_out,
       not_15_out, not_16_out, not_17_out, not_18_out, not_19_out, not_20_out, not_21_out, not_22_out,
       not_23_out, not_24_out, not_25_out, not_26_out, not_27_out, not_28_out, not_29_out, not_30_out,
       not_31_out, not_32_out, not_33_out, not_34_out, not_35_out, not_36_out, not_37_out, not_38_out,
       not_39_out, not_40_out, not_41_out, not_42_out, not_43_out, not_44_out, not_45_out, not_46_out,
       not_47_out, not_48_out, not_49_out, not_50_out, not_51_out, not_52_out, not_53_out, not_54_out,
       not_55_out, not_56_out, not_57_out, not_58_out, not_59_out, not_60_out, not_61_out, not_62_out,
       not_63_out, not_64_out, not_65_out, not_66_out, not_67_out, not_68_out, not_69_out, not_70_out,
       not_71_out, not_72_out, not_73_out, not_74_out, not_75_out, not_76_out, not_77_out, not_78_out,
       not_79_out, not_80_out, not_81_out, not_82_out, not_83_out, not_84_out, not_85_out, not_86_out,
       not_87_out, not_88_out, not_89_out, not_90_out, not_91_out, not_92_out, not_93_out, not_94_out,
       not_95_out, not_96_out, not_97_out, not_98_out, not_99_out, not_100_out, not_101_out, not_102_out,
       not_103_out, not_104_out, not_105_out, not_106_out, not_107_out, not_108_out, not_109_out,
       not_110_out, not_111_out, not_112_out, not_113_out, not_114_out, not_115_out, not_116_out,
       not_117_out, not_118_out, not_119_out, not_120_out, not_121_out, not_122_out, not_123_out,
       not_124_out, not_125_out, not_126_out, not_127_out, not_128_out, not_129_out, not_130_out,
       not_131_out, not_132_out, not_133_out, not_134_out, not_135_out, not_136_out, not_137_out,
       not_138_out, not_139_out, not_140_out, not_141_out, not_142_out, not_143_out, not_144_out,
       not_145_out, not_146_out, not_147_out, not_148_out, not_149_out, not_150_out, not_151_out,
       not_152_out, not_153_out, not_154_out, not_155_out, not_156_out, not_157_out, not_158_out,
       not_159_out, not_160_out, not_161_out, not_162_out, not_163_out, not_164_out, not_165_out,
       not_166_out, not_167_out, not_168_out, not_169_out, not_170_out, not_171_out, not_172_out,
       not_173_out, not_174_out, not_175_out, not_176_out, not_177_out, not_178_out, not_179_out,
       not_180_out, not_181_out, not_182_out, not_183_out, not_184_out, not_185_out, not_186_out,
       not_187_out, not_188_out, not_189_out, not_190_out, not_191_out, not_192_out, not_193_out,
       not_194_out, not_195_out, not_196_out, not_197_out, not_198_out, not_199_out, not_200_out,
       not_201_out, not_202_out, not_203_out, not_204_out, not_205_out, not_206_out, not_207_out,
       not_208_out, not_209_out, not_210_out, not_211_out, not_212_out, not_213_out, not_214_out,
       not_215_out, not_216_out, not_217_out, not_218_out, not_219_out, not_220_out, not_221_out,
       not_222_out, not_223_out, not_224_out, not_225_out, not_226_out, not_227_out, not_228_out,
       not_229_out, not_230_out, not_231_out, not_232_out, not_233_out, not_234_out, not_235_out,
       not_236_out, not_237_out, not_238_out, not_239_out, not_240_out, not_241_out, not_242_out,
       not_243_out, not_244_out, not_245_out, not_246_out, not_247_out, not_248_out, not_249_out,
       not_250_out, not_251_out, not_252_out, not_253_out, not_254_out, not_255_out, not_256_out,
       not_257_out, not_258_out, not_259_out, not_260_out, not_261_out, not_262_out, not_263_out,
       not_264_out, not_265_out, not_266_out, not_267_out, not_268_out, not_269_out, not_270_out,
       not_271_out, not_272_out, not_273_out, not_274_out, not_275_out, not_276_out, not_277_out,
       not_278_out, not_279_out, not_280_out, not_281_out, not_282_out, not_283_out, not_284_out,
       not_285_out, not_286_out, not_287_out, not_288_out, not_289_out, not_290_out, not_291_out,
       not_292_out, not_293_out, not_294_out, not_295_out, not_296_out, not_297_out, not_298_out,
       not_299_out, not_300_out, not_301_out, not_302_out, not_303_out, not_304_out, not_305_out,
       not_306_out, not_307_out, not_308_out, not_309_out, not_310_out, not_311_out, not_312_out,
       not_313_out, not_314_out, not_315_out, not_316_out, not_317_out, not_318_out, not_319_out,
       not_320_out, not_321_out, not_322_out, not_323_out, not_324_out, not_325_out, not_326_out,
       not_327_out, not_328_out, not_329_out, not_330_out, not_331_out, not_332_out, not_333_out,
       not_334_out, not_335_out, not_336_out, not_337_out, not_338_out, not_339_out, not_340_out,
       not_341_out, not_342_out, not_343_out, not_344_out, not_345_out, not_346_out, not_347_out,
       not_348_out, not_349_out, not_350_out, not_351_out, not_352_out, not_353_out, not_354_out,
       not_355_out, not_356_out, not_357_out, not_358_out, not_359_out, not_360_out, not_361_out,
       not_362_out, not_363_out, not_364_out, not_365_out, not_366_out, not_367_out, not_368_out,
       not_369_out, not_370_out, not_371_out, not_372_out, not_373_out, not_374_out, not_375_out,
       not_376_out, not_377_out, not_378_out, not_379_out, not_380_out, not_381_out, not_382_out,
       not_383_out, not_384_out, not_385_out, not_386_out, not_387_out, not_388_out, not_389_out,
       not_390_out, not_391_out, not_392_out, not_393_out;

  not not_1 (not_1_out, OP4);
  not not_2 (not_2_out, OP2);
  not not_3 (not_3_out, OP5);
  not not_4 (not_4_out, OP4);
  not not_5 (not_5_out, OP3);
  not not_6 (not_6_out, OP2);
  not not_7 (not_7_out, OP5);
  not not_8 (not_8_out, OP4);
  not not_9 (not_9_out, OP3);
  not not_10 (not_10_out, OP2);
  not not_11 (not_11_out, OP0);
  not not_12 (not_12_out, OP5);
  not not_13 (not_13_out, OP4);
  not not_14 (not_14_out, OP2);
  not not_15 (not_15_out, OP1);
  not not_16 (not_16_out, OP0);
  not not_17 (not_17_out, OP5);
  not not_18 (not_18_out, OP4);
  not not_19 (not_19_out, OP1);
  not not_20 (not_20_out, OP0);
  not not_21 (not_21_out, OP5);
  not not_22 (not_22_out, OP4);
  not not_23 (not_23_out, OP2);
  not not_24 (not_24_out, OP1);
  not not_25 (not_25_out, OP5);
  not not_26 (not_26_out, OP4);
  not not_27 (not_27_out, OP2);
  not not_28 (not_28_out, OP0);
  not not_29 (not_29_out, OP5);
  not not_30 (not_30_out, OP4);
  not not_31 (not_31_out, OP1);
  not not_32 (not_32_out, OP4);
  not not_33 (not_33_out, OP3);
  not not_34 (not_34_out, OP2);
  not not_35 (not_35_out, OP4);
  not not_36 (not_36_out, OP2);
  not not_37 (not_37_out, OP4);
  not not_38 (not_38_out, OP3);
  not not_39 (not_39_out, OP1);
  not not_40 (not_40_out, OP0);
  not not_41 (not_41_out, OP5);
  not not_42 (not_42_out, OP4);
  not not_43 (not_43_out, OP3);
  not not_44 (not_44_out, OP2);
  not not_45 (not_45_out, OP1);
  not not_46 (not_46_out, OP0);
  not not_47 (not_47_out, F5);
  not not_48 (not_48_out, F4);
  not not_49 (not_49_out, F3);
  not not_50 (not_50_out, F2);
  not not_51 (not_51_out, F1);
  not not_52 (not_52_out, F0);
  not not_53 (not_53_out, OP5);
  not not_54 (not_54_out, OP4);
  not not_55 (not_55_out, OP3);
  not not_56 (not_56_out, OP2);
  not not_57 (not_57_out, OP1);
  not not_58 (not_58_out, OP0);
  not not_59 (not_59_out, F5);
  not not_60 (not_60_out, F4);
  not not_61 (not_61_out, F3);
  not not_62 (not_62_out, F2);
  not not_63 (not_63_out, OP5);
  not not_64 (not_64_out, OP4);
  not not_65 (not_65_out, OP3);
  not not_66 (not_66_out, OP2);
  not not_67 (not_67_out, OP1);
  not not_68 (not_68_out, OP0);
  not not_69 (not_69_out, F5);
  not not_70 (not_70_out, F4);
  not not_71 (not_71_out, F3);
  not not_72 (not_72_out, F2);
  not not_73 (not_73_out, F0);
  not not_74 (not_74_out, OP5);
  not not_75 (not_75_out, OP4);
  not not_76 (not_76_out, OP3);
  not not_77 (not_77_out, OP2);
  not not_78 (not_78_out, OP1);
  not not_79 (not_79_out, OP0);
  not not_80 (not_80_out, F4);
  not not_81 (not_81_out, F3);
  not not_82 (not_82_out, F2);
  not not_83 (not_83_out, F1);
  not not_84 (not_84_out, F0);
  not not_85 (not_85_out, OP5);
  not not_86 (not_86_out, OP4);
  not not_87 (not_87_out, OP3);
  not not_88 (not_88_out, OP2);
  not not_89 (not_89_out, OP1);
  not not_90 (not_90_out, OP0);
  not not_91 (not_91_out, F4);
  not not_92 (not_92_out, F3);
  not not_93 (not_93_out, F2);
  not not_94 (not_94_out, F1);
  not not_95 (not_95_out, OP5);
  not not_96 (not_96_out, OP4);
  not not_97 (not_97_out, OP3);
  not not_98 (not_98_out, OP2);
  not not_99 (not_99_out, OP1);
  not not_100 (not_100_out, OP0);
  not not_101 (not_101_out, F4);
  not not_102 (not_102_out, F3);
  not not_103 (not_103_out, F2);
  not not_104 (not_104_out, F0);
  not not_105 (not_105_out, OP5);
  not not_106 (not_106_out, OP4);
  not not_107 (not_107_out, OP3);
  not not_108 (not_108_out, OP2);
  not not_109 (not_109_out, OP1);
  not not_110 (not_110_out, OP0);
  not not_111 (not_111_out, F4);
  not not_112 (not_112_out, F3);
  not not_113 (not_113_out, F1);
  not not_114 (not_114_out, F0);
  not not_115 (not_115_out, OP5);
  not not_116 (not_116_out, OP4);
  not not_117 (not_117_out, OP3);
  not not_118 (not_118_out, OP2);
  not not_119 (not_119_out, OP1);
  not not_120 (not_120_out, OP0);
  not not_121 (not_121_out, F4);
  not not_122 (not_122_out, F3);
  not not_123 (not_123_out, F1);
  not not_124 (not_124_out, OP5);
  not not_125 (not_125_out, OP4);
  not not_126 (not_126_out, OP3);
  not not_127 (not_127_out, OP2);
  not not_128 (not_128_out, OP1);
  not not_129 (not_129_out, OP0);
  not not_130 (not_130_out, F4);
  not not_131 (not_131_out, F3);
  not not_132 (not_132_out, OP5);
  not not_133 (not_133_out, OP4);
  not not_134 (not_134_out, OP3);
  not not_135 (not_135_out, OP2);
  not not_136 (not_136_out, OP1);
  not not_137 (not_137_out, OP0);
  not not_138 (not_138_out, F4);
  not not_139 (not_139_out, F2);
  not not_140 (not_140_out, F0);
  not not_141 (not_141_out, OP5);
  not not_142 (not_142_out, OP4);
  not not_143 (not_143_out, OP3);
  not not_144 (not_144_out, OP2);
  not not_145 (not_145_out, OP1);
  not not_146 (not_146_out, OP0);
  not not_147 (not_147_out, F4);
  not not_148 (not_148_out, F2);
  not not_149 (not_149_out, OP5);
  not not_150 (not_150_out, OP4);
  not not_151 (not_151_out, OP3);
  not not_152 (not_152_out, OP2);
  not not_153 (not_153_out, OP5);
  not not_154 (not_154_out, OP4);
  not not_155 (not_155_out, OP2);
  not not_156 (not_156_out, OP1);
  not not_157 (not_157_out, OP0);
  not not_158 (not_158_out, OP5);
  not not_159 (not_159_out, OP4);
  not not_160 (not_160_out, OP1);
  not not_161 (not_161_out, OP0);
  not not_162 (not_162_out, OP5);
  not not_163 (not_163_out, OP4);
  not not_164 (not_164_out, OP2);
  not not_165 (not_165_out, OP1);
  not not_166 (not_166_out, OP5);
  not not_167 (not_167_out, OP4);
  not not_168 (not_168_out, OP2);
  not not_169 (not_169_out, OP0);
  not not_170 (not_170_out, OP5);
  not not_171 (not_171_out, OP4);
  not not_172 (not_172_out, OP1);
  not not_173 (not_173_out, OP4);
  not not_174 (not_174_out, OP3);
  not not_175 (not_175_out, OP2);
  not not_176 (not_176_out, OP5);
  not not_177 (not_177_out, OP4);
  not not_178 (not_178_out, OP3);
  not not_179 (not_179_out, OP2);
  not not_180 (not_180_out, OP1);
  not not_181 (not_181_out, OP0);
  not not_182 (not_182_out, F5);
  not not_183 (not_183_out, F4);
  not not_184 (not_184_out, F3);
  not not_185 (not_185_out, F0);
  not not_186 (not_186_out, OP5);
  not not_187 (not_187_out, OP4);
  not not_188 (not_188_out, OP3);
  not not_189 (not_189_out, OP2);
  not not_190 (not_190_out, OP1);
  not not_191 (not_191_out, OP0);
  not not_192 (not_192_out, F4);
  not not_193 (not_193_out, F3);
  not not_194 (not_194_out, F0);
  not not_195 (not_195_out, OP4);
  not not_196 (not_196_out, OP3);
  not not_197 (not_197_out, OP1);
  not not_198 (not_198_out, OP0);
  not not_199 (not_199_out, OP5);
  not not_200 (not_200_out, OP4);
  not not_201 (not_201_out, OP3);
  not not_202 (not_202_out, OP2);
  not not_203 (not_203_out, OP1);
  not not_204 (not_204_out, OP0);
  not not_205 (not_205_out, F5);
  not not_206 (not_206_out, F4);
  not not_207 (not_207_out, F1);
  not not_208 (not_208_out, F0);
  not not_209 (not_209_out, OP4);
  not not_210 (not_210_out, OP3);
  not not_211 (not_211_out, OP2);
  not not_212 (not_212_out, OP4);
  not not_213 (not_213_out, OP3);
  not not_214 (not_214_out, OP1);
  not not_215 (not_215_out, OP0);
  not not_216 (not_216_out, OP5);
  not not_217 (not_217_out, OP4);
  not not_218 (not_218_out, OP3);
  not not_219 (not_219_out, OP1);
  not not_220 (not_220_out, OP0);
  not not_221 (not_221_out, OP5);
  not not_222 (not_222_out, OP4);
  not not_223 (not_223_out, OP3);
  not not_224 (not_224_out, OP1);
  not not_225 (not_225_out, OP5);
  not not_226 (not_226_out, OP4);
  not not_227 (not_227_out, OP2);
  not not_228 (not_228_out, OP1);
  not not_229 (not_229_out, OP0);
  not not_230 (not_230_out, OP5);
  not not_231 (not_231_out, OP4);
  not not_232 (not_232_out, OP2);
  not not_233 (not_233_out, OP0);
  not not_234 (not_234_out, OP4);
  not not_235 (not_235_out, OP3);
  not not_236 (not_236_out, OP2);
  not not_237 (not_237_out, OP4);
  not not_238 (not_238_out, OP2);
  not not_239 (not_239_out, OP4);
  not not_240 (not_240_out, OP3);
  not not_241 (not_241_out, OP1);
  not not_242 (not_242_out, OP0);
  not not_243 (not_243_out, OP5);
  not not_244 (not_244_out, OP4);
  not not_245 (not_245_out, OP3);
  not not_246 (not_246_out, OP0);
  not not_247 (not_247_out, OP5);
  not not_248 (not_248_out, OP4);
  not not_249 (not_249_out, OP3);
  not not_250 (not_250_out, OP2);
  not not_251 (not_251_out, OP1);
  not not_252 (not_252_out, OP0);
  not not_253 (not_253_out, F5);
  not not_254 (not_254_out, F4);
  not not_255 (not_255_out, F3);
  not not_256 (not_256_out, F2);
  not not_257 (not_257_out, F1);
  not not_258 (not_258_out, F0);
  not not_259 (not_259_out, OP5);
  not not_260 (not_260_out, OP4);
  not not_261 (not_261_out, OP3);
  not not_262 (not_262_out, OP2);
  not not_263 (not_263_out, OP1);
  not not_264 (not_264_out, OP0);
  not not_265 (not_265_out, F5);
  not not_266 (not_266_out, F4);
  not not_267 (not_267_out, F3);
  not not_268 (not_268_out, F2);
  not not_269 (not_269_out, OP5);
  not not_270 (not_270_out, OP4);
  not not_271 (not_271_out, OP3);
  not not_272 (not_272_out, OP2);
  not not_273 (not_273_out, OP1);
  not not_274 (not_274_out, OP0);
  not not_275 (not_275_out, F5);
  not not_276 (not_276_out, F4);
  not not_277 (not_277_out, F3);
  not not_278 (not_278_out, F2);
  not not_279 (not_279_out, F0);
  not not_280 (not_280_out, OP5);
  not not_281 (not_281_out, OP4);
  not not_282 (not_282_out, OP3);
  not not_283 (not_283_out, OP2);
  not not_284 (not_284_out, OP1);
  not not_285 (not_285_out, OP0);
  not not_286 (not_286_out, F4);
  not not_287 (not_287_out, F3);
  not not_288 (not_288_out, F2);
  not not_289 (not_289_out, F1);
  not not_290 (not_290_out, F0);
  not not_291 (not_291_out, OP5);
  not not_292 (not_292_out, OP4);
  not not_293 (not_293_out, OP3);
  not not_294 (not_294_out, OP2);
  not not_295 (not_295_out, OP1);
  not not_296 (not_296_out, OP0);
  not not_297 (not_297_out, F4);
  not not_298 (not_298_out, F3);
  not not_299 (not_299_out, F2);
  not not_300 (not_300_out, F1);
  not not_301 (not_301_out, OP5);
  not not_302 (not_302_out, OP4);
  not not_303 (not_303_out, OP3);
  not not_304 (not_304_out, OP2);
  not not_305 (not_305_out, OP1);
  not not_306 (not_306_out, OP0);
  not not_307 (not_307_out, F4);
  not not_308 (not_308_out, F3);
  not not_309 (not_309_out, F2);
  not not_310 (not_310_out, F0);
  not not_311 (not_311_out, OP5);
  not not_312 (not_312_out, OP4);
  not not_313 (not_313_out, OP3);
  not not_314 (not_314_out, OP2);
  not not_315 (not_315_out, OP1);
  not not_316 (not_316_out, OP0);
  not not_317 (not_317_out, F4);
  not not_318 (not_318_out, F3);
  not not_319 (not_319_out, F1);
  not not_320 (not_320_out, F0);
  not not_321 (not_321_out, OP5);
  not not_322 (not_322_out, OP4);
  not not_323 (not_323_out, OP3);
  not not_324 (not_324_out, OP2);
  not not_325 (not_325_out, OP1);
  not not_326 (not_326_out, OP0);
  not not_327 (not_327_out, F4);
  not not_328 (not_328_out, F3);
  not not_329 (not_329_out, F1);
  not not_330 (not_330_out, OP5);
  not not_331 (not_331_out, OP4);
  not not_332 (not_332_out, OP3);
  not not_333 (not_333_out, OP2);
  not not_334 (not_334_out, OP1);
  not not_335 (not_335_out, OP0);
  not not_336 (not_336_out, F4);
  not not_337 (not_337_out, F3);
  not not_338 (not_338_out, OP5);
  not not_339 (not_339_out, OP4);
  not not_340 (not_340_out, OP3);
  not not_341 (not_341_out, OP2);
  not not_342 (not_342_out, OP1);
  not not_343 (not_343_out, OP0);
  not not_344 (not_344_out, F4);
  not not_345 (not_345_out, F2);
  not not_346 (not_346_out, F0);
  not not_347 (not_347_out, OP5);
  not not_348 (not_348_out, OP4);
  not not_349 (not_349_out, OP3);
  not not_350 (not_350_out, OP2);
  not not_351 (not_351_out, OP1);
  not not_352 (not_352_out, OP0);
  not not_353 (not_353_out, F4);
  not not_354 (not_354_out, F2);
  not not_355 (not_355_out, OP5);
  not not_356 (not_356_out, OP4);
  not not_357 (not_357_out, OP3);
  not not_358 (not_358_out, OP2);
  not not_359 (not_359_out, OP1);
  not not_360 (not_360_out, OP0);
  not not_361 (not_361_out, F5);
  not not_362 (not_362_out, F4);
  not not_363 (not_363_out, F3);
  not not_364 (not_364_out, F0);
  not not_365 (not_365_out, OP5);
  not not_366 (not_366_out, OP4);
  not not_367 (not_367_out, OP3);
  not not_368 (not_368_out, OP2);
  not not_369 (not_369_out, OP1);
  not not_370 (not_370_out, OP0);
  not not_371 (not_371_out, F4);
  not not_372 (not_372_out, F3);
  not not_373 (not_373_out, F0);
  not not_374 (not_374_out, OP5);
  not not_375 (not_375_out, OP4);
  not not_376 (not_376_out, OP3);
  not not_377 (not_377_out, OP1);
  not not_378 (not_378_out, OP0);
  not not_379 (not_379_out, OP5);
  not not_380 (not_380_out, OP4);
  not not_381 (not_381_out, OP3);
  not not_382 (not_382_out, OP1);
  not not_383 (not_383_out, OP5);
  not not_384 (not_384_out, OP4);
  not not_385 (not_385_out, OP3);
  not not_386 (not_386_out, OP2);
  not not_387 (not_387_out, OP1);
  not not_388 (not_388_out, OP0);
  not not_389 (not_389_out, F5);
  not not_390 (not_390_out, F4);
  not not_391 (not_391_out, F2);
  not not_392 (not_392_out, F1);
  not not_393 (not_393_out, F0);
  and and_1 (MemWrite, OP5, not_1_out, OP3, not_2_out, OP1, OP0);
  and and_2 (JAL, not_3_out, not_4_out, not_5_out, not_6_out, OP1, OP0);
  and and_3 (JMP, not_7_out, not_8_out, not_9_out, not_10_out, OP1, not_11_out);
  and and_4 (and_4_out, not_12_out, not_13_out, OP3, not_14_out, not_15_out, not_16_out);
  and and_5 (and_5_out, not_17_out, not_18_out, OP3, OP2, not_19_out, not_20_out);
  and and_6 (and_6_out, not_21_out, not_22_out, OP3, not_23_out, not_24_out, OP0);
  and and_7 (and_7_out, not_25_out, not_26_out, OP3, not_27_out, OP1, not_28_out);
  and and_8 (and_8_out, not_29_out, not_30_out, OP3, OP2, not_31_out, OP0);
  and and_9 (and_9_out, OP5, not_32_out, not_33_out, not_34_out, OP1, OP0);
  and and_10 (and_10_out, OP5, not_35_out, OP3, not_36_out, OP1, OP0);
  and and_11 (and_11_out, OP5, not_37_out, not_38_out, OP2, not_39_out, not_40_out);
  and and_12 (and_12_out, not_41_out, not_42_out, not_43_out, not_44_out, not_45_out, not_46_out, not_47_out, not_48_out, not_49_out, not_50_out, not_51_out, not_52_out);
  and and_13 (and_13_out, not_53_out, not_54_out, not_55_out, not_56_out, not_57_out, not_58_out, not_59_out, not_60_out, not_61_out, not_62_out, F1, F0);
  and and_14 (and_14_out, not_63_out, not_64_out, not_65_out, not_66_out, not_67_out, not_68_out, not_69_out, not_70_out, not_71_out, not_72_out, F1, not_73_out);
  and and_15 (and_15_out, not_74_out, not_75_out, not_76_out, not_77_out, not_78_out, not_79_out, F5, not_80_out, not_81_out, not_82_out, not_83_out, not_84_out);
  and and_16 (and_16_out, not_85_out, not_86_out, not_87_out, not_88_out, not_89_out, not_90_out, F5, not_91_out, not_92_out, not_93_out, not_94_out, F0);
  and and_17 (and_17_out, not_95_out, not_96_out, not_97_out, not_98_out, not_99_out, not_100_out, F5, not_101_out, not_102_out, not_103_out, F1, not_104_out);
  and and_18 (and_18_out, not_105_out, not_106_out, not_107_out, not_108_out, not_109_out, not_110_out, F5, not_111_out, not_112_out, F2, not_113_out, not_114_out);
  and and_19 (and_19_out, not_115_out, not_116_out, not_117_out, not_118_out, not_119_out, not_120_out, F5, not_121_out, not_122_out, F2, not_123_out, F0);
  and and_20 (and_20_out, not_124_out, not_125_out, not_126_out, not_127_out, not_128_out, not_129_out, F5, not_130_out, not_131_out, F2, F1, F0);
  and and_21 (and_21_out, not_132_out, not_133_out, not_134_out, not_135_out, not_136_out, not_137_out, F5, not_138_out, F3, not_139_out, F1, not_140_out);
  and and_22 (and_22_out, not_141_out, not_142_out, not_143_out, not_144_out, not_145_out, not_146_out, F5, not_147_out, F3, not_148_out, F1, F0);
  and and_23 (and_23_out, not_149_out, not_150_out, not_151_out, not_152_out, OP1, OP0);
  and and_24 (and_24_out, not_153_out, not_154_out, OP3, not_155_out, not_156_out, not_157_out);
  and and_25 (and_25_out, not_158_out, not_159_out, OP3, OP2, not_160_out, not_161_out);
  and and_26 (and_26_out, not_162_out, not_163_out, OP3, not_164_out, not_165_out, OP0);
  and and_27 (and_27_out, not_166_out, not_167_out, OP3, not_168_out, OP1, not_169_out);
  and and_28 (and_28_out, not_170_out, not_171_out, OP3, OP2, not_172_out, OP0);
  and and_29 (and_29_out, OP5, not_173_out, not_174_out, not_175_out, OP1, OP0);
  and and_30 (and_30_out, not_176_out, not_177_out, not_178_out, not_179_out, not_180_out, not_181_out, not_182_out, not_183_out, not_184_out, F2, F1, not_185_out);
  and and_31 (and_31_out, not_186_out, not_187_out, not_188_out, not_189_out, not_190_out, not_191_out, F5, not_192_out, not_193_out, F2, F1, not_194_out);
  and and_32 (and_32_out, OP5, not_195_out, not_196_out, OP2, not_197_out, not_198_out);
  and and_33 (SysCALL, not_199_out, not_200_out, not_201_out, not_202_out, not_203_out, not_204_out, not_205_out, not_206_out, F3, F2, not_207_out, not_208_out);
  and and_34 (and_34_out, OP5, not_209_out, not_210_out, not_211_out, OP1, OP0);
  and and_35 (and_35_out, OP5, not_212_out, not_213_out, OP2, not_214_out, not_215_out);
  and and_36 (and_36_out, not_216_out, not_217_out, not_218_out, OP2, not_219_out, not_220_out);
  and and_37 (and_37_out, not_221_out, not_222_out, not_223_out, OP2, not_224_out, OP0);
  and and_38 (and_38_out, not_225_out, not_226_out, OP3, not_227_out, not_228_out, not_229_out);
  and and_39 (and_39_out, not_230_out, not_231_out, OP3, not_232_out, OP1, not_233_out);
  and and_40 (and_40_out, OP5, not_234_out, not_235_out, not_236_out, OP1, OP0);
  and and_41 (and_41_out, OP5, not_237_out, OP3, not_238_out, OP1, OP0);
  and and_42 (and_42_out, OP5, not_239_out, not_240_out, OP2, not_241_out, not_242_out);
  and and_43 (and_43_out, not_243_out, not_244_out, not_245_out, OP2, OP1, not_246_out);
  and and_44 (and_44_out, not_247_out, not_248_out, not_249_out, not_250_out, not_251_out, not_252_out, not_253_out, not_254_out, not_255_out, not_256_out, not_257_out, not_258_out);
  and and_45 (and_45_out, not_259_out, not_260_out, not_261_out, not_262_out, not_263_out, not_264_out, not_265_out, not_266_out, not_267_out, not_268_out, F1, F0);
  and and_46 (and_46_out, not_269_out, not_270_out, not_271_out, not_272_out, not_273_out, not_274_out, not_275_out, not_276_out, not_277_out, not_278_out, F1, not_279_out);
  and and_47 (and_47_out, not_280_out, not_281_out, not_282_out, not_283_out, not_284_out, not_285_out, F5, not_286_out, not_287_out, not_288_out, not_289_out, not_290_out);
  and and_48 (and_48_out, not_291_out, not_292_out, not_293_out, not_294_out, not_295_out, not_296_out, F5, not_297_out, not_298_out, not_299_out, not_300_out, F0);
  and and_49 (and_49_out, not_301_out, not_302_out, not_303_out, not_304_out, not_305_out, not_306_out, F5, not_307_out, not_308_out, not_309_out, F1, not_310_out);
  and and_50 (and_50_out, not_311_out, not_312_out, not_313_out, not_314_out, not_315_out, not_316_out, F5, not_317_out, not_318_out, F2, not_319_out, not_320_out);
  and and_51 (and_51_out, not_321_out, not_322_out, not_323_out, not_324_out, not_325_out, not_326_out, F5, not_327_out, not_328_out, F2, not_329_out, F0);
  and and_52 (and_52_out, not_330_out, not_331_out, not_332_out, not_333_out, not_334_out, not_335_out, F5, not_336_out, not_337_out, F2, F1, F0);
  and and_53 (and_53_out, not_338_out, not_339_out, not_340_out, not_341_out, not_342_out, not_343_out, F5, not_344_out, F3, not_345_out, F1, not_346_out);
  and and_54 (and_54_out, not_347_out, not_348_out, not_349_out, not_350_out, not_351_out, not_352_out, F5, not_353_out, F3, not_354_out, F1, F0);
  and and_55 (and_55_out, not_355_out, not_356_out, not_357_out, not_358_out, not_359_out, not_360_out, not_361_out, not_362_out, not_363_out, F2, F1, not_364_out);
  and and_56 (and_56_out, not_365_out, not_366_out, not_367_out, not_368_out, not_369_out, not_370_out, F5, not_371_out, not_372_out, F2, F1, not_373_out);
  and and_57 (BEQ, not_374_out, not_375_out, not_376_out, OP2, not_377_out, not_378_out);
  and and_58 (BNE, not_379_out, not_380_out, not_381_out, OP2, not_382_out, OP0);
  and and_59 (JR, not_383_out, not_384_out, not_385_out, not_386_out, not_387_out, not_388_out, not_389_out, not_390_out, F3, not_391_out, not_392_out, not_393_out);
  or or_1 (ALU_SRC, and_4_out, and_5_out, and_6_out, and_7_out, and_8_out, and_9_out, and_10_out, and_11_out);
  or or_2 (MemtoReg, and_34_out, and_35_out);
  or or_3 (SignedExt, and_36_out, and_37_out, and_38_out, and_39_out, and_40_out, and_41_out, and_42_out, and_43_out);
  or or_4 (RegWrite, and_12_out, and_13_out, and_14_out, and_15_out, and_16_out, and_17_out, and_18_out, and_19_out, and_20_out, and_21_out, and_22_out, and_23_out, and_24_out, and_25_out, and_26_out, and_27_out, and_28_out, and_29_out, and_30_out, and_31_out, and_32_out);
  or or_5 (RegDst, and_44_out, and_45_out, and_46_out, and_47_out, and_48_out, and_49_out, and_50_out, and_51_out, and_52_out, and_53_out, and_54_out, and_55_out, and_56_out);
endmodule

// ALU
module MIPS_ALU (
  input  [4:0] shamt,
  input  [31:0] X,
  input  [31:0] Y,
  input  [3:0] AluOP,
  output Equal,
  output [31:0] Result,
  output [31:0] Result_2
);

  wire [0:0] comparator_1_lt, comparator_2_lt;
  wire [31:0] adder_1_out, AND_out, divider_1_out, divider_1_rem, multiplier_1_cout, multiplier_1_out,
       NOR_out, OR_out, shifter_1_out, shifter_2_out, shifter_3_out, subtractor_1_out, XOR_out;

  assign AND_out = X & Y;  // AND_Gate AND, 32 bits wide
  assign OR_out = X | Y;  // OR_Gate OR, 32 bits wide
  Shifter #(.width(32)) shifter_1 (.in(Y), .\dist (shamt), .out(shifter_1_out));
  Shifter #(.width(32), .shift("ar")) shifter_2 (.in(Y), .\dist (shamt), .out(shifter_2_out));
  Shifter #(.width(32), .shift("lr")) shifter_3 (.in(Y), .\dist (shamt), .out(shifter_3_out));
  Multiplier #(.width(32)) multiplier_1 (.a(X), .b(Y), .out(multiplier_1_out), .cout(multiplier_1_cout));  // open: cin
  Divider #(.width(32)) divider_1 (.a(X), .b(Y), .out(divider_1_out), .rem(divider_1_rem));  // open: upper
  Adder #(.width(32)) adder_1 (.a(X), .b(Y), .out(adder_1_out));  // open: cin, cout
  Subtractor #(.width(32)) subtractor_1 (.a(X), .b(Y), .out(subtractor_1_out));  // open: bin, bout
  assign XOR_out = X ^ Y;  // XOR_Gate XOR, 32 bits wide
  assign NOR_out = ~(X | Y);  // NOR_Gate NOR, 32 bits wide
  Comparator #(.width(32)) comparator_1 (.a(X), .b(Y), .eq(Equal), .lt(comparator_1_lt[0]));  // open: gt
  Comparator #(.width(32), .mode("unsigned")) comparator_2 (.a(X), .b(Y), .lt(comparator_2_lt[0]));  // open: gt, eq
  Multiplexer #(.select(4), .width(32), .enable("false")) multiplexer_1 (
    .in0(shifter_1_out), .in1(shifter_2_out), .in2(shifter_3_out), .in3(multiplier_1_out),
    .in4(divider_1_out), .in5(adder_1_out), .in6(subtractor_1_out), .in7(AND_out), .in8(OR_out),
    .in9(XOR_out), .in10(NOR_out), .in11({{31{1'b0}}, comparator_1_lt[0]}),
    .in12({{31{1'b0}}, comparator_2_lt[0]}), .in13({32{1'b0}}), .in14({32{1'b0}}), .in15({32{1'b0}}),
    .out(Result), .sel(AluOP));
  Multiplexer #(.select(4), .width(32), .enable("false")) multiplexer_2 (
    .in0({32{1'b0}}), .in1({32{1'b0}}), .in2({32{1'b0}}), .in3(multiplier_1_cout), .in4(divider_1_rem),
    .in5({32{1'b0}}), .in6({32{1'b0}}), .in7({32{1'b0}}), .in8({32{1'b0}}), .in9({32{1'b0}}),
    .in10({32{1'b0}}), .in11({32{1'b0}}), .in12({32{1'b0}}), .in13({32{1'b0}}), .in14({32{1'b0}}),
    .in15({32{1'b0}}), .out(Result_2), .sel(AluOP));

  // Other names for the same wires on the sheet: Result2[31:0] = Result_2; S[3:0] = AluOP

  // Notes on the sheet:
  //   不要改变此引脚区域内容，也不要改变ALU封装形式
  //   输入引脚
  //   输出引脚
endmodule

module MIPS_Regifile (
  input  [31:0] Din,
  input  Clk,
  input  WE,
  input  [4:0] R1_num,
  input  [4:0] W_num,
  input  [4:0] R2_num,
  output [31:0] R1,
  output [31:0] R2
);

  // RegisterFile registerfile_1: pin names not known; wires that end beside it: Din, Clk, WE, W_num, R1_num, R2_num, R1, R2
endmodule

module IF_ID (
  input  [31:0] IR,
  input  [31:0] PC,
  input  rst,
  input  En,
  input  clk,
  input  tmp_rst,
  output [31:0] IR_out,
  output [31:0] PC_out,
  output En_out
);

  wire [31:0] multiplexer_1_out, multiplexer_2_out;

  Multiplexer #(.width(32), .enable("false")) multiplexer_1 (
    .in0(IR), .in1({32{1'b0}}), .out(multiplexer_1_out), .sel(tmp_rst));
  Multiplexer #(.width(32), .enable("false")) multiplexer_2 (
    .in0(PC), .in1({32{1'b0}}), .out(multiplexer_2_out), .sel(tmp_rst));
  Register #(.width(32)) register_1 (.D(multiplexer_1_out), .en(En), .Q(IR_out), .clk(clk), .clr(rst));
  Register #(.width(32)) register_2 (.D(multiplexer_2_out), .en(En), .Q(PC_out), .clk(clk), .clr(rst));
  Register #(.width(1)) register_3 (.D(En), .en(1'b1), .Q(En_out), .clk(clk), .clr(tmp_rst));
endmodule

module ID_EX (
  input  [4:0] shamt,
  input  [31:0] JPC,
  input  syscall,
  input  [31:0] PC,
  input  RegWrite,
  input  beq,
  input  jal,
  input  [1:0] r1_sel,
  input  [31:0] Reg_A,
  input  MemtoReg,
  input  bne,
  input  jmp,
  input  [1:0] r2_sel,
  input  [31:0] Reg_B,
  input  [4:0] W_num,
  input  [3:0] ALUop,
  input  jr,
  input  srlv,
  input  MemWrite,
  input  ALUsrcB,
  input  [31:0] Imm,
  input  lbu,
  input  blez,
  input  En,
  input  clk,
  input  rst,
  input  tmp_rst,
  output [4:0] shamt_out,
  output [31:0] JPC_out,
  output syscall_out,
  output [31:0] PC_out,
  output RegWrite_out,
  output beq_out,
  output jal_out,
  output [1:0] r1_sel_out,
  output [31:0] Reg_A_out,
  output MemtoReg_out,
  output bne_out,
  output jmp_out,
  output [1:0] r2_sel_out,
  output [31:0] Reg_B_out,
  output [4:0] W__out,
  output [3:0] ALUop_out,
  output jr_out,
  output srlv_out,
  output MemWrite_out,
  output ALUsrcB_out,
  output [31:0] Imm_out,
  output lbu_out,
  output blez_out,
  output En_out
);

  wire multiplexer_7_out, multiplexer_8_out, multiplexer_10_out, multiplexer_11_out, multiplexer_12_out,
       multiplexer_13_out, multiplexer_15_out, multiplexer_16_out, multiplexer_17_out, multiplexer_18_out,
       multiplexer_19_out, multiplexer_22_out, multiplexer_23_out;
  wire [1:0] multiplexer_20_out, multiplexer_21_out;
  wire [3:0] multiplexer_14_out;
  wire [4:0] multiplexer_1_out, multiplexer_9_out;
  wire [31:0] multiplexer_2_out, multiplexer_3_out, multiplexer_4_out, multiplexer_5_out, multiplexer_6_out;

  Multiplexer #(.width(5), .enable("false")) multiplexer_1 (
    .in0(shamt), .in1({5{1'b0}}), .out(multiplexer_1_out), .sel(tmp_rst));
  Multiplexer #(.width(32), .enable("false")) multiplexer_2 (
    .in0(PC), .in1({32{1'b0}}), .out(multiplexer_2_out), .sel(tmp_rst));
  Multiplexer #(.width(32), .enable("false")) multiplexer_3 (
    .in0(Reg_A), .in1({32{1'b0}}), .out(multiplexer_3_out), .sel(tmp_rst));
  Multiplexer #(.width(32), .enable("false")) multiplexer_4 (
    .in0(Reg_B), .in1({32{1'b0}}), .out(multiplexer_4_out), .sel(tmp_rst));
  Multiplexer #(.width(32), .enable("false")) multiplexer_5 (
    .in0(Imm), .in1({32{1'b0}}), .out(multiplexer_5_out), .sel(tmp_rst));
  Register #(.width(5)) register_1 (.D(multiplexer_1_out), .en(En), .Q(shamt_out), .clk(clk), .clr(rst));
  Register #(.width(32)) register_2 (.D(multiplexer_2_out), .en(En), .Q(PC_out), .clk(clk), .clr(rst));
  Register #(.width(32)) register_3 (.D(multiplexer_3_out), .Q(Reg_A_out), .clk(clk), .clr(rst));  // open: en
  Register #(.width(32)) register_4 (.D(multiplexer_4_out), .en(En), .Q(Reg_B_out), .clk(clk), .clr(rst));
  Register #(.width(32)) register_5 (.D(multiplexer_5_out), .en(En), .Q(Imm_out), .clk(clk), .clr(rst));
  Register #(.width(1)) register_6 (.D(En), .en(1'b1), .Q(En_out), .clk(clk), .clr(rst));
  Multiplexer #(.width(32), .enable("false")) multiplexer_6 (
    .in0(JPC), .in1({32{1'b0}}), .out(multiplexer_6_out), .sel(tmp_rst));
  Multiplexer #(.enable("false")) multiplexer_7 (.in0(RegWrite), .in1(1'b0), .out(multiplexer_7_out), .sel(tmp_rst));
  Multiplexer #(.enable("false")) multiplexer_8 (.in0(MemtoReg), .in1(1'b0), .out(multiplexer_8_out), .sel(tmp_rst));
  Multiplexer #(.width(5), .enable("false")) multiplexer_9 (
    .in0(W_num), .in1({5{1'b0}}), .out(multiplexer_9_out), .sel(tmp_rst));
  Multiplexer #(.enable("false")) multiplexer_10 (.in0(MemWrite), .in1(1'b0), .out(multiplexer_10_out), .sel(tmp_rst));
  Register #(.width(32)) register_7 (.D(multiplexer_6_out), .en(En), .Q(JPC_out), .clk(clk));  // open: clr
  Register #(.width(1)) register_8 (.D(multiplexer_7_out), .en(En), .Q(RegWrite_out), .clk(clk), .clr(rst));
  Register #(.width(1)) register_9 (.D(multiplexer_8_out), .en(En), .Q(MemtoReg_out), .clk(clk), .clr(rst));
  Register #(.width(5)) register_10 (.D(multiplexer_9_out), .en(En), .Q(W__out), .clk(clk), .clr(rst));
  Register #(.width(1)) register_11 (.D(multiplexer_10_out), .en(En), .Q(MemWrite_out), .clk(clk), .clr(rst));
  Multiplexer #(.enable("false")) multiplexer_11 (.in0(syscall), .in1(1'b0), .out(multiplexer_11_out), .sel(tmp_rst));
  Multiplexer #(.enable("false")) multiplexer_12 (.in0(beq), .in1(1'b0), .out(multiplexer_12_out), .sel(tmp_rst));
  Multiplexer #(.enable("false")) multiplexer_13 (.in0(bne), .in1(1'b0), .out(multiplexer_13_out), .sel(tmp_rst));
  Multiplexer #(.width(4), .enable("false")) multiplexer_14 (
    .in0(ALUop), .in1(4'b0000), .out(multiplexer_14_out), .sel(tmp_rst));
  Multiplexer #(.enable("false")) multiplexer_15 (.in0(ALUsrcB), .in1(1'b0), .out(multiplexer_15_out), .sel(tmp_rst));
  Register #(.width(1)) register_12 (.D(multiplexer_11_out), .en(En), .Q(syscall_out), .clk(clk), .clr(rst));
  Register #(.width(1)) register_13 (.D(multiplexer_12_out), .en(En), .Q(beq_out), .clk(clk), .clr(rst));
  Register #(.width(1)) register_14 (.D(multiplexer_13_out), .en(En), .Q(bne_out), .clk(clk), .clr(rst));
  Register #(.width(4)) register_15 (.D(multiplexer_14_out), .en(En), .Q(ALUop_out), .clk(clk), .clr(rst));
  Register #(.width(1)) register_16 (.D(multiplexer_15_out), .en(En), .Q(ALUsrcB_out), .clk(clk), .clr(rst));
  Multiplexer #(.enable("false")) multiplexer_16 (.in0(jal), .in1(1'b0), .out(multiplexer_16_out), .sel(tmp_rst));
  Multiplexer #(.enable("false")) multiplexer_17 (.in0(jmp), .in1(1'b0), .out(multiplexer_17_out), .sel(tmp_rst));
  Multiplexer #(.enable("false")) multiplexer_18 (.in0(jr), .in1(1'b0), .out(multiplexer_18_out), .sel(tmp_rst));
  Multiplexer #(.enable("false")) multiplexer_19 (.in0(lbu), .in1(1'b0), .out(multiplexer_19_out), .sel(tmp_rst));
  Register #(.width(1)) register_17 (.D(multiplexer_16_out), .en(En), .Q(jal_out), .clk(clk), .clr(rst));
  Register #(.width(1)) register_18 (.D(multiplexer_17_out), .en(En), .Q(jmp_out), .clk(clk), .clr(rst));
  Register #(.width(1)) register_19 (.D(multiplexer_18_out), .en(En), .Q(jr_out), .clk(clk), .clr(rst));
  Register #(.width(1)) register_20 (.D(multiplexer_19_out), .en(En), .Q(lbu_out), .clk(clk), .clr(rst));
  Multiplexer #(.width(2), .enable("false")) multiplexer_20 (
    .in0(r1_sel), .in1(2'b00), .out(multiplexer_20_out), .sel(tmp_rst));
  Multiplexer #(.width(2), .enable("false")) multiplexer_21 (
    .in0(r2_sel), .in1(2'b00), .out(multiplexer_21_out), .sel(tmp_rst));
  Multiplexer #(.enable("false")) multiplexer_22 (.in0(srlv), .in1(1'b0), .out(multiplexer_22_out), .sel(tmp_rst));
  Multiplexer #(.enable("false")) multiplexer_23 (.in0(blez), .in1(1'b0), .out(multiplexer_23_out), .sel(tmp_rst));
  Register #(.width(2)) register_21 (.D(multiplexer_20_out), .en(En), .Q(r1_sel_out), .clk(clk), .clr(rst));
  Register #(.width(2)) register_22 (.D(multiplexer_21_out), .en(En), .Q(r2_sel_out), .clk(clk), .clr(rst));
  Register #(.width(1)) register_23 (.D(multiplexer_22_out), .en(En), .Q(srlv_out), .clk(clk), .clr(rst));
  Register #(.width(1)) register_24 (.D(multiplexer_23_out), .en(En), .Q(blez_out), .clk(clk), .clr(rst));

  // Other names for the same wires on the sheet: ALL_RST = rst; RST_t = tmp_rst
endmodule

module EX_MEM (
  input  [31:0] RegA,
  input  [31:0] PC,
  input  RegWrite,
  input  [31:0] ALU_Result,
  input  MemtoReg,
  input  syscall,
  input  [31:0] Reg_B,
  input  [4:0] W_num,
  input  MemWrite,
  input  lbu,
  input  Jal,
  input  En,
  input  clk,
  input  rst,
  output [31:0] RegA_out,
  output [31:0] PC_out,
  output RegWrite_out,
  output [31:0] ALU_Result_out,
  output MemtoReg_out,
  output syscall_out,
  output [31:0] Reg_B_out,
  output [4:0] W__out,
  output MemWrite_out,
  output lbu_out,
  output Jal_out,
  output En_out
);

  wire not_1_out;

  not not_1 (not_1_out, En);
  Register #(.width(32)) register_1 (.D(RegA), .en(not_1_out), .Q(RegA_out), .clk(clk), .clr(rst));
  Register #(.width(32)) register_2 (.D(PC), .en(not_1_out), .Q(PC_out), .clk(clk), .clr(rst));
  Register #(.width(32)) register_3 (.D(ALU_Result), .Q(ALU_Result_out), .clk(clk), .clr(rst));  // open: en
  Register #(.width(32)) register_4 (.D(Reg_B), .en(not_1_out), .Q(Reg_B_out), .clk(clk), .clr(rst));
  Register #(.width(1)) register_5 (.D(Jal), .en(not_1_out), .Q(Jal_out), .clk(clk), .clr(rst));
  Register #(.width(1)) register_6 (.D(not_1_out), .en(1'b1), .Q(En_out), .clk(clk), .clr(rst));
  Register #(.width(1)) register_7 (.D(RegWrite), .en(not_1_out), .Q(RegWrite_out), .clk(clk), .clr(rst));
  Register #(.width(1)) register_8 (.D(MemtoReg), .en(not_1_out), .Q(MemtoReg_out), .clk(clk), .clr(rst));
  Register #(.width(5)) register_9 (.D(W_num), .en(not_1_out), .Q(W__out), .clk(clk), .clr(rst));
  Register #(.width(1)) register_10 (.D(MemWrite), .en(not_1_out), .Q(MemWrite_out), .clk(clk), .clr(rst));
  Register #(.width(1)) register_11 (.D(syscall), .en(not_1_out), .Q(syscall_out), .clk(clk), .clr(rst));
  Register #(.width(1)) register_12 (.D(lbu), .en(not_1_out), .Q(lbu_out), .clk(clk), .clr(rst));
endmodule

module MEM_WB (
  input  syscall,
  input  [31:0] RegA,
  input  [31:0] PC,
  input  RegWrite,
  input  [31:0] ALU_Result,
  input  MemtoReg,
  input  [31:0] MemData,
  input  [4:0] W_num,
  input  Jal,
  input  [31:0] RegB,
  input  En,
  input  clk,
  input  rst,
  output syscall_out,
  output [31:0] RegA_out,
  output [31:0] PC_out,
  output RegWrite_out,
  output [31:0] ALU_Result_out,
  output MemtoReg_out,
  output [31:0] MemData_out,
  output [4:0] W__out,
  output Jal_out,
  output [31:0] RegB_out,
  output En_out
);

  wire not_1_out;

  not not_1 (not_1_out, En);
  Register #(.width(32)) register_1 (.D(RegA), .en(not_1_out), .Q(RegA_out), .clk(clk), .clr(rst));
  Register #(.width(32)) register_2 (.D(PC), .en(not_1_out), .Q(PC_out), .clk(clk), .clr(rst));
  Register #(.width(32)) register_3 (.D(ALU_Result), .Q(ALU_Result_out), .clk(clk), .clr(rst));  // open: en
  Register #(.width(32)) register_4 (.D(MemData), .en(not_1_out), .Q(MemData_out), .clk(clk), .clr(rst));
  Register #(.width(1)) register_5 (.D(Jal), .en(not_1_out), .Q(Jal_out), .clk(clk), .clr(rst));
  Register #(.width(1)) register_6 (.D(not_1_out), .en(1'b1), .Q(En_out), .clk(clk), .clr(rst));
  Register #(.width(1)) register_7 (.D(syscall), .en(not_1_out), .Q(syscall_out), .clk(clk), .clr(rst));
  Register #(.width(1)) register_8 (.D(RegWrite), .en(not_1_out), .Q(RegWrite_out), .clk(clk), .clr(rst));
  Register #(.width(1)) register_9 (.D(MemtoReg), .en(not_1_out), .Q(MemtoReg_out), .clk(clk), .clr(rst));
  Register #(.width(5)) register_10 (.D(W_num), .en(not_1_out), .Q(W__out), .clk(clk), .clr(rst));
  Register #(.width(32)) register_11 (.D(RegB), .en(not_1_out), .Q(RegB_out), .clk(clk), .clr(rst));
endmodule
// 源寄存器使用情况
module \源寄存器使用情况检测  (
  input  OP0,
  input  OP1,
  input  OP2,
  input  OP3,
  input  OP4,
  input  OP5,
  input  F0,
  input  F1,
  input  F2,
  input  F3,
  input  F4,
  input  F5,
  output R1_used,
  output R2_used
);

  wire and_1_out, and_2_out, and_3_out, and_4_out, and_5_out, and_6_out, and_7_out, and_8_out, and_9_out,
       and_10_out, and_11_out, and_12_out, and_13_out, and_14_out, and_15_out, and_16_out, and_17_out,
       and_18_out, and_19_out, and_20_out, and_21_out, and_22_out, and_23_out, and_24_out, and_25_out,
       and_26_out, and_27_out, and_28_out, and_29_out, and_30_out, and_31_out, and_32_out, and_33_out,
       and_34_out, and_35_out, and_36_out, and_37_out, and_38_out, and_39_out, and_40_out, and_41_out,
       and_42_out, and_43_out, and_44_out, and_45_out, and_46_out, and_47_out, and_48_out, and_49_out,
       and_50_out, and_51_out, and_52_out, and_53_out, and_54_out, and_55_out, and_56_out, and_57_out,
       and_58_out, and_59_out, and_60_out, and_61_out, and_62_out, and_63_out, and_64_out, and_65_out,
       and_66_out, and_67_out, and_68_out, and_69_out, and_70_out, and_71_out, and_72_out, and_73_out,
       and_74_out, and_75_out, and_76_out, and_77_out, and_78_out, and_79_out, and_80_out, and_81_out,
       and_82_out, and_83_out, and_84_out, and_85_out, and_86_out, and_87_out, and_88_out, and_89_out,
       and_90_out, and_91_out, and_92_out, and_93_out, and_94_out, and_95_out, and_96_out, and_97_out,
       and_98_out, and_99_out, and_100_out, and_101_out, and_102_out, and_103_out, and_104_out, and_105_out,
       and_106_out, and_107_out, and_108_out, and_109_out, and_110_out, and_111_out, and_112_out,
       and_113_out, and_114_out, and_115_out, and_116_out, and_117_out, and_118_out, and_119_out,
       and_120_out, and_121_out, and_122_out, and_123_out, and_124_out, and_125_out, and_126_out,
       and_127_out, and_128_out, not_1_out, not_2_out, not_3_out, not_4_out, not_5_out, not_6_out, not_7_out,
       not_8_out, not_9_out, not_10_out, not_11_out, not_12_out, not_13_out, not_14_out, not_15_out,
       not_16_out, not_17_out, not_18_out, not_19_out, not_20_out, not_21_out, not_22_out, not_23_out,
       not_24_out, not_25_out, not_26_out, not_27_out, not_28_out, not_29_out, not_30_out, not_31_out,
       not_32_out, not_33_out, not_34_out, not_35_out, not_36_out, not_37_out, not_38_out, not_39_out,
       not_40_out, not_41_out, not_42_out, not_43_out, not_44_out, not_45_out, not_46_out, not_47_out,
       not_48_out, not_49_out, not_50_out, not_51_out, not_52_out, not_53_out, not_54_out, not_55_out,
       not_56_out, not_57_out, not_58_out, not_59_out, not_60_out, not_61_out, not_62_out, not_63_out,
       not_64_out, not_65_out, not_66_out, not_67_out, not_68_out, not_69_out, not_70_out, not_71_out,
       not_72_out, not_73_out, not_74_out, not_75_out, not_76_out, not_77_out, not_78_out, not_79_out,
       not_80_out, not_81_out, not_82_out, not_83_out, not_84_out, not_85_out, not_86_out, not_87_out,
       not_88_out, not_89_out, not_90_out, not_91_out, not_92_out, not_93_out, not_94_out, not_95_out,
       not_96_out, not_97_out, not_98_out, not_99_out, not_100_out, not_101_out, not_102_out, not_103_out,
       not_104_out, not_105_out, not_106_out, not_107_out, not_108_out, not_109_out, not_110_out,
       not_111_out, not_112_out, not_113_out, not_114_out, not_115_out, not_116_out, not_117_out,
       not_118_out, not_119_out, not_120_out, not_121_out, not_122_out, not_123_out, not_124_out,
       not_125_out, not_126_out, not_127_out, not_128_out, not_129_out, not_130_out, not_131_out,
       not_132_out, not_133_out, not_134_out, not_135_out, not_136_out, not_137_out, not_138_out,
       not_139_out, not_140_out, not_141_out, not_142_out, not_143_out, not_144_out, not_145_out,
       not_146_out, not_147_out, not_148_out, not_149_out, not_150_out, not_151_out, not_152_out,
       not_153_out, not_154_out, not_155_out, not_156_out, not_157_out, not_158_out, not_159_out,
       not_160_out, not_161_out, not_162_out, not_163_out, not_164_out, not_165_out, not_166_out,
       not_167_out, not_168_out, not_169_out, not_170_out, not_171_out, not_172_out, not_173_out,
       not_174_out, not_175_out, not_176_out, not_177_out, not_178_out, not_179_out, not_180_out,
       not_181_out, not_182_out, not_183_out, not_184_out, not_185_out, not_186_out, not_187_out,
       not_188_out, not_189_out, not_190_out, not_191_out, not_192_out, not_193_out, not_194_out,
       not_195_out, not_196_out, not_197_out, not_198_out, not_199_out, not_200_out, not_201_out,
       not_202_out, not_203_out, not_204_out, not_205_out, not_206_out, not_207_out, not_208_out,
       not_209_out, not_210_out, not_211_out, not_212_out, not_213_out, not_214_out, not_215_out,
       not_216_out, not_217_out, not_218_out, not_219_out, not_220_out, not_221_out, not_222_out,
       not_223_out, not_224_out, not_225_out, not_226_out, not_227_out, not_228_out, not_229_out,
       not_230_out, not_231_out, not_232_out, not_233_out, not_234_out, not_235_out, not_236_out,
       not_237_out, not_238_out, not_239_out, not_240_out, not_241_out, not_242_out, not_243_out,
       not_244_out, not_245_out, not_246_out, not_247_out, not_248_out, not_249_out, not_250_out,
       not_251_out, not_252_out, not_253_out, not_254_out, not_255_out, not_256_out, not_257_out,
       not_258_out, not_259_out, not_260_out, not_261_out, not_262_out, not_263_out, not_264_out,
       not_265_out, not_266_out, not_267_out, not_268_out, not_269_out, not_270_out, not_271_out,
       not_272_out, not_273_out, not_274_out, not_275_out, not_276_out, not_277_out, not_278_out,
       not_279_out, not_280_out, not_281_out, not_282_out, not_283_out, not_284_out, not_285_out,
       not_286_out, not_287_out, not_288_out, not_289_out, not_290_out, not_291_out, not_292_out,
       not_293_out, not_294_out, not_295_out, not_296_out, not_297_out, not_298_out, not_299_out,
       not_300_out, not_301_out, not_302_out, not_303_out, not_304_out, not_305_out, not_306_out,
       not_307_out, not_308_out, not_309_out, not_310_out, not_311_out, not_312_out, not_313_out,
       not_314_out, not_315_out, not_316_out, not_317_out, not_318_out, not_319_out, not_320_out,
       not_321_out, not_322_out, not_323_out, not_324_out, not_325_out, not_326_out, not_327_out,
       not_328_out, not_329_out, not_330_out, not_331_out, not_332_out, not_333_out, not_334_out,
       not_335_out, not_336_out, not_337_out, not_338_out, not_339_out, not_340_out, not_341_out,
       not_342_out, not_343_out, not_344_out, not_345_out, not_346_out, not_347_out, not_348_out,
       not_349_out, not_350_out, not_351_out, not_352_out, not_353_out, not_354_out, not_355_out,
       not_356_out, not_357_out, not_358_out, not_359_out, not_360_out, not_361_out, not_362_out,
       not_363_out, not_364_out, not_365_out, not_366_out, not_367_out, not_368_out, not_369_out,
       not_370_out, not_371_out, not_372_out, not_373_out, not_374_out, not_375_out, not_376_out,
       not_377_out, not_378_out, not_379_out, not_380_out, not_381_out, not_382_out, not_383_out,
       not_384_out, not_385_out, not_386_out, not_387_out, not_388_out, not_389_out, not_390_out,
       not_391_out, not_392_out, not_393_out, not_394_out, not_395_out, not_396_out, not_397_out,
       not_398_out, not_399_out, not_400_out, not_401_out, not_402_out, not_403_out, not_404_out,
       not_405_out, not_406_out, not_407_out, not_408_out, not_409_out, not_410_out, not_411_out,
       not_412_out, not_413_out, not_414_out, not_415_out, not_416_out, not_417_out, not_418_out,
       not_419_out, not_420_out, not_421_out, not_422_out, not_423_out, not_424_out, not_425_out,
       not_426_out, not_427_out, not_428_out, not_429_out, not_430_out, not_431_out, not_432_out,
       not_433_out, not_434_out, not_435_out, not_436_out, not_437_out, not_438_out, not_439_out,
       not_440_out, not_441_out, not_442_out, not_443_out, not_444_out, not_445_out, not_446_out,
       not_447_out, not_448_out, not_449_out, not_450_out, not_451_out, not_452_out, not_453_out,
       not_454_out, not_455_out, not_456_out, not_457_out, not_458_out, not_459_out, not_460_out,
       not_461_out, not_462_out, not_463_out, not_464_out, not_465_out, not_466_out, not_467_out,
       not_468_out, not_469_out, not_470_out, not_471_out, not_472_out, not_473_out, not_474_out,
       not_475_out, not_476_out, not_477_out, not_478_out, not_479_out, not_480_out, not_481_out,
       not_482_out, not_483_out, not_484_out, not_485_out, not_486_out, not_487_out, not_488_out,
       not_489_out, not_490_out, not_491_out, not_492_out, not_493_out, not_494_out, not_495_out,
       not_496_out, not_497_out, not_498_out, not_499_out, not_500_out, not_501_out, not_502_out,
       not_503_out, not_504_out, not_505_out, not_506_out, not_507_out, not_508_out, not_509_out,
       not_510_out, not_511_out, not_512_out, not_513_out, not_514_out, not_515_out, not_516_out,
       not_517_out, not_518_out, not_519_out, not_520_out, not_521_out, not_522_out, not_523_out,
       not_524_out, not_525_out, not_526_out, not_527_out, not_528_out, not_529_out, not_530_out,
       not_531_out, not_532_out, not_533_out, not_534_out, not_535_out, not_536_out, not_537_out,
       not_538_out, not_539_out, not_540_out, not_541_out, not_542_out, not_543_out, not_544_out,
       not_545_out, not_546_out, not_547_out, not_548_out, not_549_out, not_550_out, not_551_out,
       not_552_out, not_553_out, not_554_out, not_555_out, not_556_out, not_557_out, not_558_out,
       not_559_out, not_560_out, not_561_out, not_562_out, not_563_out, not_564_out, not_565_out,
       not_566_out, not_567_out, not_568_out, not_569_out, not_570_out, not_571_out, not_572_out,
       not_573_out, not_574_out, not_575_out, not_576_out, not_577_out, not_578_out, not_579_out,
       not_580_out, not_581_out, not_582_out, not_583_out, not_584_out, not_585_out, not_586_out,
       not_587_out, not_588_out, not_589_out, not_590_out, not_591_out, not_592_out, not_593_out,
       not_594_out, not_595_out, not_596_out, not_597_out, not_598_out, not_599_out, not_600_out,
       not_601_out, not_602_out, not_603_out, not_604_out, not_605_out, not_606_out, not_607_out,
       not_608_out, not_609_out, not_610_out, not_611_out, not_612_out, not_613_out, not_614_out,
       not_615_out, not_616_out, not_617_out, not_618_out, not_619_out, not_620_out, not_621_out,
       not_622_out, not_623_out, not_624_out, not_625_out, not_626_out, not_627_out, not_628_out,
       not_629_out, not_630_out, not_631_out, not_632_out, not_633_out, not_634_out, not_635_out,
       not_636_out, not_637_out, not_638_out, not_639_out, not_640_out, not_641_out, not_642_out,
       not_643_out, not_644_out, not_645_out, not_646_out, not_647_out, not_648_out, not_649_out,
       not_650_out, not_651_out, not_652_out, not_653_out, not_654_out, not_655_out, not_656_out,
       not_657_out, not_658_out, not_659_out, not_660_out, not_661_out, not_662_out, not_663_out,
       not_664_out, not_665_out, not_666_out, not_667_out, not_668_out, not_669_out, not_670_out,
       not_671_out, not_672_out, not_673_out, not_674_out, not_675_out, not_676_out, not_677_out,
       not_678_out, not_679_out, not_680_out, not_681_out, not_682_out, not_683_out, not_684_out,
       not_685_out, not_686_out, not_687_out, not_688_out, not_689_out, not_690_out, not_691_out,
       not_692_out, not_693_out, not_694_out, not_695_out, not_696_out, not_697_out, not_698_out,
       not_699_out, not_700_out, not_701_out, not_702_out, not_703_out, not_704_out, not_705_out,
       not_706_out, not_707_out, not_708_out, not_709_out, not_710_out, not_711_out, not_712_out,
       not_713_out, not_714_out, not_715_out, not_716_out, not_717_out, not_718_out, not_719_out,
       not_720_out, not_721_out, not_722_out, not_723_out, not_724_out, not_725_out, not_726_out,
       not_727_out, not_728_out, not_729_out, not_730_out, not_731_out, not_732_out, not_733_out,
       not_734_out, not_735_out, not_736_out, not_737_out, not_738_out, not_739_out, not_740_out,
       not_741_out, not_742_out, not_743_out, not_744_out, not_745_out, not_746_out, not_747_out,
       not_748_out, not_749_out, not_750_out, not_751_out, not_752_out, not_753_out, not_754_out,
       not_755_out, not_756_out, not_757_out, not_758_out, not_759_out, not_760_out, not_761_out,
       not_762_out, not_763_out, not_764_out, not_765_out, not_766_out, not_767_out, not_768_out,
       not_769_out, not_770_out, not_771_out, not_772_out, not_773_out, not_774_out, not_775_out,
       not_776_out, not_777_out, not_778_out, not_779_out, not_780_out, not_781_out, not_782_out,
       not_783_out, not_784_out, not_785_out, not_786_out, not_787_out, not_788_out, not_789_out,
       not_790_out, not_791_out, not_792_out, not_793_out, not_794_out, not_795_out, not_796_out,
       not_797_out, not_798_out, not_799_out, not_800_out, not_801_out, not_802_out, not_803_out,
       not_804_out, not_805_out, not_806_out, not_807_out, not_808_out, not_809_out, not_810_out,
       not_811_out, not_812_out, not_813_out, not_814_out, not_815_out, not_816_out, not_817_out,
       not_818_out, not_819_out, not_820_out, not_821_out, not_822_out, not_823_out, not_824_out,
       not_825_out, not_826_out, not_827_out, not_828_out, not_829_out, not_830_out, not_831_out,
       not_832_out, not_833_out, not_834_out, not_835_out, not_836_out, not_837_out, not_838_out,
       not_839_out, not_840_out, not_841_out, not_842_out, not_843_out, not_844_out, not_845_out,
       not_846_out, not_847_out, not_848_out, not_849_out, not_850_out, not_851_out, not_852_out,
       not_853_out, not_854_out, not_855_out, not_856_out, not_857_out, not_858_out, not_859_out,
       not_860_out, not_861_out, not_862_out, not_863_out, not_864_out, not_865_out, not_866_out,
       not_867_out, not_868_out, not_869_out, not_870_out, not_871_out, not_872_out, not_873_out,
       not_874_out, not_875_out, not_876_out, not_877_out, not_878_out, not_879_out, not_880_out,
       not_881_out, not_882_out, not_883_out, not_884_out, not_885_out, not_886_out, not_887_out,
       not_888_out, not_889_out, not_890_out, not_891_out, not_892_out, not_893_out, not_894_out,
       not_895_out, not_896_out, not_897_out, not_898_out, not_899_out, not_900_out, not_901_out,
       not_902_out, not_903_out, not_904_out, not_905_out, not_906_out, not_907_out, not_908_out,
       not_909_out, not_910_out, not_911_out, not_912_out, not_913_out, not_914_out, not_915_out,
       not_916_out, not_917_out, not_918_out, not_919_out, not_920_out, not_921_out, not_922_out,
       not_923_out, not_924_out, not_925_out, not_926_out, not_927_out, not_928_out, not_929_out,
       not_930_out, not_931_out, not_932_out, not_933_out, or_2_out, or_3_out, or_4_out, or_5_out;

  not not_1 (not_1_out, OP5);
  not not_2 (not_2_out, OP4);
  not not_3 (not_3_out, OP3);
  not not_4 (not_4_out, OP2);
  not not_5 (not_5_out, OP1);
  not not_6 (not_6_out, OP0);
  not not_7 (not_7_out, F4);
  not not_8 (not_8_out, F3);
  not not_9 (not_9_out, F2);
  not not_10 (not_10_out, F1);
  not not_11 (not_11_out, F0);
  not not_12 (not_12_out, OP5);
  not not_13 (not_13_out, OP4);
  not not_14 (not_14_out, OP3);
  not not_15 (not_15_out, OP2);
  not not_16 (not_16_out, OP1);
  not not_17 (not_17_out, OP0);
  not not_18 (not_18_out, F4);
  not not_19 (not_19_out, F3);
  not not_20 (not_20_out, F2);
  not not_21 (not_21_out, F1);
  not not_22 (not_22_out, OP5);
  not not_23 (not_23_out, OP4);
  not not_24 (not_24_out, OP3);
  not not_25 (not_25_out, OP2);
  not not_26 (not_26_out, OP1);
  not not_27 (not_27_out, OP0);
  not not_28 (not_28_out, F4);
  not not_29 (not_29_out, F3);
  not not_30 (not_30_out, F2);
  not not_31 (not_31_out, F0);
  not not_32 (not_32_out, OP5);
  not not_33 (not_33_out, OP4);
  not not_34 (not_34_out, OP3);
  not not_35 (not_35_out, OP2);
  not not_36 (not_36_out, OP1);
  not not_37 (not_37_out, OP0);
  not not_38 (not_38_out, F4);
  not not_39 (not_39_out, F3);
  not not_40 (not_40_out, F1);
  not not_41 (not_41_out, F0);
  not not_42 (not_42_out, OP5);
  not not_43 (not_43_out, OP4);
  not not_44 (not_44_out, OP3);
  not not_45 (not_45_out, OP2);
  not not_46 (not_46_out, OP1);
  not not_47 (not_47_out, OP0);
  not not_48 (not_48_out, F4);
  not not_49 (not_49_out, F3);
  not not_50 (not_50_out, F1);
  not not_51 (not_51_out, OP5);
  not not_52 (not_52_out, OP4);
  not not_53 (not_53_out, OP3);
  not not_54 (not_54_out, OP2);
  not not_55 (not_55_out, OP1);
  not not_56 (not_56_out, OP0);
  not not_57 (not_57_out, F4);
  not not_58 (not_58_out, F3);
  not not_59 (not_59_out, OP5);
  not not_60 (not_60_out, OP4);
  not not_61 (not_61_out, OP3);
  not not_62 (not_62_out, OP2);
  not not_63 (not_63_out, OP1);
  not not_64 (not_64_out, OP0);
  not not_65 (not_65_out, F4);
  not not_66 (not_66_out, F2);
  not not_67 (not_67_out, F0);
  not not_68 (not_68_out, OP5);
  not not_69 (not_69_out, OP4);
  not not_70 (not_70_out, OP3);
  not not_71 (not_71_out, OP2);
  not not_72 (not_72_out, OP1);
  not not_73 (not_73_out, OP0);
  not not_74 (not_74_out, F4);
  not not_75 (not_75_out, F2);
  not not_76 (not_76_out, OP5);
  not not_77 (not_77_out, OP4);
  not not_78 (not_78_out, OP3);
  not not_79 (not_79_out, OP2);
  not not_80 (not_80_out, OP1);
  not not_81 (not_81_out, OP0);
  not not_82 (not_82_out, F5);
  not not_83 (not_83_out, F4);
  not not_84 (not_84_out, F2);
  not not_85 (not_85_out, F1);
  not not_86 (not_86_out, F0);
  not not_87 (not_87_out, OP5);
  not not_88 (not_88_out, OP4);
  not not_89 (not_89_out, OP3);
  not not_90 (not_90_out, OP2);
  not not_91 (not_91_out, OP1);
  not not_92 (not_92_out, OP0);
  not not_93 (not_93_out, F5);
  not not_94 (not_94_out, F4);
  not not_95 (not_95_out, F1);
  not not_96 (not_96_out, F0);
  not not_97 (not_97_out, OP5);
  not not_98 (not_98_out, OP4);
  not not_99 (not_99_out, OP3);
  not not_100 (not_100_out, OP1);
  not not_101 (not_101_out, OP0);
  not not_102 (not_102_out, OP5);
  not not_103 (not_103_out, OP4);
  not not_104 (not_104_out, OP3);
  not not_105 (not_105_out, OP1);
  not not_106 (not_106_out, OP5);
  not not_107 (not_107_out, OP4);
  not not_108 (not_108_out, OP2);
  not not_109 (not_109_out, OP1);
  not not_110 (not_110_out, OP0);
  not not_111 (not_111_out, OP5);
  not not_112 (not_112_out, OP4);
  not not_113 (not_113_out, OP1);
  not not_114 (not_114_out, OP0);
  not not_115 (not_115_out, OP5);
  not not_116 (not_116_out, OP4);
  not not_117 (not_117_out, OP2);
  not not_118 (not_118_out, OP1);
  not not_119 (not_119_out, OP5);
  not not_120 (not_120_out, OP4);
  not not_121 (not_121_out, OP2);
  not not_122 (not_122_out, OP0);
  not not_123 (not_123_out, OP5);
  not not_124 (not_124_out, OP4);
  not not_125 (not_125_out, OP1);
  not not_126 (not_126_out, OP4);
  not not_127 (not_127_out, OP3);
  not not_128 (not_128_out, OP2);
  not not_129 (not_129_out, OP4);
  not not_130 (not_130_out, OP2);
  not not_131 (not_131_out, OP5);
  not not_132 (not_132_out, OP4);
  not not_133 (not_133_out, OP3);
  not not_134 (not_134_out, OP2);
  not not_135 (not_135_out, OP1);
  not not_136 (not_136_out, OP0);
  not not_137 (not_137_out, F5);
  not not_138 (not_138_out, F4);
  not not_139 (not_139_out, F3);
  not not_140 (not_140_out, F0);
  not not_141 (not_141_out, OP5);
  not not_142 (not_142_out, OP4);
  not not_143 (not_143_out, OP3);
  not not_144 (not_144_out, OP2);
  not not_145 (not_145_out, OP1);
  not not_146 (not_146_out, OP0);
  not not_147 (not_147_out, F4);
  not not_148 (not_148_out, F3);
  not not_149 (not_149_out, F0);
  not not_150 (not_150_out, OP4);
  not not_151 (not_151_out, OP3);
  not not_152 (not_152_out, OP1);
  not not_153 (not_153_out, OP0);
  not not_154 (not_154_out, OP5);
  not not_155 (not_155_out, OP4);
  not not_156 (not_156_out, OP3);
  not not_157 (not_157_out, OP0);
  not not_158 (not_158_out, OP5);
  not not_159 (not_159_out, OP4);
  not not_160 (not_160_out, OP3);
  not not_161 (not_161_out, OP2);
  not not_162 (not_162_out, OP1);
  not not_163 (not_163_out, OP0);
  not not_164 (not_164_out, F4);
  not not_165 (not_165_out, F3);
  not not_166 (not_166_out, F2);
  not not_167 (not_167_out, F1);
  not not_168 (not_168_out, F0);
  not not_169 (not_169_out, OP5);
  not not_170 (not_170_out, OP4);
  not not_171 (not_171_out, OP3);
  not not_172 (not_172_out, OP2);
  not not_173 (not_173_out, OP1);
  not not_174 (not_174_out, OP0);
  not not_175 (not_175_out, F4);
  not not_176 (not_176_out, F3);
  not not_177 (not_177_out, F2);
  not not_178 (not_178_out, F1);
  not not_179 (not_179_out, OP5);
  not not_180 (not_180_out, OP4);
  not not_181 (not_181_out, OP3);
  not not_182 (not_182_out, OP2);
  not not_183 (not_183_out, OP1);
  not not_184 (not_184_out, OP0);
  not not_185 (not_185_out, F4);
  not not_186 (not_186_out, F3);
  not not_187 (not_187_out, F2);
  not not_188 (not_188_out, F0);
  not not_189 (not_189_out, OP5);
  not not_190 (not_190_out, OP4);
  not not_191 (not_191_out, OP3);
  not not_192 (not_192_out, OP2);
  not not_193 (not_193_out, OP1);
  not not_194 (not_194_out, OP0);
  not not_195 (not_195_out, F4);
  not not_196 (not_196_out, F3);
  not not_197 (not_197_out, F1);
  not not_198 (not_198_out, F0);
  not not_199 (not_199_out, OP5);
  not not_200 (not_200_out, OP4);
  not not_201 (not_201_out, OP3);
  not not_202 (not_202_out, OP2);
  not not_203 (not_203_out, OP1);
  not not_204 (not_204_out, OP0);
  not not_205 (not_205_out, F4);
  not not_206 (not_206_out, F3);
  not not_207 (not_207_out, F1);
  not not_208 (not_208_out, OP5);
  not not_209 (not_209_out, OP4);
  not not_210 (not_210_out, OP3);
  not not_211 (not_211_out, OP2);
  not not_212 (not_212_out, OP1);
  not not_213 (not_213_out, OP0);
  not not_214 (not_214_out, F4);
  not not_215 (not_215_out, F3);
  not not_216 (not_216_out, OP5);
  not not_217 (not_217_out, OP4);
  not not_218 (not_218_out, OP3);
  not not_219 (not_219_out, OP2);
  not not_220 (not_220_out, OP1);
  not not_221 (not_221_out, OP0);
  not not_222 (not_222_out, F4);
  not not_223 (not_223_out, F2);
  not not_224 (not_224_out, F0);
  not not_225 (not_225_out, OP5);
  not not_226 (not_226_out, OP4);
  not not_227 (not_227_out, OP3);
  not not_228 (not_228_out, OP2);
  not not_229 (not_229_out, OP1);
  not not_230 (not_230_out, OP0);
  not not_231 (not_231_out, F4);
  not not_232 (not_232_out, F2);
  not not_233 (not_233_out, OP5);
  not not_234 (not_234_out, OP4);
  not not_235 (not_235_out, OP3);
  not not_236 (not_236_out, OP2);
  not not_237 (not_237_out, OP1);
  not not_238 (not_238_out, OP0);
  not not_239 (not_239_out, F5);
  not not_240 (not_240_out, F4);
  not not_241 (not_241_out, F2);
  not not_242 (not_242_out, F1);
  not not_243 (not_243_out, F0);
  not not_244 (not_244_out, OP5);
  not not_245 (not_245_out, OP4);
  not not_246 (not_246_out, OP3);
  not not_247 (not_247_out, OP2);
  not not_248 (not_248_out, OP1);
  not not_249 (not_249_out, OP0);
  not not_250 (not_250_out, F5);
  not not_251 (not_251_out, F4);
  not not_252 (not_252_out, F1);
  not not_253 (not_253_out, F0);
  not not_254 (not_254_out, OP5);
  not not_255 (not_255_out, OP4);
  not not_256 (not_256_out, OP3);
  not not_257 (not_257_out, OP1);
  not not_258 (not_258_out, OP0);
  not not_259 (not_259_out, OP5);
  not not_260 (not_260_out, OP4);
  not not_261 (not_261_out, OP3);
  not not_262 (not_262_out, OP1);
  not not_263 (not_263_out, OP5);
  not not_264 (not_264_out, OP4);
  not not_265 (not_265_out, OP2);
  not not_266 (not_266_out, OP1);
  not not_267 (not_267_out, OP0);
  not not_268 (not_268_out, OP5);
  not not_269 (not_269_out, OP4);
  not not_270 (not_270_out, OP1);
  not not_271 (not_271_out, OP0);
  not not_272 (not_272_out, OP5);
  not not_273 (not_273_out, OP4);
  not not_274 (not_274_out, OP2);
  not not_275 (not_275_out, OP1);
  not not_276 (not_276_out, OP5);
  not not_277 (not_277_out, OP4);
  not not_278 (not_278_out, OP2);
  not not_279 (not_279_out, OP0);
  not not_280 (not_280_out, OP5);
  not not_281 (not_281_out, OP4);
  not not_282 (not_282_out, OP1);
  not not_283 (not_283_out, OP4);
  not not_284 (not_284_out, OP3);
  not not_285 (not_285_out, OP2);
  not not_286 (not_286_out, OP4);
  not not_287 (not_287_out, OP2);
  not not_288 (not_288_out, OP5);
  not not_289 (not_289_out, OP4);
  not not_290 (not_290_out, OP3);
  not not_291 (not_291_out, OP2);
  not not_292 (not_292_out, OP1);
  not not_293 (not_293_out, OP0);
  not not_294 (not_294_out, F5);
  not not_295 (not_295_out, F4);
  not not_296 (not_296_out, F3);
  not not_297 (not_297_out, F0);
  not not_298 (not_298_out, OP5);
  not not_299 (not_299_out, OP4);
  not not_300 (not_300_out, OP3);
  not not_301 (not_301_out, OP2);
  not not_302 (not_302_out, OP1);
  not not_303 (not_303_out, OP0);
  not not_304 (not_304_out, F4);
  not not_305 (not_305_out, F3);
  not not_306 (not_306_out, F0);
  not not_307 (not_307_out, OP4);
  not not_308 (not_308_out, OP3);
  not not_309 (not_309_out, OP1);
  not not_310 (not_310_out, OP0);
  not not_311 (not_311_out, OP5);
  not not_312 (not_312_out, OP4);
  not not_313 (not_313_out, OP3);
  not not_314 (not_314_out, OP0);
  not not_315 (not_315_out, OP5);
  not not_316 (not_316_out, OP4);
  not not_317 (not_317_out, OP3);
  not not_318 (not_318_out, OP2);
  not not_319 (not_319_out, OP1);
  not not_320 (not_320_out, OP0);
  not not_321 (not_321_out, F4);
  not not_322 (not_322_out, F3);
  not not_323 (not_323_out, F2);
  not not_324 (not_324_out, F1);
  not not_325 (not_325_out, F0);
  not not_326 (not_326_out, OP5);
  not not_327 (not_327_out, OP4);
  not not_328 (not_328_out, OP3);
  not not_329 (not_329_out, OP2);
  not not_330 (not_330_out, OP1);
  not not_331 (not_331_out, OP0);
  not not_332 (not_332_out, F4);
  not not_333 (not_333_out, F3);
  not not_334 (not_334_out, F2);
  not not_335 (not_335_out, F1);
  not not_336 (not_336_out, OP5);
  not not_337 (not_337_out, OP4);
  not not_338 (not_338_out, OP3);
  not not_339 (not_339_out, OP2);
  not not_340 (not_340_out, OP1);
  not not_341 (not_341_out, OP0);
  not not_342 (not_342_out, F4);
  not not_343 (not_343_out, F3);
  not not_344 (not_344_out, F2);
  not not_345 (not_345_out, F0);
  not not_346 (not_346_out, OP5);
  not not_347 (not_347_out, OP4);
  not not_348 (not_348_out, OP3);
  not not_349 (not_349_out, OP2);
  not not_350 (not_350_out, OP1);
  not not_351 (not_351_out, OP0);
  not not_352 (not_352_out, F4);
  not not_353 (not_353_out, F3);
  not not_354 (not_354_out, F1);
  not not_355 (not_355_out, F0);
  not not_356 (not_356_out, OP5);
  not not_357 (not_357_out, OP4);
  not not_358 (not_358_out, OP3);
  not not_359 (not_359_out, OP2);
  not not_360 (not_360_out, OP1);
  not not_361 (not_361_out, OP0);
  not not_362 (not_362_out, F4);
  not not_363 (not_363_out, F3);
  not not_364 (not_364_out, F1);
  not not_365 (not_365_out, OP5);
  not not_366 (not_366_out, OP4);
  not not_367 (not_367_out, OP3);
  not not_368 (not_368_out, OP2);
  not not_369 (not_369_out, OP1);
  not not_370 (not_370_out, OP0);
  not not_371 (not_371_out, F4);
  not not_372 (not_372_out, F3);
  not not_373 (not_373_out, OP5);
  not not_374 (not_374_out, OP4);
  not not_375 (not_375_out, OP3);
  not not_376 (not_376_out, OP2);
  not not_377 (not_377_out, OP1);
  not not_378 (not_378_out, OP0);
  not not_379 (not_379_out, F4);
  not not_380 (not_380_out, F2);
  not not_381 (not_381_out, F0);
  not not_382 (not_382_out, OP5);
  not not_383 (not_383_out, OP4);
  not not_384 (not_384_out, OP3);
  not not_385 (not_385_out, OP2);
  not not_386 (not_386_out, OP1);
  not not_387 (not_387_out, OP0);
  not not_388 (not_388_out, F4);
  not not_389 (not_389_out, F2);
  not not_390 (not_390_out, OP5);
  not not_391 (not_391_out, OP4);
  not not_392 (not_392_out, OP3);
  not not_393 (not_393_out, OP2);
  not not_394 (not_394_out, OP1);
  not not_395 (not_395_out, OP0);
  not not_396 (not_396_out, F5);
  not not_397 (not_397_out, F4);
  not not_398 (not_398_out, F2);
  not not_399 (not_399_out, F1);
  not not_400 (not_400_out, F0);
  not not_401 (not_401_out, OP5);
  not not_402 (not_402_out, OP4);
  not not_403 (not_403_out, OP3);
  not not_404 (not_404_out, OP2);
  not not_405 (not_405_out, OP1);
  not not_406 (not_406_out, OP0);
  not not_407 (not_407_out, F5);
  not not_408 (not_408_out, F4);
  not not_409 (not_409_out, F1);
  not not_410 (not_410_out, F0);
  not not_411 (not_411_out, OP5);
  not not_412 (not_412_out, OP4);
  not not_413 (not_413_out, OP3);
  not not_414 (not_414_out, OP1);
  not not_415 (not_415_out, OP0);
  not not_416 (not_416_out, OP5);
  not not_417 (not_417_out, OP4);
  not not_418 (not_418_out, OP3);
  not not_419 (not_419_out, OP1);
  not not_420 (not_420_out, OP5);
  not not_421 (not_421_out, OP4);
  not not_422 (not_422_out, OP2);
  not not_423 (not_423_out, OP1);
  not not_424 (not_424_out, OP0);
  not not_425 (not_425_out, OP5);
  not not_426 (not_426_out, OP4);
  not not_427 (not_427_out, OP1);
  not not_428 (not_428_out, OP0);
  not not_429 (not_429_out, OP5);
  not not_430 (not_430_out, OP4);
  not not_431 (not_431_out, OP2);
  not not_432 (not_432_out, OP1);
  not not_433 (not_433_out, OP5);
  not not_434 (not_434_out, OP4);
  not not_435 (not_435_out, OP2);
  not not_436 (not_436_out, OP0);
  not not_437 (not_437_out, OP5);
  not not_438 (not_438_out, OP4);
  not not_439 (not_439_out, OP1);
  not not_440 (not_440_out, OP4);
  not not_441 (not_441_out, OP3);
  not not_442 (not_442_out, OP2);
  not not_443 (not_443_out, OP4);
  not not_444 (not_444_out, OP2);
  not not_445 (not_445_out, OP5);
  not not_446 (not_446_out, OP4);
  not not_447 (not_447_out, OP3);
  not not_448 (not_448_out, OP2);
  not not_449 (not_449_out, OP1);
  not not_450 (not_450_out, OP0);
  not not_451 (not_451_out, F5);
  not not_452 (not_452_out, F4);
  not not_453 (not_453_out, F3);
  not not_454 (not_454_out, F0);
  not not_455 (not_455_out, OP5);
  not not_456 (not_456_out, OP4);
  not not_457 (not_457_out, OP3);
  not not_458 (not_458_out, OP2);
  not not_459 (not_459_out, OP1);
  not not_460 (not_460_out, OP0);
  not not_461 (not_461_out, F4);
  not not_462 (not_462_out, F3);
  not not_463 (not_463_out, F0);
  not not_464 (not_464_out, OP4);
  not not_465 (not_465_out, OP3);
  not not_466 (not_466_out, OP1);
  not not_467 (not_467_out, OP0);
  not not_468 (not_468_out, OP5);
  not not_469 (not_469_out, OP4);
  not not_470 (not_470_out, OP3);
  not not_471 (not_471_out, OP0);
  not not_472 (not_472_out, OP5);
  not not_473 (not_473_out, OP4);
  not not_474 (not_474_out, OP3);
  not not_475 (not_475_out, OP2);
  not not_476 (not_476_out, OP1);
  not not_477 (not_477_out, OP0);
  not not_478 (not_478_out, F4);
  not not_479 (not_479_out, F3);
  not not_480 (not_480_out, F2);
  not not_481 (not_481_out, F1);
  not not_482 (not_482_out, F0);
  not not_483 (not_483_out, OP5);
  not not_484 (not_484_out, OP4);
  not not_485 (not_485_out, OP3);
  not not_486 (not_486_out, OP2);
  not not_487 (not_487_out, OP1);
  not not_488 (not_488_out, OP0);
  not not_489 (not_489_out, F4);
  not not_490 (not_490_out, F3);
  not not_491 (not_491_out, F2);
  not not_492 (not_492_out, F1);
  not not_493 (not_493_out, OP5);
  not not_494 (not_494_out, OP4);
  not not_495 (not_495_out, OP3);
  not not_496 (not_496_out, OP2);
  not not_497 (not_497_out, OP1);
  not not_498 (not_498_out, OP0);
  not not_499 (not_499_out, F4);
  not not_500 (not_500_out, F3);
  not not_501 (not_501_out, F2);
  not not_502 (not_502_out, F0);
  not not_503 (not_503_out, OP5);
  not not_504 (not_504_out, OP4);
  not not_505 (not_505_out, OP3);
  not not_506 (not_506_out, OP2);
  not not_507 (not_507_out, OP1);
  not not_508 (not_508_out, OP0);
  not not_509 (not_509_out, F4);
  not not_510 (not_510_out, F3);
  not not_511 (not_511_out, F1);
  not not_512 (not_512_out, F0);
  not not_513 (not_513_out, OP5);
  not not_514 (not_514_out, OP4);
  not not_515 (not_515_out, OP3);
  not not_516 (not_516_out, OP2);
  not not_517 (not_517_out, OP1);
  not not_518 (not_518_out, OP0);
  not not_519 (not_519_out, F4);
  not not_520 (not_520_out, F3);
  not not_521 (not_521_out, F1);
  not not_522 (not_522_out, OP5);
  not not_523 (not_523_out, OP4);
  not not_524 (not_524_out, OP3);
  not not_525 (not_525_out, OP2);
  not not_526 (not_526_out, OP1);
  not not_527 (not_527_out, OP0);
  not not_528 (not_528_out, F4);
  not not_529 (not_529_out, F3);
  not not_530 (not_530_out, OP5);
  not not_531 (not_531_out, OP4);
  not not_532 (not_532_out, OP3);
  not not_533 (not_533_out, OP2);
  not not_534 (not_534_out, OP1);
  not not_535 (not_535_out, OP0);
  not not_536 (not_536_out, F4);
  not not_537 (not_537_out, F2);
  not not_538 (not_538_out, F0);
  not not_539 (not_539_out, OP5);
  not not_540 (not_540_out, OP4);
  not not_541 (not_541_out, OP3);
  not not_542 (not_542_out, OP2);
  not not_543 (not_543_out, OP1);
  not not_544 (not_544_out, OP0);
  not not_545 (not_545_out, F4);
  not not_546 (not_546_out, F2);
  not not_547 (not_547_out, OP5);
  not not_548 (not_548_out, OP4);
  not not_549 (not_549_out, OP3);
  not not_550 (not_550_out, OP2);
  not not_551 (not_551_out, OP1);
  not not_552 (not_552_out, OP0);
  not not_553 (not_553_out, F5);
  not not_554 (not_554_out, F4);
  not not_555 (not_555_out, F2);
  not not_556 (not_556_out, F1);
  not not_557 (not_557_out, F0);
  not not_558 (not_558_out, OP5);
  not not_559 (not_559_out, OP4);
  not not_560 (not_560_out, OP3);
  not not_561 (not_561_out, OP2);
  not not_562 (not_562_out, OP1);
  not not_563 (not_563_out, OP0);
  not not_564 (not_564_out, F5);
  not not_565 (not_565_out, F4);
  not not_566 (not_566_out, F1);
  not not_567 (not_567_out, F0);
  not not_568 (not_568_out, OP5);
  not not_569 (not_569_out, OP4);
  not not_570 (not_570_out, OP3);
  not not_571 (not_571_out, OP1);
  not not_572 (not_572_out, OP0);
  not not_573 (not_573_out, OP5);
  not not_574 (not_574_out, OP4);
  not not_575 (not_575_out, OP3);
  not not_576 (not_576_out, OP1);
  not not_577 (not_577_out, OP5);
  not not_578 (not_578_out, OP4);
  not not_579 (not_579_out, OP2);
  not not_580 (not_580_out, OP1);
  not not_581 (not_581_out, OP0);
  not not_582 (not_582_out, OP5);
  not not_583 (not_583_out, OP4);
  not not_584 (not_584_out, OP1);
  not not_585 (not_585_out, OP0);
  not not_586 (not_586_out, OP5);
  not not_587 (not_587_out, OP4);
  not not_588 (not_588_out, OP2);
  not not_589 (not_589_out, OP1);
  not not_590 (not_590_out, OP5);
  not not_591 (not_591_out, OP4);
  not not_592 (not_592_out, OP2);
  not not_593 (not_593_out, OP0);
  not not_594 (not_594_out, OP5);
  not not_595 (not_595_out, OP4);
  not not_596 (not_596_out, OP1);
  not not_597 (not_597_out, OP4);
  not not_598 (not_598_out, OP3);
  not not_599 (not_599_out, OP2);
  not not_600 (not_600_out, OP4);
  not not_601 (not_601_out, OP2);
  not not_602 (not_602_out, OP5);
  not not_603 (not_603_out, OP4);
  not not_604 (not_604_out, OP3);
  not not_605 (not_605_out, OP2);
  not not_606 (not_606_out, OP1);
  not not_607 (not_607_out, OP0);
  not not_608 (not_608_out, F5);
  not not_609 (not_609_out, F4);
  not not_610 (not_610_out, F3);
  not not_611 (not_611_out, F0);
  not not_612 (not_612_out, OP5);
  not not_613 (not_613_out, OP4);
  not not_614 (not_614_out, OP3);
  not not_615 (not_615_out, OP2);
  not not_616 (not_616_out, OP1);
  not not_617 (not_617_out, OP0);
  not not_618 (not_618_out, F4);
  not not_619 (not_619_out, F3);
  not not_620 (not_620_out, F0);
  not not_621 (not_621_out, OP4);
  not not_622 (not_622_out, OP3);
  not not_623 (not_623_out, OP1);
  not not_624 (not_624_out, OP0);
  not not_625 (not_625_out, OP5);
  not not_626 (not_626_out, OP4);
  not not_627 (not_627_out, OP3);
  not not_628 (not_628_out, OP0);
  not not_629 (not_629_out, OP5);
  not not_630 (not_630_out, OP4);
  not not_631 (not_631_out, OP3);
  not not_632 (not_632_out, OP2);
  not not_633 (not_633_out, OP1);
  not not_634 (not_634_out, OP0);
  not not_635 (not_635_out, F4);
  not not_636 (not_636_out, F3);
  not not_637 (not_637_out, F2);
  not not_638 (not_638_out, F1);
  not not_639 (not_639_out, F0);
  not not_640 (not_640_out, OP5);
  not not_641 (not_641_out, OP4);
  not not_642 (not_642_out, OP3);
  not not_643 (not_643_out, OP2);
  not not_644 (not_644_out, OP1);
  not not_645 (not_645_out, OP0);
  not not_646 (not_646_out, F4);
  not not_647 (not_647_out, F3);
  not not_648 (not_648_out, F2);
  not not_649 (not_649_out, F1);
  not not_650 (not_650_out, OP5);
  not not_651 (not_651_out, OP4);
  not not_652 (not_652_out, OP3);
  not not_653 (not_653_out, OP2);
  not not_654 (not_654_out, OP1);
  not not_655 (not_655_out, OP0);
  not not_656 (not_656_out, F4);
  not not_657 (not_657_out, F3);
  not not_658 (not_658_out, F2);
  not not_659 (not_659_out, F0);
  not not_660 (not_660_out, OP5);
  not not_661 (not_661_out, OP4);
  not not_662 (not_662_out, OP3);
  not not_663 (not_663_out, OP2);
  not not_664 (not_664_out, OP1);
  not not_665 (not_665_out, OP0);
  not not_666 (not_666_out, F4);
  not not_667 (not_667_out, F3);
  not not_668 (not_668_out, F1);
  not not_669 (not_669_out, F0);
  not not_670 (not_670_out, OP5);
  not not_671 (not_671_out, OP4);
  not not_672 (not_672_out, OP3);
  not not_673 (not_673_out, OP2);
  not not_674 (not_674_out, OP1);
  not not_675 (not_675_out, OP0);
  not not_676 (not_676_out, F4);
  not not_677 (not_677_out, F3);
  not not_678 (not_678_out, F1);
  not not_679 (not_679_out, OP5);
  not not_680 (not_680_out, OP4);
  not not_681 (not_681_out, OP3);
  not not_682 (not_682_out, OP2);
  not not_683 (not_683_out, OP1);
  not not_684 (not_684_out, OP0);
  not not_685 (not_685_out, F4);
  not not_686 (not_686_out, F3);
  not not_687 (not_687_out, OP5);
  not not_688 (not_688_out, OP4);
  not not_689 (not_689_out, OP3);
  not not_690 (not_690_out, OP2);
  not not_691 (not_691_out, OP1);
  not not_692 (not_692_out, OP0);
  not not_693 (not_693_out, F4);
  not not_694 (not_694_out, F2);
  not not_695 (not_695_out, F0);
  not not_696 (not_696_out, OP5);
  not not_697 (not_697_out, OP4);
  not not_698 (not_698_out, OP3);
  not not_699 (not_699_out, OP2);
  not not_700 (not_700_out, OP1);
  not not_701 (not_701_out, OP0);
  not not_702 (not_702_out, F4);
  not not_703 (not_703_out, F2);
  not not_704 (not_704_out, OP5);
  not not_705 (not_705_out, OP4);
  not not_706 (not_706_out, OP3);
  not not_707 (not_707_out, OP2);
  not not_708 (not_708_out, OP1);
  not not_709 (not_709_out, OP0);
  not not_710 (not_710_out, F5);
  not not_711 (not_711_out, F4);
  not not_712 (not_712_out, F2);
  not not_713 (not_713_out, F1);
  not not_714 (not_714_out, F0);
  not not_715 (not_715_out, OP5);
  not not_716 (not_716_out, OP4);
  not not_717 (not_717_out, OP3);
  not not_718 (not_718_out, OP2);
  not not_719 (not_719_out, OP1);
  not not_720 (not_720_out, OP0);
  not not_721 (not_721_out, F5);
  not not_722 (not_722_out, F4);
  not not_723 (not_723_out, F1);
  not not_724 (not_724_out, F0);
  not not_725 (not_725_out, OP5);
  not not_726 (not_726_out, OP4);
  not not_727 (not_727_out, OP3);
  not not_728 (not_728_out, OP1);
  not not_729 (not_729_out, OP0);
  not not_730 (not_730_out, OP5);
  not not_731 (not_731_out, OP4);
  not not_732 (not_732_out, OP3);
  not not_733 (not_733_out, OP1);
  not not_734 (not_734_out, OP5);
  not not_735 (not_735_out, OP4);
  not not_736 (not_736_out, OP2);
  not not_737 (not_737_out, OP1);
  not not_738 (not_738_out, OP0);
  not not_739 (not_739_out, OP5);
  not not_740 (not_740_out, OP4);
  not not_741 (not_741_out, OP1);
  not not_742 (not_742_out, OP0);
  not not_743 (not_743_out, OP5);
  not not_744 (not_744_out, OP4);
  not not_745 (not_745_out, OP2);
  not not_746 (not_746_out, OP1);
  not not_747 (not_747_out, OP5);
  not not_748 (not_748_out, OP4);
  not not_749 (not_749_out, OP2);
  not not_750 (not_750_out, OP0);
  not not_751 (not_751_out, OP5);
  not not_752 (not_752_out, OP4);
  not not_753 (not_753_out, OP1);
  not not_754 (not_754_out, OP4);
  not not_755 (not_755_out, OP3);
  not not_756 (not_756_out, OP2);
  not not_757 (not_757_out, OP4);
  not not_758 (not_758_out, OP2);
  not not_759 (not_759_out, OP5);
  not not_760 (not_760_out, OP4);
  not not_761 (not_761_out, OP3);
  not not_762 (not_762_out, OP2);
  not not_763 (not_763_out, OP1);
  not not_764 (not_764_out, OP0);
  not not_765 (not_765_out, F5);
  not not_766 (not_766_out, F4);
  not not_767 (not_767_out, F3);
  not not_768 (not_768_out, F0);
  not not_769 (not_769_out, OP5);
  not not_770 (not_770_out, OP4);
  not not_771 (not_771_out, OP3);
  not not_772 (not_772_out, OP2);
  not not_773 (not_773_out, OP1);
  not not_774 (not_774_out, OP0);
  not not_775 (not_775_out, F4);
  not not_776 (not_776_out, F3);
  not not_777 (not_777_out, F0);
  not not_778 (not_778_out, OP4);
  not not_779 (not_779_out, OP3);
  not not_780 (not_780_out, OP1);
  not not_781 (not_781_out, OP0);
  not not_782 (not_782_out, OP5);
  not not_783 (not_783_out, OP4);
  not not_784 (not_784_out, OP3);
  not not_785 (not_785_out, OP0);
  not not_786 (not_786_out, OP5);
  not not_787 (not_787_out, OP4);
  not not_788 (not_788_out, OP3);
  not not_789 (not_789_out, OP2);
  not not_790 (not_790_out, OP1);
  not not_791 (not_791_out, OP0);
  not not_792 (not_792_out, F5);
  not not_793 (not_793_out, F4);
  not not_794 (not_794_out, F3);
  not not_795 (not_795_out, F2);
  not not_796 (not_796_out, F1);
  not not_797 (not_797_out, F0);
  not not_798 (not_798_out, OP5);
  not not_799 (not_799_out, OP4);
  not not_800 (not_800_out, OP3);
  not not_801 (not_801_out, OP2);
  not not_802 (not_802_out, OP1);
  not not_803 (not_803_out, OP0);
  not not_804 (not_804_out, F5);
  not not_805 (not_805_out, F4);
  not not_806 (not_806_out, F3);
  not not_807 (not_807_out, F2);
  not not_808 (not_808_out, OP5);
  not not_809 (not_809_out, OP4);
  not not_810 (not_810_out, OP3);
  not not_811 (not_811_out, OP2);
  not not_812 (not_812_out, OP1);
  not not_813 (not_813_out, OP0);
  not not_814 (not_814_out, F5);
  not not_815 (not_815_out, F4);
  not not_816 (not_816_out, F3);
  not not_817 (not_817_out, F2);
  not not_818 (not_818_out, F0);
  not not_819 (not_819_out, OP5);
  not not_820 (not_820_out, OP4);
  not not_821 (not_821_out, OP3);
  not not_822 (not_822_out, OP2);
  not not_823 (not_823_out, OP1);
  not not_824 (not_824_out, OP0);
  not not_825 (not_825_out, F4);
  not not_826 (not_826_out, F3);
  not not_827 (not_827_out, F2);
  not not_828 (not_828_out, F1);
  not not_829 (not_829_out, F0);
  not not_830 (not_830_out, OP5);
  not not_831 (not_831_out, OP4);
  not not_832 (not_832_out, OP3);
  not not_833 (not_833_out, OP2);
  not not_834 (not_834_out, OP1);
  not not_835 (not_835_out, OP0);
  not not_836 (not_836_out, F4);
  not not_837 (not_837_out, F3);
  not not_838 (not_838_out, F2);
  not not_839 (not_839_out, F1);
  not not_840 (not_840_out, OP5);
  not not_841 (not_841_out, OP4);
  not not_842 (not_842_out, OP3);
  not not_843 (not_843_out, OP2);
  not not_844 (not_844_out, OP1);
  not not_845 (not_845_out, OP0);
  not not_846 (not_846_out, F4);
  not not_847 (not_847_out, F3);
  not not_848 (not_848_out, F2);
  not not_849 (not_849_out, F0);
  not not_850 (not_850_out, OP5);
  not not_851 (not_851_out, OP4);
  not not_852 (not_852_out, OP3);
  not not_853 (not_853_out, OP2);
  not not_854 (not_854_out, OP1);
  not not_855 (not_855_out, OP0);
  not not_856 (not_856_out, F4);
  not not_857 (not_857_out, F3);
  not not_858 (not_858_out, F1);
  not not_859 (not_859_out, F0);
  not not_860 (not_860_out, OP5);
  not not_861 (not_861_out, OP4);
  not not_862 (not_862_out, OP3);
  not not_863 (not_863_out, OP2);
  not not_864 (not_864_out, OP1);
  not not_865 (not_865_out, OP0);
  not not_866 (not_866_out, F4);
  not not_867 (not_867_out, F3);
  not not_868 (not_868_out, F1);
  not not_869 (not_869_out, OP5);
  not not_870 (not_870_out, OP4);
  not not_871 (not_871_out, OP3);
  not not_872 (not_872_out, OP2);
  not not_873 (not_873_out, OP1);
  not not_874 (not_874_out, OP0);
  not not_875 (not_875_out, F4);
  not not_876 (not_876_out, F3);
  not not_877 (not_877_out, OP5);
  not not_878 (not_878_out, OP4);
  not not_879 (not_879_out, OP3);
  not not_880 (not_880_out, OP2);
  not not_881 (not_881_out, OP1);
  not not_882 (not_882_out, OP0);
  not not_883 (not_883_out, F4);
  not not_884 (not_884_out, F2);
  not not_885 (not_885_out, F0);
  not not_886 (not_886_out, OP5);
  not not_887 (not_887_out, OP4);
  not not_888 (not_888_out, OP3);
  not not_889 (not_889_out, OP2);
  not not_890 (not_890_out, OP1);
  not not_891 (not_891_out, OP0);
  not not_892 (not_892_out, F4);
  not not_893 (not_893_out, F2);
  not not_894 (not_894_out, OP5);
  not not_895 (not_895_out, OP4);
  not not_896 (not_896_out, OP3);
  not not_897 (not_897_out, OP2);
  not not_898 (not_898_out, OP1);
  not not_899 (not_899_out, OP0);
  not not_900 (not_900_out, F5);
  not not_901 (not_901_out, F4);
  not not_902 (not_902_out, F1);
  not not_903 (not_903_out, F0);
  not not_904 (not_904_out, OP5);
  not not_905 (not_905_out, OP4);
  not not_906 (not_906_out, OP3);
  not not_907 (not_907_out, OP1);
  not not_908 (not_908_out, OP0);
  not not_909 (not_909_out, OP5);
  not not_910 (not_910_out, OP4);
  not not_911 (not_911_out, OP3);
  not not_912 (not_912_out, OP1);
  not not_913 (not_913_out, OP4);
  not not_914 (not_914_out, OP2);
  not not_915 (not_915_out, OP5);
  not not_916 (not_916_out, OP4);
  not not_917 (not_917_out, OP3);
  not not_918 (not_918_out, OP2);
  not not_919 (not_919_out, OP1);
  not not_920 (not_920_out, OP0);
  not not_921 (not_921_out, F5);
  not not_922 (not_922_out, F4);
  not not_923 (not_923_out, F3);
  not not_924 (not_924_out, F0);
  not not_925 (not_925_out, OP5);
  not not_926 (not_926_out, OP4);
  not not_927 (not_927_out, OP3);
  not not_928 (not_928_out, OP2);
  not not_929 (not_929_out, OP1);
  not not_930 (not_930_out, OP0);
  not not_931 (not_931_out, F4);
  not not_932 (not_932_out, F3);
  not not_933 (not_933_out, F0);
  and and_1 (and_1_out, not_1_out, not_2_out, not_3_out, not_4_out, not_5_out, not_6_out, F5, not_7_out, not_8_out, not_9_out, not_10_out, not_11_out);
  and and_2 (and_2_out, not_12_out, not_13_out, not_14_out, not_15_out, not_16_out, not_17_out, F5, not_18_out, not_19_out, not_20_out, not_21_out, F0);
  and and_3 (and_3_out, not_22_out, not_23_out, not_24_out, not_25_out, not_26_out, not_27_out, F5, not_28_out, not_29_out, not_30_out, F1, not_31_out);
  and and_4 (and_4_out, not_32_out, not_33_out, not_34_out, not_35_out, not_36_out, not_37_out, F5, not_38_out, not_39_out, F2, not_40_out, not_41_out);
  and and_5 (and_5_out, not_42_out, not_43_out, not_44_out, not_45_out, not_46_out, not_47_out, F5, not_48_out, not_49_out, F2, not_50_out, F0);
  and and_6 (and_6_out, not_51_out, not_52_out, not_53_out, not_54_out, not_55_out, not_56_out, F5, not_57_out, not_58_out, F2, F1, F0);
  and and_7 (and_7_out, not_59_out, not_60_out, not_61_out, not_62_out, not_63_out, not_64_out, F5, not_65_out, F3, not_66_out, F1, not_67_out);
  and and_8 (and_8_out, not_68_out, not_69_out, not_70_out, not_71_out, not_72_out, not_73_out, F5, not_74_out, F3, not_75_out, F1, F0);
  and and_9 (and_9_out, not_76_out, not_77_out, not_78_out, not_79_out, not_80_out, not_81_out, not_82_out, not_83_out, F3, not_84_out, not_85_out, not_86_out);
  and and_10 (and_10_out, not_87_out, not_88_out, not_89_out, not_90_out, not_91_out, not_92_out, not_93_out, not_94_out, F3, F2, not_95_out, not_96_out);
  and and_11 (and_11_out, not_97_out, not_98_out, not_99_out, OP2, not_100_out, not_101_out);
  and and_12 (and_12_out, not_102_out, not_103_out, not_104_out, OP2, not_105_out, OP0);
  and and_13 (and_13_out, not_106_out, not_107_out, OP3, not_108_out, not_109_out, not_110_out);
  and and_14 (and_14_out, not_111_out, not_112_out, OP3, OP2, not_113_out, not_114_out);
  and and_15 (and_15_out, not_115_out, not_116_out, OP3, not_117_out, not_118_out, OP0);
  and and_16 (and_16_out, not_119_out, not_120_out, OP3, not_121_out, OP1, not_122_out);
  and and_17 (and_17_out, not_123_out, not_124_out, OP3, OP2, not_125_out, OP0);
  and and_18 (and_18_out, OP5, not_126_out, not_127_out, not_128_out, OP1, OP0);
  and and_19 (and_19_out, OP5, not_129_out, OP3, not_130_out, OP1, OP0);
  and and_20 (and_20_out, not_131_out, not_132_out, not_133_out, not_134_out, not_135_out, not_136_out, not_137_out, not_138_out, not_139_out, F2, F1, not_140_out);
  and and_21 (and_21_out, not_141_out, not_142_out, not_143_out, not_144_out, not_145_out, not_146_out, F5, not_147_out, not_148_out, F2, F1, not_149_out);
  and and_22 (and_22_out, OP5, not_150_out, not_151_out, OP2, not_152_out, not_153_out);
  and and_23 (and_23_out, not_154_out, not_155_out, not_156_out, OP2, OP1, not_157_out, not_158_out, not_159_out, not_160_out, not_161_out, not_162_out, not_163_out, F5, not_164_out, not_165_out, not_166_out, not_167_out, not_168_out);
  and and_24 (and_24_out, not_169_out, not_170_out, not_171_out, not_172_out, not_173_out, not_174_out, F5, not_175_out, not_176_out, not_177_out, not_178_out, F0);
  and and_25 (and_25_out, not_179_out, not_180_out, not_181_out, not_182_out, not_183_out, not_184_out, F5, not_185_out, not_186_out, not_187_out, F1, not_188_out);
  and and_26 (and_26_out, not_189_out, not_190_out, not_191_out, not_192_out, not_193_out, not_194_out, F5, not_195_out, not_196_out, F2, not_197_out, not_198_out);
  and and_27 (and_27_out, not_199_out, not_200_out, not_201_out, not_202_out, not_203_out, not_204_out, F5, not_205_out, not_206_out, F2, not_207_out, F0);
  and and_28 (and_28_out, not_208_out, not_209_out, not_210_out, not_211_out, not_212_out, not_213_out, F5, not_214_out, not_215_out, F2, F1, F0);
  and and_29 (and_29_out, not_216_out, not_217_out, not_218_out, not_219_out, not_220_out, not_221_out, F5, not_222_out, F3, not_223_out, F1, not_224_out);
  and and_30 (and_30_out, not_225_out, not_226_out, not_227_out, not_228_out, not_229_out, not_230_out, F5, not_231_out, F3, not_232_out, F1, F0);
  and and_31 (and_31_out, not_233_out, not_234_out, not_235_out, not_236_out, not_237_out, not_238_out, not_239_out, not_240_out, F3, not_241_out, not_242_out, not_243_out);
  and and_32 (and_32_out, not_244_out, not_245_out, not_246_out, not_247_out, not_248_out, not_249_out, not_250_out, not_251_out, F3, F2, not_252_out, not_253_out);
  and and_33 (and_33_out, not_254_out, not_255_out, not_256_out, OP2, not_257_out, not_258_out);
  and and_34 (and_34_out, not_259_out, not_260_out, not_261_out, OP2, not_262_out, OP0);
  and and_35 (and_35_out, not_263_out, not_264_out, OP3, not_265_out, not_266_out, not_267_out);
  and and_36 (and_36_out, not_268_out, not_269_out, OP3, OP2, not_270_out, not_271_out);
  and and_37 (and_37_out, not_272_out, not_273_out, OP3, not_274_out, not_275_out, OP0);
  and and_38 (and_38_out, not_276_out, not_277_out, OP3, not_278_out, OP1, not_279_out);
  and and_39 (and_39_out, not_280_out, not_281_out, OP3, OP2, not_282_out, OP0);
  and and_40 (and_40_out, OP5, not_283_out, not_284_out, not_285_out, OP1, OP0);
  and and_41 (and_41_out, OP5, not_286_out, OP3, not_287_out, OP1, OP0);
  and and_42 (and_42_out, not_288_out, not_289_out, not_290_out, not_291_out, not_292_out, not_293_out, not_294_out, not_295_out, not_296_out, F2, F1, not_297_out);
  and and_43 (and_43_out, not_298_out, not_299_out, not_300_out, not_301_out, not_302_out, not_303_out, F5, not_304_out, not_305_out, F2, F1, not_306_out);
  and and_44 (and_44_out, OP5, not_307_out, not_308_out, OP2, not_309_out, not_310_out);
  and and_45 (and_45_out, not_311_out, not_312_out, not_313_out, OP2, OP1, not_314_out, not_315_out, not_316_out, not_317_out, not_318_out, not_319_out, not_320_out, F5, not_321_out, not_322_out, not_323_out, not_324_out, not_325_out);
  and and_46 (and_46_out, not_326_out, not_327_out, not_328_out, not_329_out, not_330_out, not_331_out, F5, not_332_out, not_333_out, not_334_out, not_335_out, F0);
  and and_47 (and_47_out, not_336_out, not_337_out, not_338_out, not_339_out, not_340_out, not_341_out, F5, not_342_out, not_343_out, not_344_out, F1, not_345_out);
  and and_48 (and_48_out, not_346_out, not_347_out, not_348_out, not_349_out, not_350_out, not_351_out, F5, not_352_out, not_353_out, F2, not_354_out, not_355_out);
  and and_49 (and_49_out, not_356_out, not_357_out, not_358_out, not_359_out, not_360_out, not_361_out, F5, not_362_out, not_363_out, F2, not_364_out, F0);
  and and_50 (and_50_out, not_365_out, not_366_out, not_367_out, not_368_out, not_369_out, not_370_out, F5, not_371_out, not_372_out, F2, F1, F0);
  and and_51 (and_51_out, not_373_out, not_374_out, not_375_out, not_376_out, not_377_out, not_378_out, F5, not_379_out, F3, not_380_out, F1, not_381_out);
  and and_52 (and_52_out, not_382_out, not_383_out, not_384_out, not_385_out, not_386_out, not_387_out, F5, not_388_out, F3, not_389_out, F1, F0);
  and and_53 (and_53_out, not_390_out, not_391_out, not_392_out, not_393_out, not_394_out, not_395_out, not_396_out, not_397_out, F3, not_398_out, not_399_out, not_400_out);
  and and_54 (and_54_out, not_401_out, not_402_out, not_403_out, not_404_out, not_405_out, not_406_out, not_407_out, not_408_out, F3, F2, not_409_out, not_410_out);
  and and_55 (and_55_out, not_411_out, not_412_out, not_413_out, OP2, not_414_out, not_415_out);
  and and_56 (and_56_out, not_416_out, not_417_out, not_418_out, OP2, not_419_out, OP0);
  and and_57 (and_57_out, not_420_out, not_421_out, OP3, not_422_out, not_423_out, not_424_out);
  and and_58 (and_58_out, not_425_out, not_426_out, OP3, OP2, not_427_out, not_428_out);
  and and_59 (and_59_out, not_429_out, not_430_out, OP3, not_431_out, not_432_out, OP0);
  and and_60 (and_60_out, not_433_out, not_434_out, OP3, not_435_out, OP1, not_436_out);
  and and_61 (and_61_out, not_437_out, not_438_out, OP3, OP2, not_439_out, OP0);
  and and_62 (and_62_out, OP5, not_440_out, not_441_out, not_442_out, OP1, OP0);
  and and_63 (and_63_out, OP5, not_443_out, OP3, not_444_out, OP1, OP0);
  and and_64 (and_64_out, not_445_out, not_446_out, not_447_out, not_448_out, not_449_out, not_450_out, not_451_out, not_452_out, not_453_out, F2, F1, not_454_out);
  and and_65 (and_65_out, not_455_out, not_456_out, not_457_out, not_458_out, not_459_out, not_460_out, F5, not_461_out, not_462_out, F2, F1, not_463_out);
  and and_66 (and_66_out, OP5, not_464_out, not_465_out, OP2, not_466_out, not_467_out);
  and and_67 (and_67_out, not_468_out, not_469_out, not_470_out, OP2, OP1, not_471_out, not_472_out, not_473_out, not_474_out, not_475_out, not_476_out, not_477_out, F5, not_478_out, not_479_out, not_480_out, not_481_out, not_482_out);
  and and_68 (and_68_out, not_483_out, not_484_out, not_485_out, not_486_out, not_487_out, not_488_out, F5, not_489_out, not_490_out, not_491_out, not_492_out, F0);
  and and_69 (and_69_out, not_493_out, not_494_out, not_495_out, not_496_out, not_497_out, not_498_out, F5, not_499_out, not_500_out, not_501_out, F1, not_502_out);
  and and_70 (and_70_out, not_503_out, not_504_out, not_505_out, not_506_out, not_507_out, not_508_out, F5, not_509_out, not_510_out, F2, not_511_out, not_512_out);
  and and_71 (and_71_out, not_513_out, not_514_out, not_515_out, not_516_out, not_517_out, not_518_out, F5, not_519_out, not_520_out, F2, not_521_out, F0);
  and and_72 (and_72_out, not_522_out, not_523_out, not_524_out, not_525_out, not_526_out, not_527_out, F5, not_528_out, not_529_out, F2, F1, F0);
  and and_73 (and_73_out, not_530_out, not_531_out, not_532_out, not_533_out, not_534_out, not_535_out, F5, not_536_out, F3, not_537_out, F1, not_538_out);
  and and_74 (and_74_out, not_539_out, not_540_out, not_541_out, not_542_out, not_543_out, not_544_out, F5, not_545_out, F3, not_546_out, F1, F0);
  and and_75 (and_75_out, not_547_out, not_548_out, not_549_out, not_550_out, not_551_out, not_552_out, not_553_out, not_554_out, F3, not_555_out, not_556_out, not_557_out);
  and and_76 (and_76_out, not_558_out, not_559_out, not_560_out, not_561_out, not_562_out, not_563_out, not_564_out, not_565_out, F3, F2, not_566_out, not_567_out);
  and and_77 (and_77_out, not_568_out, not_569_out, not_570_out, OP2, not_571_out, not_572_out);
  and and_78 (and_78_out, not_573_out, not_574_out, not_575_out, OP2, not_576_out, OP0);
  and and_79 (and_79_out, not_577_out, not_578_out, OP3, not_579_out, not_580_out, not_581_out);
  and and_80 (and_80_out, not_582_out, not_583_out, OP3, OP2, not_584_out, not_585_out);
  and and_81 (and_81_out, not_586_out, not_587_out, OP3, not_588_out, not_589_out, OP0);
  and and_82 (and_82_out, not_590_out, not_591_out, OP3, not_592_out, OP1, not_593_out);
  and and_83 (and_83_out, not_594_out, not_595_out, OP3, OP2, not_596_out, OP0);
  and and_84 (and_84_out, OP5, not_597_out, not_598_out, not_599_out, OP1, OP0);
  and and_85 (and_85_out, not_786_out, not_787_out, not_788_out, not_789_out, not_790_out, not_791_out, not_792_out, not_793_out, not_794_out, not_795_out, not_796_out, not_797_out);
  and and_86 (and_86_out, not_798_out, not_799_out, not_800_out, not_801_out, not_802_out, not_803_out, not_804_out, not_805_out, not_806_out, not_807_out, F1, F0);
  and and_87 (and_87_out, not_808_out, not_809_out, not_810_out, not_811_out, not_812_out, not_813_out, not_814_out, not_815_out, not_816_out, not_817_out, F1, not_818_out);
  and and_88 (and_88_out, not_819_out, not_820_out, not_821_out, not_822_out, not_823_out, not_824_out, F5, not_825_out, not_826_out, not_827_out, not_828_out, not_829_out);
  and and_89 (and_89_out, not_830_out, not_831_out, not_832_out, not_833_out, not_834_out, not_835_out, F5, not_836_out, not_837_out, not_838_out, not_839_out, F0);
  and and_90 (and_90_out, not_840_out, not_841_out, not_842_out, not_843_out, not_844_out, not_845_out, F5, not_846_out, not_847_out, not_848_out, F1, not_849_out);
  and and_91 (and_91_out, not_850_out, not_851_out, not_852_out, not_853_out, not_854_out, not_855_out, F5, not_856_out, not_857_out, F2, not_858_out, not_859_out);
  and and_92 (and_92_out, not_860_out, not_861_out, not_862_out, not_863_out, not_864_out, not_865_out, F5, not_866_out, not_867_out, F2, not_868_out, F0);
  and and_93 (and_93_out, not_869_out, not_870_out, not_871_out, not_872_out, not_873_out, not_874_out, F5, not_875_out, not_876_out, F2, F1, F0);
  and and_94 (and_94_out, not_877_out, not_878_out, not_879_out, not_880_out, not_881_out, not_882_out, F5, not_883_out, F3, not_884_out, F1, not_885_out);
  and and_95 (and_95_out, not_886_out, not_887_out, not_888_out, not_889_out, not_890_out, not_891_out, F5, not_892_out, F3, not_893_out, F1, F0);
  and and_96 (and_96_out, not_894_out, not_895_out, not_896_out, not_897_out, not_898_out, not_899_out, not_900_out, not_901_out, F3, F2, not_902_out, not_903_out);
  and and_97 (and_97_out, not_904_out, not_905_out, not_906_out, OP2, not_907_out, not_908_out);
  and and_98 (and_98_out, not_909_out, not_910_out, not_911_out, OP2, not_912_out, OP0);
  and and_99 (and_99_out, OP5, not_913_out, OP3, not_914_out, OP1, OP0);
  and and_100 (and_100_out, not_915_out, not_916_out, not_917_out, not_918_out, not_919_out, not_920_out, not_921_out, not_922_out, not_923_out, F2, F1, not_924_out);
  and and_101 (and_101_out, not_925_out, not_926_out, not_927_out, not_928_out, not_929_out, not_930_out, F5, not_931_out, not_932_out, F2, F1, not_933_out);
  and and_102 (and_102_out, OP5, not_600_out, OP3, not_601_out, OP1, OP0);
  and and_103 (and_103_out, not_602_out, not_603_out, not_604_out, not_605_out, not_606_out, not_607_out, not_608_out, not_609_out, not_610_out, F2, F1, not_611_out);
  and and_104 (and_104_out, not_612_out, not_613_out, not_614_out, not_615_out, not_616_out, not_617_out, F5, not_618_out, not_619_out, F2, F1, not_620_out);
  and and_105 (and_105_out, OP5, not_621_out, not_622_out, OP2, not_623_out, not_624_out);
  and and_106 (and_106_out, not_625_out, not_626_out, not_627_out, OP2, OP1, not_628_out, not_629_out, not_630_out, not_631_out, not_632_out, not_633_out, not_634_out, F5, not_635_out, not_636_out, not_637_out, not_638_out, not_639_out);
  and and_107 (and_107_out, not_640_out, not_641_out, not_642_out, not_643_out, not_644_out, not_645_out, F5, not_646_out, not_647_out, not_648_out, not_649_out, F0);
  and and_108 (and_108_out, not_650_out, not_651_out, not_652_out, not_653_out, not_654_out, not_655_out, F5, not_656_out, not_657_out, not_658_out, F1, not_659_out);
  and and_109 (and_109_out, not_660_out, not_661_out, not_662_out, not_663_out, not_664_out, not_665_out, F5, not_666_out, not_667_out, F2, not_668_out, not_669_out);
  and and_110 (and_110_out, not_670_out, not_671_out, not_672_out, not_673_out, not_674_out, not_675_out, F5, not_676_out, not_677_out, F2, not_678_out, F0);
  and and_111 (and_111_out, not_679_out, not_680_out, not_681_out, not_682_out, not_683_out, not_684_out, F5, not_685_out, not_686_out, F2, F1, F0);
  and and_112 (and_112_out, not_687_out, not_688_out, not_689_out, not_690_out, not_691_out, not_692_out, F5, not_693_out, F3, not_694_out, F1, not_695_out);
  and and_113 (and_113_out, not_696_out, not_697_out, not_698_out, not_699_out, not_700_out, not_701_out, F5, not_702_out, F3, not_703_out, F1, F0);
  and and_114 (and_114_out, not_704_out, not_705_out, not_706_out, not_707_out, not_708_out, not_709_out, not_710_out, not_711_out, F3, not_712_out, not_713_out, not_714_out);
  and and_115 (and_115_out, not_715_out, not_716_out, not_717_out, not_718_out, not_719_out, not_720_out, not_721_out, not_722_out, F3, F2, not_723_out, not_724_out);
  and and_116 (and_116_out, not_725_out, not_726_out, not_727_out, OP2, not_728_out, not_729_out);
  and and_117 (and_117_out, not_730_out, not_731_out, not_732_out, OP2, not_733_out, OP0);
  and and_118 (and_118_out, not_734_out, not_735_out, OP3, not_736_out, not_737_out, not_738_out);
  and and_119 (and_119_out, not_739_out, not_740_out, OP3, OP2, not_741_out, not_742_out);
  and and_120 (and_120_out, not_743_out, not_744_out, OP3, not_745_out, not_746_out, OP0);
  and and_121 (and_121_out, not_747_out, not_748_out, OP3, not_749_out, OP1, not_750_out);
  and and_122 (and_122_out, not_751_out, not_752_out, OP3, OP2, not_753_out, OP0);
  and and_123 (and_123_out, OP5, not_754_out, not_755_out, not_756_out, OP1, OP0);
  and and_124 (and_124_out, OP5, not_757_out, OP3, not_758_out, OP1, OP0);
  and and_125 (and_125_out, not_759_out, not_760_out, not_761_out, not_762_out, not_763_out, not_764_out, not_765_out, not_766_out, not_767_out, F2, F1, not_768_out);
  and and_126 (and_126_out, not_769_out, not_770_out, not_771_out, not_772_out, not_773_out, not_774_out, F5, not_775_out, not_776_out, F2, F1, not_777_out);
  and and_127 (and_127_out, OP5, not_778_out, not_779_out, OP2, not_780_out, not_781_out);
  and and_128 (and_128_out, not_782_out, not_783_out, not_784_out, OP2, OP1, not_785_out);
  or or_1 (R2_used, and_85_out, and_86_out, and_87_out, and_88_out, and_89_out, and_90_out, and_91_out, and_92_out, and_93_out, and_94_out, and_95_out, and_96_out, and_97_out, and_98_out, and_99_out, and_100_out, and_101_out);
  or or_2 (or_2_out, and_1_out, and_2_out, and_3_out, and_4_out, and_5_out, and_6_out, and_7_out, and_8_out, and_9_out, and_10_out, and_11_out, and_12_out, and_13_out, and_14_out, and_15_out, and_16_out, and_17_out, and_18_out, and_19_out, and_20_out, and_21_out, and_22_out, and_23_out, and_24_out, and_25_out, and_26_out, and_27_out, and_28_out);
  or or_3 (or_3_out, and_29_out, and_30_out, and_31_out, and_32_out, and_33_out, and_34_out, and_35_out, and_36_out, and_37_out, and_38_out, and_39_out, and_40_out, and_41_out, and_42_out, and_43_out, and_44_out, and_45_out, and_46_out, and_47_out, and_48_out, and_49_out, and_50_out, and_51_out, and_52_out, and_53_out, and_54_out, and_55_out, and_56_out);
  or or_4 (or_4_out, and_57_out, and_58_out, and_59_out, and_60_out, and_61_out, and_62_out, and_63_out, and_64_out, and_65_out, and_66_out, and_67_out, and_68_out, and_69_out, and_70_out, and_71_out, and_72_out, and_73_out, and_74_out, and_75_out, and_76_out, and_77_out, and_78_out, and_79_out, and_80_out, and_81_out, and_82_out, and_83_out, and_84_out);
  or or_5 (or_5_out, and_102_out, and_103_out, and_104_out, and_105_out, and_106_out, and_107_out, and_108_out, and_109_out, and_110_out, and_111_out, and_112_out, and_113_out, and_114_out, and_115_out, and_116_out, and_117_out, and_118_out, and_119_out, and_120_out, and_121_out, and_122_out, and_123_out, and_124_out, and_125_out, and_126_out, and_127_out, and_128_out);
  or or_6 (R1_used, or_2_out, or_3_out, or_4_out, or_5_out);
endmodule

module \数据相关检测  (
  input  R1_Used,
  input  R2_Used,
  input  EX_RegWrite,
  input  MEM_RegWrite,
  input  [4:0] R1_num,
  input  [4:0] R2_num,
  input  [4:0] EX_WriteReg_num,
  input  [4:0] MEM_WriteReg_num,
  output R1_EX_Related,
  output R2_EX_Related,
  output R1_MEM_Related,
  output R2_MEM_Related
);

  wire and_1_out, and_2_out, and_3_out, and_4_out, comparator_1_eq, comparator_2_eq, comparator_3_eq,
       comparator_4_eq, comparator_5_eq, comparator_6_eq;

  Comparator #(.width(5)) comparator_1 (.a(R1_num), .b({5{1'b0}}), .eq(comparator_1_eq));  // open: gt, lt
  Comparator #(.width(5)) comparator_2 (.a({5{1'b0}}), .b(R2_num), .eq(comparator_2_eq));  // open: gt, lt
  Comparator #(.width(5)) comparator_3 (.a(R1_num), .b(EX_WriteReg_num), .eq(comparator_3_eq));  // open: gt, lt
  Comparator #(.width(5)) comparator_4 (.a(R2_num), .b(EX_WriteReg_num), .eq(comparator_4_eq));  // open: gt, lt
  Comparator #(.width(5)) comparator_5 (.a(R1_num), .b(MEM_WriteReg_num), .eq(comparator_5_eq));  // open: gt, lt
  Comparator #(.width(5)) comparator_6 (.a(R2_num), .b(MEM_WriteReg_num), .eq(comparator_6_eq));  // open: gt, lt
  and and_1 (and_1_out, EX_RegWrite, comparator_3_eq);
  and and_2 (and_2_out, EX_RegWrite, comparator_4_eq);
  and and_3 (and_3_out, MEM_RegWrite, comparator_5_eq);
  and and_4 (and_4_out, MEM_RegWrite, comparator_6_eq);
  and and_5 (R1_EX_Related, R1_Used, ~comparator_1_eq, and_1_out);  // AND_Gate
  and and_6 (R2_EX_Related, R2_Used, ~comparator_2_eq, and_2_out);  // AND_Gate
  and and_7 (R1_MEM_Related, R1_Used, ~comparator_1_eq, and_3_out);  // AND_Gate
  and and_8 (R2_MEM_Related, R2_Used, ~comparator_2_eq, and_4_out);  // AND_Gate
endmodule

module \CCMB控制信号生成  (
  input  OP0,
  input  OP1,
  input  OP2,
  input  OP3,
  input  OP4,
  input  OP5,
  input  F0,
  input  F1,
  input  F2,
  input  F3,
  input  F4,
  input  F5,
  output SRLV,
  output LBU,
  output BLEZ
);

  wire not_1_out, not_2_out, not_3_out, not_4_out, not_5_out, not_6_out, not_7_out, not_8_out, not_9_out,
       not_10_out, not_11_out, not_12_out, not_13_out, not_14_out, not_15_out, not_16_out, not_17_out,
       not_18_out;

  not not_1 (not_1_out, OP5);
  not not_2 (not_2_out, OP4);
  not not_3 (not_3_out, OP3);
  not not_4 (not_4_out, OP2);
  not not_5 (not_5_out, OP1);
  not not_6 (not_6_out, OP0);
  not not_7 (not_7_out, F5);
  not not_8 (not_8_out, F4);
  not not_9 (not_9_out, F3);
  not not_10 (not_10_out, F0);
  not not_11 (not_11_out, OP4);
  not not_12 (not_12_out, OP3);
  not not_13 (not_13_out, OP1);
  not not_14 (not_14_out, OP0);
  not not_15 (not_15_out, OP5);
  not not_16 (not_16_out, OP4);
  not not_17 (not_17_out, OP3);
  not not_18 (not_18_out, OP0);
  and and_1 (SRLV, not_1_out, not_2_out, not_3_out, not_4_out, not_5_out, not_6_out, not_7_out, not_8_out, not_9_out, F2, F1, not_10_out);
  and and_2 (LBU, OP5, not_11_out, not_12_out, OP2, not_13_out, not_14_out);
  and and_3 (BLEZ, not_15_out, not_16_out, not_17_out, OP2, OP1, not_18_out);
endmodule

module bypass_total (
);

  wire and_1_out, and_2_out, and_4_out, and_6_out, and_7_out, and_8_out, BLEZ, branch_hazard, CLK,
       comparator_1_eq, con_if, ex_mem_1_jal_out, ex_mem_1_memtoreg_out, ex_mem_1_memwrite_out, Ex_MtR,
       EX_Wt, Go, HALT, id_ex_1_alusrcb_out, id_ex_1_beq_out, id_ex_1_blez_out, id_ex_1_bne_out,
       id_ex_1_memwrite_out, IR1, IR2, IR3, JAL, JAL_EX, JMP, JMP_EX, JR, JR_EX, LBU, LBU_EX, LBU_MEM,
       LoadUse, mem_wb_1_jal_out, mem_wb_1_memtoreg_out, mem_wb_1_regwrite_out, Mem_Wt, mips_alu_1_equal,
       or_2_out, or_3_out, or_4_out, or_5_out, or_6_out, or_8_out, R1_EX_Hazard, R1_Mem_Hazard, R1_Used,
       R2_EX_Hazard, R2_Mem_Hazard, R2_Used, RST, SignedExt, SRLV, SRLV_EX, Syscall, Syscall_EX, Syscall_Mem,
       Syscall_WB, uncon_if, W1, W2, W3, \硬布线控制器_1_alu_src , \硬布线控制器_1_beq , \硬布线控制器_1_bne ,
       \硬布线控制器_1_memtoreg , \硬布线控制器_1_memwrite , \硬布线控制器_1_regdst , \硬布线控制器_1_regwrite ;
  wire [0:0] or_1_out;
  wire [1:0] R1_sel, R2_sel;
  wire [3:0] id_ex_1_aluop_out, \硬布线控制器_1_alu_op ;
  wire [4:0] Ex_Wt_num, id_ex_1_shamt_out, if_id_1_ir_out_2, Mem_Wt_num, multiplexer_4_out,
       multiplexer_5_out, multiplexer_8_out, R1_num, R2_num, WB_num;
  wire [15:0] \总周期数 , \插入气泡数 , \无条件分支数 , \条件分支成功数 ;
  wire [31:0] AluResult2, and_9_out, and_10_out, and_11_out, and_12_out, b_pc, bit_extender_1_out,
       bit_extender_2_out, bit_extender_3_out, EX_DATA, ex_mem_1_reg_b_out, EX_PC, EX_RD1_in, EX_RD1_out,
       EX_RD2_in, EX_RD2_out, id_ex_1_imm_out, ID_PC, if_id_1_ir_out, IF_PC, j_pc, LedData, MD_final, MD_out,
       Mem_DATA, MEM_PC, mem_wb_1_alu_result_out, mem_wb_1_memdata_out, mips_alu_1_result, multiplexer_1_out,
       multiplexer_6_out, multiplexer_7_out, multiplexer_11_out, multiplexer_12_out, next_pc, R2, R2_WB,
       rom_1_data, RS, RS_Mem, RS_WB, shifter_1_out, shifter_2_out, shifter_3_out, shifter_4_out,
       shifter_5_out, WB_PC;

  Button \u_总复位  (.out(RST));
  Button _1 (.out(IR1));
  Button _2 (.out(IR2));
  Button _3 (.out(IR3));
  Button \u_继续运行  (.out(Go));
  LED led_1 (.in(W1));
  LED led_2 (.in(W2));
  LED led_3 (.in(W3));
  or or_1 (or_1_out[0], con_if, JR_EX);
  Hex_Digit_Display hex_digit_display_1 (.value(LedData[31:28]));  // open: dp
  Multiplexer #(.select(2), .width(32), .enable("false")) multiplexer_1 (
    .in0(next_pc), .in1(b_pc), .in2(j_pc), .in3(EX_RD1_out), .out(multiplexer_1_out),
    .sel({uncon_if, or_1_out[0]}));
  Hex_Digit_Display hex_digit_display_2 (.value(LedData[23:20]));  // open: dp
  Hex_Digit_Display hex_digit_display_3 (.value(LedData[27:24]));  // open: dp
  and and_1 (and_1_out, or_2_out, ~LoadUse);  // AND_Gate
  or or_2 (or_2_out, Go, ~HALT);  // OR_Gate
  Hex_Digit_Display hex_digit_display_4 (.value(LedData[15:12]));  // open: dp
  Hex_Digit_Display hex_digit_display_5 (.value(LedData[19:16]));  // open: dp
  Counter #(.width(16), .max('hffff)) counter_1 (
    .count(and_2_out), .Q(\插入气泡数 ), .clk(CLK), .clr(RST));  // open: load, D, carry
  and and_2 (and_2_out, LoadUse, ~HALT);  // AND_Gate
  Counter #(.width(16), .max('hffff)) counter_2 (
    .count(con_if), .Q(\条件分支成功数 ), .clk(CLK), .clr(RST));  // open: load, D, carry
  Counter #(.width(16), .max('hffff)) counter_3 (
    .count(uncon_if), .Q(\无条件分支数 ), .clk(CLK), .clr(RST));  // open: load, D, carry
  Counter #(.width(16), .max('hffff)) counter_4 (
    .count(or_2_out), .Q(\总周期数 ), .clk(CLK), .clr(RST));  // open: load, D, carry
  Register #(.width(32)) PC (.D(multiplexer_1_out), .en(and_1_out), .Q(IF_PC), .clk(CLK), .clr(RST));
  Hex_Digit_Display hex_digit_display_6 (.value(LedData[11:8]));  // open: dp
  Hex_Digit_Display hex_digit_display_7 (.value(LedData[7:4]));  // open: dp
  Clock clock_1 (.out(CLK));
  Hex_Digit_Display hex_digit_display_8 (.value(LedData[3:0]));  // open: dp
  Adder #(.width(32)) adder_1 (.a(IF_PC), .b(32'h4), .out(next_pc));  // open: cin, cout
  // Probe on rom_1_data
  or or_3 (or_3_out, LoadUse, or_2_out);
  ROM #(.addrWidth(10), .dataWidth(32)) rom_1 (.addr(IF_PC[11:2]), .data(rom_1_data));  // open: sel
  or or_4 (or_4_out, branch_hazard, LoadUse);
  // Probe on \总周期数 
  // Probe on \无条件分支数 
  // Probe on \条件分支成功数 
  // Probe on \插入气泡数 
  // Probe on IF_PC[11:0]
  IF_ID if_id_1 (
    .En(or_3_out), .clk(CLK), .tmp_rst(branch_hazard),
    .IR_out({if_id_1_ir_out[31:11], if_id_1_ir_out_2, if_id_1_ir_out[5:0]}), .PC_out(ID_PC), .IR(rom_1_data),
    .PC(next_pc), .rst(RST));  // open: En_out
  // Probe on ID_PC[11:0]
  and and_3 (LoadUse, Ex_MtR, or_5_out);
  or or_5 (or_5_out, R1_EX_Hazard, R2_EX_Hazard);
  // Probe on MEM_PC[11:0]
  // Probe on EX_PC[11:0]
  \硬布线控制器  \u_硬布线控制器_1  (
    .Func(if_id_1_ir_out[5:0]), .OP(if_id_1_ir_out[31:26]), .ALU_OP(\硬布线控制器_1_alu_op ),
    .MemToReg(\硬布线控制器_1_memtoreg ), .MemWrite(\硬布线控制器_1_memwrite ), .ALU_SRC(\硬布线控制器_1_alu_src ),
    .RegWrite(\硬布线控制器_1_regwrite ), .SysCALL(Syscall), .SignedExt(SignedExt), .RegDst(\硬布线控制器_1_regdst ),
    .JR(JR), .JMP(JMP), .Beq(\硬布线控制器_1_beq ), .JAL(JAL), .Bne(\硬布线控制器_1_bne ), .R1_Used(R1_Used),
    .R2_Used(R2_Used), .BLEZ(BLEZ), .SRLV(SRLV), .LBU(LBU));
  Multiplexer #(.width(5), .enable("false")) multiplexer_2 (
    .in0(if_id_1_ir_out[25:21]), .in1(5'b00010), .out(R1_num), .sel(Syscall));
  Multiplexer #(.width(5), .enable("false")) multiplexer_3 (
    .in0(if_id_1_ir_out[20:16]), .in1(5'b00100), .out(R2_num), .sel(Syscall));
  Multiplexer #(.width(5), .enable("false")) multiplexer_4 (
    .in0(if_id_1_ir_out[20:16]), .in1(if_id_1_ir_out[15:11]), .out(multiplexer_4_out), .sel(\硬布线控制器_1_regdst ));
  // Probe on WB_PC[11:0]
  assign bit_extender_1_out = {{16{1'b0}}, {if_id_1_ir_out[15:11], if_id_1_ir_out_2, if_id_1_ir_out[5:0]}};  // Bit_Extender bit_extender_1
  assign bit_extender_2_out = {{16{if_id_1_ir_out[15]}}, {if_id_1_ir_out[15:11], if_id_1_ir_out_2, if_id_1_ir_out[5:0]}};  // Bit_Extender bit_extender_2
  assign bit_extender_3_out = {{6{1'b0}}, {if_id_1_ir_out[25:11], if_id_1_ir_out_2, if_id_1_ir_out[5:0]}};  // Bit_Extender bit_extender_3
  MIPS_Regifile mips_regifile_1 (
    .Din(multiplexer_11_out), .Clk(CLK), .R1(RS), .R2(R2), .WE(mem_wb_1_regwrite_out), .W_num(WB_num),
    .R1_num(R1_num), .R2_num(R2_num));
  \数据相关检测  \u_数据相关检测_1  (
    .R1_Used(R1_Used), .R2_Used(R2_Used), .EX_RegWrite(EX_Wt), .MEM_RegWrite(Mem_Wt),
    .R1_EX_Related(R1_EX_Hazard), .R1_num(R1_num), .R2_num(R2_num), .R2_EX_Related(R2_EX_Hazard),
    .EX_WriteReg_num(Ex_Wt_num), .R1_MEM_Related(R1_Mem_Hazard), .MEM_WriteReg_num(Mem_Wt_num),
    .R2_MEM_Related(R2_Mem_Hazard));
  Multiplexer #(.width(5), .enable("false")) multiplexer_5 (
    .in0(multiplexer_4_out), .in1({5{1'b1}}), .out(multiplexer_5_out), .sel(JAL));
  Multiplexer #(.width(32), .enable("false")) multiplexer_6 (
    .in0(bit_extender_1_out), .in1(bit_extender_2_out), .out(multiplexer_6_out), .sel(SignedExt));
  Shifter #(.width(32)) shifter_1 (.in(bit_extender_3_out), .\dist (5'b00010), .out(shifter_1_out));
  Comparator #(.width(32)) comparator_1 (.a(RS_WB), .b(32'h22), .eq(comparator_1_eq));  // open: gt, lt
  and and_4 (and_4_out, Syscall_WB, comparator_1_eq);
  Register #(.width(32)) Led_4 (.D(R2_WB), .en(and_4_out), .Q(LedData), .clk(CLK), .clr(RST));
  and and_5 (HALT, ~comparator_1_eq, Syscall_WB);  // AND_Gate
  ID_EX id_ex_1 (
    .PC(ID_PC), .Reg_A(RS), .Reg_B(R2), .Imm(multiplexer_6_out), .En(or_6_out), .clk(CLK), .rst(RST),
    .PC_out(EX_PC), .Reg_A_out(EX_RD1_in), .Reg_B_out(EX_RD2_in), .Imm_out(id_ex_1_imm_out),
    .RegWrite(\硬布线控制器_1_regwrite ), .RegWrite_out(EX_Wt), .MemtoReg(\硬布线控制器_1_memtoreg ),
    .MemtoReg_out(Ex_MtR), .W_num(multiplexer_5_out), .W__out(Ex_Wt_num), .beq(\硬布线控制器_1_beq ),
    .beq_out(id_ex_1_beq_out), .bne(\硬布线控制器_1_bne ), .bne_out(id_ex_1_bne_out), .ALUop(\硬布线控制器_1_alu_op ),
    .ALUop_out(id_ex_1_aluop_out), .MemWrite(\硬布线控制器_1_memwrite ), .MemWrite_out(id_ex_1_memwrite_out),
    .ALUsrcB(\硬布线控制器_1_alu_src ), .ALUsrcB_out(id_ex_1_alusrcb_out), .shamt(if_id_1_ir_out_2),
    .shamt_out(id_ex_1_shamt_out), .JPC(shifter_1_out), .JPC_out(j_pc), .jal(JAL), .jal_out(JAL_EX),
    .jmp(JMP), .jmp_out(JMP_EX), .jr(JR), .jr_out(JR_EX), .tmp_rst(or_4_out), .syscall(Syscall),
    .syscall_out(Syscall_EX), .lbu(LBU), .lbu_out(LBU_EX), .srlv(SRLV), .srlv_out(SRLV_EX), .blez(BLEZ),
    .blez_out(id_ex_1_blez_out), .r1_sel({R1_EX_Hazard, R1_Mem_Hazard}), .r1_sel_out(R1_sel),
    .r2_sel({R2_EX_Hazard, R2_Mem_Hazard}), .r2_sel_out(R2_sel));  // open: En_out
  or or_6 (or_6_out, Go, ~HALT);  // OR_Gate
  Multiplexer #(.width(32), .enable("false")) multiplexer_7 (
    .in0(EX_RD2_out), .in1(id_ex_1_imm_out), .out(multiplexer_7_out), .sel(id_ex_1_alusrcb_out));
  Multiplexer #(.width(5), .enable("false")) multiplexer_8 (
    .in0(id_ex_1_shamt_out), .in1(EX_RD1_out[4:0]), .out(multiplexer_8_out), .sel(SRLV_EX));
  or or_7 (branch_hazard, uncon_if, con_if);
  Shifter #(.width(32)) shifter_2 (.in(id_ex_1_imm_out), .\dist (5'b00010), .out(shifter_2_out));
  MIPS_ALU mips_alu_1 (
    .X(EX_RD1_out), .Y(multiplexer_7_out), .AluOP(id_ex_1_aluop_out), .Equal(mips_alu_1_equal),
    .Result(mips_alu_1_result), .Result_2(AluResult2), .shamt(multiplexer_8_out));
  Adder #(.width(32)) adder_2 (.a(EX_PC), .b(shifter_2_out), .out(b_pc));  // open: cin, cout
  and and_6 (and_6_out, mips_alu_1_equal, id_ex_1_beq_out);
  and and_7 (and_7_out, id_ex_1_bne_out, ~mips_alu_1_equal);  // AND_Gate
  or or_8 (or_8_out, mips_alu_1_equal, mips_alu_1_result[0]);
  Multiplexer #(.select(2), .width(32), .enable("false")) multiplexer_9 (
    .in0(EX_RD1_in), .in1(Mem_DATA), .in2(EX_DATA), .in3(EX_DATA), .out(EX_RD1_out), .sel(R1_sel));
  Multiplexer #(.select(2), .width(32), .enable("false")) multiplexer_10 (
    .in0(EX_RD2_in), .in1(Mem_DATA), .in2(EX_DATA), .in3(EX_DATA), .out(EX_RD2_out), .sel(R2_sel));
  and and_8 (and_8_out, or_8_out, id_ex_1_blez_out);
  or or_9 (uncon_if, JAL_EX, JMP_EX, JR_EX);
  or or_10 (con_if, and_6_out, and_7_out, and_8_out);
  EX_MEM ex_mem_1 (
    .PC(EX_PC), .RegWrite(EX_Wt), .ALU_Result(mips_alu_1_result), .MemtoReg(Ex_MtR), .Reg_B(EX_RD2_out),
    .W_num(Ex_Wt_num), .MemWrite(id_ex_1_memwrite_out), .Jal(JAL_EX), .En(or_6_out), .clk(CLK), .rst(RST),
    .PC_out(MEM_PC), .RegWrite_out(Mem_Wt), .ALU_Result_out(EX_DATA), .MemtoReg_out(ex_mem_1_memtoreg_out),
    .Reg_B_out(ex_mem_1_reg_b_out), .W__out(Mem_Wt_num), .MemWrite_out(ex_mem_1_memwrite_out),
    .Jal_out(ex_mem_1_jal_out), .lbu(LBU_EX), .lbu_out(LBU_MEM), .syscall(Syscall_EX),
    .syscall_out(Syscall_Mem), .RegA(EX_RD1_out), .RegA_out(RS_Mem));  // open: En_out
  Multiplexer #(.width(32), .enable("false")) multiplexer_11 (
    .in0(Mem_DATA), .in1(WB_PC), .out(multiplexer_11_out), .sel(mem_wb_1_jal_out));
  assign and_9_out = MD_out & 32'hff;  // AND_Gate and_9, 32 bits wide
  assign and_10_out = MD_out & 32'hff00;  // AND_Gate and_10, 32 bits wide
  assign and_11_out = MD_out & 32'hff0000;  // AND_Gate and_11, 32 bits wide
  assign and_12_out = MD_out & 32'hff000000;  // AND_Gate and_12, 32 bits wide
  // MIPS_RAM mips_ram_1: pin names not known; wires that end beside it: EX_DATA[11:2], ex_mem_1_reg_b_out, ex_mem_1_memwrite_out, 4'b1111, CLK, MD_out
  Shifter #(.width(32), .shift("lr")) shifter_3 (.in(and_10_out), .\dist (5'b01000), .out(shifter_3_out));
  Shifter #(.width(32), .shift("lr")) shifter_4 (.in(and_11_out), .\dist (5'b10000), .out(shifter_4_out));
  Shifter #(.width(32), .shift("lr")) shifter_5 (.in(and_12_out), .\dist (5'b11000), .out(shifter_5_out));
  Multiplexer #(.select(2), .width(32), .enable("false")) multiplexer_12 (
    .in0(and_9_out), .in1(shifter_3_out), .in2(shifter_4_out), .in3(shifter_5_out), .out(multiplexer_12_out),
    .sel(EX_DATA[1:0]));
  MEM_WB mem_wb_1 (
    .PC(MEM_PC), .RegWrite(Mem_Wt), .ALU_Result(EX_DATA), .MemtoReg(ex_mem_1_memtoreg_out),
    .MemData(MD_final), .W_num(Mem_Wt_num), .Jal(ex_mem_1_jal_out), .En(or_6_out), .clk(CLK), .rst(RST),
    .PC_out(WB_PC), .RegWrite_out(mem_wb_1_regwrite_out), .ALU_Result_out(mem_wb_1_alu_result_out),
    .MemtoReg_out(mem_wb_1_memtoreg_out), .MemData_out(mem_wb_1_memdata_out), .W__out(WB_num),
    .Jal_out(mem_wb_1_jal_out), .syscall(Syscall_Mem), .syscall_out(Syscall_WB), .RegA(RS_Mem),
    .RegA_out(RS_WB), .RegB(ex_mem_1_reg_b_out), .RegB_out(R2_WB));  // open: En_out
  Multiplexer #(.width(32), .enable("false")) multiplexer_13 (
    .in0(MD_out), .in1(multiplexer_12_out), .out(MD_final), .sel(LBU_MEM));
  Multiplexer #(.width(32), .enable("false")) multiplexer_14 (
    .in0(mem_wb_1_alu_result_out), .in1(mem_wb_1_memdata_out), .out(Mem_DATA), .sel(mem_wb_1_memtoreg_out));

  // Other names for the same wires on the sheet: ram_sel[1:0] = EX_DATA[1:0]; R2_EX[31:0] = EX_RD2_out;
  //   RS_EX[31:0] = EX_RD1_out

  // Notes on the sheet:
  //   中断源
  //   中断等待指示
  //   数码管输出
  //   指令存储器
  //   contents of rom_1 (hex, n*v repeats v):
  //   20110001 8000c05 20110001 20120002 20130003 8000c09 20110001 20120002 20130003 8000c0d 20110001
  //   20120002 20130003 8000c11 20110001 20120002 20130003 c000cf7 20100001 20110001 118fc0 112020
  //   20020022 c 118882 12200001 8000c15 112020 20020022 c 20110001 118880 112020 20020022 c 12200001
  //   8000c1f 20110001 118fc0 112020 20020022 c 1188c3 112020 20020022 c 118903 112020 20020022 c 118903
  //   112020 20020022 c 118903 112020 20020022 c 118903 112020 20020022 c 118903 112020 20020022 c 118903
  //   112020 20020022 c 118903 112020 20020022 c 20100001 109fc0 139fc3 8021 2012000c 24160003 26100001
  //   3210000f 20080008 20090001 139900 2709825 132020 20020022 c 1094022 1500fff9 22100001 2018000f
  //   2188024 108700 20080008 20090001 139902 2709825 132021 20020022 c 1094022 1500fff9 108702 2c9b022
  //   12c00001 8000c50 4020 1084027 84400 3508ffff 82021 20020022 c 2010ffff 20110000 ae300000 22100001
  //   22310004 ae300000 22100001 22310004 ae300000 22100001 22310004 ae300000 22100001 22310004 ae300000
  //   22100001 22310004 ae300000 22100001 22310004 ae300000 22100001 22310004 ae300000 22100001 22310004
  //   ae300000 22100001 22310004 ae300000 22100001 22310004 ae300000 22100001 22310004 ae300000 22100001
  //   22310004 ae300000 22100001 22310004 ae300000 22100001 22310004 ae300000 22100001 22310004 ae300000
  //   22100001 22310004 22100001 8020 2011003c 8e130000 8e340000 274402a 11000002 ae330000 ae140000
  //   2231fffc 1611fff8 102020 20020022 c 22100004 2011003c 1611fff2 20020032 c 20080001 20090003 20110876
  //   118d00 112020 20020022 c 200b0008 1118806 1318806 112020 20020022 c 216bffff 1560fff9 2002000a c
  //   2008ffff 20117777 112020 20020022 c 200b0010 2288826 112020 20020022 c 216bffff 1560fffa 2002000a c
  //   20090000 200b0010 34118483 20120404 118c00 129400 36318281 22520404 ad310000 2328820 21290004
  //   216bffff 1560fffb 200b0020 20090000 91310000 112020 20020022 c 21290001 216bffff 1560fff9 2002000a c
  //   2011fff1 112020 20020022 c 22310001 1a20fffb 2002000a c 20100000 22100001 102020 20020022 c 22100002
  //   102020 20020022 c 22100003 102020 20020022 c 22100004 102020 20020022 c 22100005 102020 20020022 c
  //   22100006 102020 20020022 c 22100007 102020 20020022 c 22100008 102020 20020022 20020022 c 3e00008
  //   OP
  //   Func
  //   指令字
  //   rs
  //   rt
  //   rd
  //   shamt
  //   Imm
  //   j-addr
  //   流水调试日志用
  //   JMP
  //   JR
  //   OP
  //   Func
  //   Beq
  //   Bne
  //   MemToReg
  //   MemWrite
  //   AluOP
  //   AluSrcB
  //   RegWrite
  //   JAL
  //   RegDst
  //   Syscall
endmodule
