// Logisim project 硬件堆栈.circ as structural Verilog: 1 circuit, main circuit HardwareStack
module HardwareStack (
  input  pop,
  input  push,
  input  [31:0] data_in,
  input  clr,
  output [31:0] data_out
);

  wire or_1_out, or_2_out, USE0, USE1, USE2, USE3, USE4, USE5, USE6, USE7, V0, V1, V2, V3, V4, V5, V6, V7;
  wire [2:0] POS;
  wire [31:0] demultiplexer_1_out0, demultiplexer_1_out1, demultiplexer_1_out2, demultiplexer_1_out3,
       demultiplexer_1_out4, demultiplexer_1_out5, demultiplexer_1_out6, demultiplexer_1_out7, register_1_q,
       register_2_q, register_3_q, register_4_q, register_5_q, register_6_q, register_7_q, register_8_q;

  Counter #(.width(3), .max('h7), .ongoal("stay")) counter_1 (
    .load(pop), .count(or_1_out), .Q(POS), .clk(or_1_out), .clr(clr));  // open: D, carry
  or or_1 (or_1_out, pop, push);
  Demultiplexer #(.select(3), .width(32), .enable("false")) demultiplexer_1 (
    .out0(demultiplexer_1_out0), .out1(demultiplexer_1_out1), .out2(demultiplexer_1_out2),
    .out3(demultiplexer_1_out3), .out4(demultiplexer_1_out4), .out5(demultiplexer_1_out5),
    .out6(demultiplexer_1_out6), .out7(demultiplexer_1_out7), .in(data_in), .sel(POS));
  Register #(.width(32)) register_1 (.D(demultiplexer_1_out0), .en(USE0), .Q(register_1_q), .clk(or_2_out), .clr(clr));
  Register #(.width(32)) register_2 (.D(demultiplexer_1_out1), .en(USE1), .Q(register_2_q), .clk(or_2_out), .clr(clr));
  Register #(.width(32)) register_3 (.D(demultiplexer_1_out2), .en(USE2), .Q(register_3_q), .clk(or_2_out), .clr(clr));
  Register #(.width(32)) register_4 (.D(demultiplexer_1_out3), .en(USE3), .Q(register_4_q), .clk(or_2_out), .clr(clr));
  Register #(.width(32)) register_5 (.D(demultiplexer_1_out4), .en(USE4), .Q(register_5_q), .clk(or_2_out), .clr(clr));
  Register #(.width(32)) register_6 (.D(demultiplexer_1_out5), .en(USE5), .Q(register_6_q), .clk(or_2_out), .clr(clr));
  Register #(.width(32)) register_7 (.D(demultiplexer_1_out6), .en(USE6), .Q(register_7_q), .clk(or_2_out), .clr(clr));
  Register #(.width(32)) register_8 (.D(demultiplexer_1_out7), .en(USE7), .Q(register_8_q), .clk(or_2_out), .clr(clr));
  or or_2 (or_2_out, push, pop);
  // Probe on register_1_q
  // Probe on register_2_q
  // Probe on register_3_q
  // Probe on register_4_q
  // Probe on register_5_q
  // Probe on register_6_q
  // Probe on register_7_q
  Multiplexer #(.select(3), .width(32), .disabled(0)) multiplexer_1 (
    .in0(register_1_q), .in1(register_2_q), .in2(register_3_q), .in3(register_4_q), .in4(register_5_q),
    .in5(register_6_q), .in6(register_7_q), .in7(register_8_q), .out(data_out), .sel(POS), .en(pop));
  // Probe on data_out
  Demultiplexer #(.select(3), .enable("false")) demultiplexer_2 (
    .out0(V0), .out1(V1), .out2(V2), .out3(V3), .out4(V4), .out5(V5), .out6(V6), .out7(V7), .in(1'b1),
    .sel(POS));
  and and_1 (USE0, V0, push);
  and and_2 (USE1, V1, push);
  and and_3 (USE2, V2, push);
  and and_4 (USE3, V3, push);
  and and_5 (USE4, V4, push);
  and and_6 (USE5, V5, push);
  and and_7 (USE6, V6, push);
  and and_8 (USE7, V7, push);
endmodule
